// Digital circuit 7474.dig as structural Verilog
// Dual D flip-flop
module _7474 (
  input  _1nSD,
  input  _1D,
  input  _1CP,
  input  _1nRD,
  input  _2nSD,
  input  _2D,
  input  _2CP,
  input  _2nRD,
  output _1Q,
  output _1nQ,
  output _2Q,
  output _2nQ
);

  wire not_1_out, not_2_out, not_3_out, not_4_out;

  not not_1 (not_1_out, _1nSD);
  not not_2 (not_2_out, _1nRD);
  not not_3 (not_3_out, _2nSD);
  not not_4 (not_4_out, _2nRD);
  D_FF_AS d_ff_as_1 (.Set(not_1_out), .D(_1D), .C(_1CP), .Clr(not_2_out), .Q(_1Q), .nQ(_1nQ));
  D_FF_AS d_ff_as_2 (.Set(not_3_out), .D(_2D), .C(_2CP), .Clr(not_4_out), .Q(_2Q), .nQ(_2nQ));

  // Notes on the sheet:
  //   _1Q: pin 5
  //   _1nQ: pin 6
  //   _1nSD: pin 4
  //   _1D: pin 2
  //   _1CP: pin 3
  //   _1nRD: pin 1
  //   _2Q: pin 9
  //   _2nQ: pin 8
  //   _2nSD: pin 10
  //   _2D: pin 12
  //   _2CP: pin 11
  //   _2nRD: pin 13
endmodule
