// Digital circuit Adder8bit.dig as structural Verilog
module Adder8bit (
  input  [7:0] A,
  input  [7:0] B,
  input  Takt,
  output [7:0] S,
  output C
);

  FullAdderCLA fulladdercla_1 ();
  FullAdderCLA fulladdercla_2 ();
endmodule
