// Digital circuit Ampel_3FF.dig as structural Verilog
module Ampel_3FF (
  input  clk
);

  wire and_1_out, G_q, not_1_out, R_q, Y_q;

  and and_1 (and_1_out, Y_q, R_q);
  not not_1 (not_1_out, and_1_out);
  JK_FF R (.J(Y_q), .C(clk), .K(Y_q), .Q(R_q));  // open: nQ
  JK_FF Y (.J(1'b1), .C(clk), .K(1'b1), .Q(Y_q));  // open: nQ
  JK_FF G (.J(and_1_out), .C(clk), .K(not_1_out), .Q(G_q));  // open: nQ
  LED led_1 (.in(R_q));
  LED led_2 (.in(Y_q));
  LED led_3 (.in(G_q));
endmodule
