// Digital circuit Ampel_Einfach.dig as structural Verilog
module Ampel_Einfach (
  input  Takt
);

  wire and_1_out, z_0_nq, z_0_q, z_1_nq, z_1_q;

  JK_FF z_1 (.J(z_0_q), .C(Takt), .K(z_0_q), .Q(z_1_q), .nQ(z_1_nq));
  JK_FF z_0 (.J(1'b1), .C(Takt), .K(1'b1), .Q(z_0_q), .nQ(z_0_nq));
  and and_1 (and_1_out, z_1_q, z_0_nq);
  LED Rot (.in(z_1_nq));
  LED Gelb (.in(z_0_q));
  LED \Grün  (.in(and_1_out));

  // Notes on the sheet:
  //   Takt: Hz: 10
endmodule
