// Digital circuit Ampel_Feuer.dig as structural Verilog
module Ampel_Feuer (
  input  Clock,
  input  Feuer
);

  wire and_1_out, and_2_out, and_3_out, jk_ff_1_nq, jk_ff_1_q, jk_ff_2_nq, jk_ff_2_q, not_1_out, or_1_out,
       or_2_out;

  not not_1 (not_1_out, Feuer);
  and and_1 (and_1_out, not_1_out, jk_ff_2_q);
  or or_1 (or_1_out, jk_ff_2_q, Feuer);
  JK_FF jk_ff_1 (.J(and_1_out), .C(Clock), .K(or_1_out), .Q(jk_ff_1_q), .nQ(jk_ff_1_nq));
  JK_FF jk_ff_2 (.J(not_1_out), .C(Clock), .K(1'b1), .Q(jk_ff_2_q), .nQ(jk_ff_2_nq));
  or or_2 (or_2_out, jk_ff_1_nq, Feuer);
  and and_2 (and_2_out, not_1_out, jk_ff_2_q);
  and and_3 (and_3_out, not_1_out, jk_ff_1_q, jk_ff_2_nq);
  LED Rot (.in(or_2_out));
  LED Gelb (.in(and_2_out));
  LED \Grün  (.in(and_3_out));
endmodule
