// Digital circuit Ampel_Feuer2.dig as structural Verilog
module Ampel_Feuer2 (
  input  Clock,
  input  Feuer
);

  wire and_1_out, jk_ff_1_nq, jk_ff_1_q, jk_ff_2_nq, jk_ff_2_q, not_1_out, or_1_out;

  or or_1 (or_1_out, jk_ff_1_q, not_1_out);
  not not_1 (not_1_out, Feuer);
  JK_FF jk_ff_1 (.J(jk_ff_2_q), .C(Clock), .K(jk_ff_2_q), .Q(jk_ff_1_q), .nQ(jk_ff_1_nq));
  JK_FF jk_ff_2 (.J(or_1_out), .C(Clock), .K(1'b1), .Q(jk_ff_2_q), .nQ(jk_ff_2_nq));
  and and_1 (and_1_out, jk_ff_1_q, jk_ff_2_nq);
  LED Rot (.in(jk_ff_1_nq));
  LED Gelb (.in(jk_ff_2_q));
  LED \Grün  (.in(and_1_out));
endmodule
