// Digital circuit Ampel_MSJK.dig as structural Verilog
module Ampel_MSJK (
  input  Clock,
  input  Feuer
);

  wire and_1_out, ms_jk_1_p1, ms_jk_1_p4, ms_jk_1_p5, ms_jk_2_p5, not_1_out, or_1_out;

  not not_1 (not_1_out, Feuer);
  Break break_1 ();  // open: brk
  or or_1 (or_1_out, ms_jk_1_p4, not_1_out);
  // MS_JK ms_jk_1: pin names not known; wires that end beside it: ms_jk_1_p1, Clock, ms_jk_1_p1, ms_jk_1_p4, ms_jk_1_p5
  // MS_JK ms_jk_2: pin names not known; wires that end beside it: or_1_out, Clock, 1'b1, ms_jk_1_p1, ms_jk_2_p5
  and and_1 (and_1_out, ms_jk_1_p4, ms_jk_2_p5);
  LED Rot (.in(ms_jk_1_p5));
  LED Gelb (.in(ms_jk_1_p1));
  LED \Grün  (.in(and_1_out));
endmodule
