// Digital circuit Ampel_TJK.dig as structural Verilog
module Ampel_TJK (
  input  Clock,
  input  Feuer
);

  wire and_1_out, not_1_out, or_1_out, t_jk_1_nq, t_jk_1_q, t_jk_2_nq, t_jk_2_q;

  or or_1 (or_1_out, t_jk_1_q, not_1_out);
  not not_1 (not_1_out, Feuer);
  T_JK t_jk_1 (.J(t_jk_2_q), .C(Clock), .K(t_jk_2_q), .Q(t_jk_1_q), .nQ(t_jk_1_nq));
  T_JK t_jk_2 (.J(or_1_out), .C(Clock), .K(1'b1), .Q(t_jk_2_q), .nQ(t_jk_2_nq));
  and and_1 (and_1_out, t_jk_1_q, t_jk_2_nq);
  LED Rot (.in(t_jk_1_nq));
  LED Gelb (.in(t_jk_2_q));
  LED \Grün  (.in(and_1_out));
endmodule
