// Digital circuit Count_JK.dig as structural Verilog
module Count_JK (
  input  in_5,
  output out_1,
  output out_2,
  output out_3,
  output out_4
);

  wire and_1_out, and_2_out;

  JK_FF jk_ff_1 (.J(1'b1), .C(in_5), .K(1'b1), .Q(out_1));  // open: nQ
  JK_FF jk_ff_2 (.J(out_1), .C(in_5), .K(out_1), .Q(out_2));  // open: nQ
  and and_1 (and_1_out, out_1, out_2);
  JK_FF jk_ff_3 (.J(and_1_out), .C(in_5), .K(and_1_out), .Q(out_3));  // open: nQ
  and and_2 (and_2_out, and_1_out, out_3);
  JK_FF jk_ff_4 (.J(and_2_out), .C(in_5), .K(and_2_out), .Q(out_4));  // open: nQ
endmodule
