// Digital circuit FullAdder.dig as structural Verilog
module FullAdder (
  input  C_i_1,
  input  A0,
  input  B0,
  output S0,
  output C_i
);

  wire and_1_out, and_2_out, xor_1_out;

  and and_1 (and_1_out, A0, B0);
  xor xor_1 (xor_1_out, A0, B0);
  and and_2 (and_2_out, xor_1_out, C_i_1);
  xor xor_2 (S0, xor_1_out, C_i_1);
  or or_1 (C_i, and_1_out, and_2_out);
endmodule
