// Digital circuit JK-Trigger.dig as structural Verilog
module JK_Trigger (
  input  in_1,
  input  in_2,
  input  in_3,
  output out_4,
  output out_5
);

  wire and_1_out, and_2_out, and_3_out, delay_1_out, not_1_out;

  not not_1 (not_1_out, in_1);
  and and_1 (and_1_out, delay_1_out, in_1);
  Delay delay_1 (.in(not_1_out), .out(delay_1_out));
  and and_2 (and_2_out, out_4, and_1_out);
  // Probe on and_1_out
  and and_3 (and_3_out, and_1_out, out_5);
  nor nor_1 (out_4, and_2_out, out_5);
  nor nor_2 (out_5, out_4, and_3_out);
endmodule
