// Digital circuit MS-JK.dig as structural Verilog
module MS_JK (
  input  in_1,
  input  in_2,
  input  in_3,
  output out_4,
  output out_5
);

  wire and_1_out, and_2_out, and_3_out, and_4_out, nor_1_out, nor_2_out, not_1_out;

  and and_1 (and_1_out, out_5, in_3);
  not not_1 (not_1_out, in_3);
  and and_2 (and_2_out, in_3, out_4);
  nor nor_1 (nor_1_out, and_1_out, nor_2_out);
  nor nor_2 (nor_2_out, nor_1_out, and_2_out);
  and and_3 (and_3_out, nor_1_out, not_1_out);
  and and_4 (and_4_out, not_1_out, nor_2_out);
  nor nor_3 (out_4, and_3_out, out_5);
  nor nor_4 (out_5, out_4, and_4_out);
endmodule
