// Digital circuit T_Counter.dig as structural Verilog
module T_Counter (
  input  in_5,
  output out_1,
  output out_2,
  output out_3,
  output out_4
);

  wire not_1_out, not_2_out, not_3_out;

  T_FF t_ff_1 (.T(not_1_out), .Q(out_4));  // open: C, nQ
  not not_1 (not_1_out, out_3);
  T_FF t_ff_2 (.T(not_2_out), .Q(out_3));  // open: C, nQ
  not not_2 (not_2_out, out_2);
  T_FF t_ff_3 (.T(not_3_out), .Q(out_2));  // open: C, nQ
  not not_3 (not_3_out, out_1);
  T_FF t_ff_4 (.T(in_5), .Q(out_1));  // open: C, nQ
endmodule
