// Digital circuit d-tg-ff.dig as structural Verilog
// The two FETs in the transmission gate are not 
// necessary in this simulation because no body diodes 
// are simulated.
// In order to be compatible with the literature, two FETs 
// are also used in the simulation.
module d_tg_ff (
  input  D,
  input  C,
  output nQ,
  output Q
);

  wire pfet_1_d, pfet_2_s;

  PFET pfet_1 (.G(C), .S(1'b1), .D(pfet_1_d));
  NFET nfet_1 (.G(C), .D(pfet_1_d), .S(1'b0));
  PFET pfet_2 (.G(pfet_1_d), .S(pfet_2_s), .D(D));
  NFET nfet_2 (.G(C), .D(D), .S(pfet_2_s));
  PFET pfet_3 (.G(pfet_2_s), .S(1'b1), .D(nQ));
  NFET nfet_3 (.G(pfet_2_s), .D(nQ), .S(1'b0));
  PFET pfet_4 (.G(nQ), .S(1'b1), .D(Q));
  NFET nfet_4 (.G(nQ), .D(Q), .S(1'b0));
  NFET nfet_5 (.G(pfet_1_d), .D(Q), .S(pfet_2_s));
  PFET pfet_5 (.G(C), .S(pfet_2_s), .D(Q));

  // Notes on the sheet:
  //   nQ: not Out
  //   Q: Out
  //   D: Data In
  //   C: Clock In
endmodule

/* Test case:
C D Q ~Q
1 0 0 1
0 0 0 1
0 1 0 1
0 0 0 1
1 1 1 0
0 1 1 0
0 0 1 0
1 0 0 1
0 0 0 1
*/
