// Digital circuit prom.dig as structural Verilog
module prom (
  input  A_0,
  input  A_1,
  input  A_2,
  input  A_3,
  input  CS,
  output Q
);

  wire decoder_1_out_0, decoder_1_out_1, decoder_1_out_2, decoder_1_out_3, decoder_2_out_0, decoder_2_out_1,
       decoder_2_out_2, decoder_2_out_3, diodebackward_9_out, diodebackward_13_out, nfet_1_d, nfet_2_d,
       nfet_3_d, nfet_4_d, nfet_5_s, nfet_6_d, nfet_7_d, nfet_8_d, nfet_9_d, nfet_11_d, nfet_12_d, nfet_13_d,
       nfet_14_d, nfet_16_d, nfet_17_d, nfet_18_d, nfet_19_d, pullup_1_out, pullup_2_out;

  Decoder #(.Selector_Bits(2)) decoder_1 (
    .sel({A_1, A_0}), .out_0(decoder_1_out_0), .out_1(decoder_1_out_1), .out_2(decoder_1_out_2),
    .out_3(decoder_1_out_3));
  Decoder #(.Selector_Bits(2)) decoder_2 (
    .sel({A_3, A_2}), .out_0(decoder_2_out_0), .out_1(decoder_2_out_1), .out_2(decoder_2_out_2),
    .out_3(decoder_2_out_3));
  NFET nfet_1 (.G(decoder_1_out_0), .D(nfet_1_d), .S(1'b0));
  NFET nfet_2 (.G(decoder_1_out_1), .D(nfet_2_d), .S(1'b0));
  NFET nfet_3 (.G(decoder_1_out_2), .D(nfet_3_d), .S(1'b0));
  NFET nfet_4 (.G(decoder_1_out_3), .D(nfet_4_d), .S(1'b0));
  PullUp pullup_1 (.out(pullup_1_out));
  DiodeBackward diodebackward_1 (.in(nfet_1_d), .out(pullup_1_out));
  DiodeBackward diodebackward_2 (.in(nfet_2_d), .out(pullup_1_out));
  DiodeBackward diodebackward_3 (.in(nfet_3_d), .out(pullup_1_out));
  DiodeBackward diodebackward_4 (.in(nfet_4_d), .out(pullup_1_out));
  NFET nfet_5 (.G(decoder_2_out_0), .D(pullup_1_out), .S(nfet_5_s));
  NFET nfet_6 (.G(decoder_1_out_0), .D(nfet_6_d), .S(1'b0));
  NFET nfet_7 (.G(decoder_1_out_1), .D(nfet_7_d), .S(1'b0));
  NFET nfet_8 (.G(decoder_1_out_2), .D(nfet_8_d), .S(1'b0));
  NFET nfet_9 (.G(decoder_1_out_3), .D(nfet_9_d), .S(1'b0));
  PullUp pullup_2 (.out(pullup_2_out));
  DiodeBackward diodebackward_5 (.in(nfet_6_d), .out(pullup_2_out));
  DiodeBackward diodebackward_6 (.in(nfet_7_d), .out(pullup_2_out));
  DiodeBackward #(.Blown("true")) diodebackward_7 (.in(nfet_8_d), .out(pullup_2_out));
  DiodeBackward diodebackward_8 (.in(nfet_9_d), .out(pullup_2_out));
  NFET nfet_10 (.G(decoder_2_out_1), .D(pullup_2_out), .S(nfet_5_s));
  NFET nfet_11 (.G(decoder_1_out_0), .D(nfet_11_d), .S(1'b0));
  DiodeBackward diodebackward_9 (.in(nfet_11_d), .out(diodebackward_9_out));
  NFET nfet_12 (.G(decoder_1_out_1), .D(nfet_12_d), .S(1'b0));
  DiodeBackward #(.Blown("true")) diodebackward_10 (.in(nfet_12_d), .out(diodebackward_9_out));
  NFET nfet_13 (.G(decoder_1_out_2), .D(nfet_13_d), .S(1'b0));
  DiodeBackward diodebackward_11 (.in(nfet_13_d), .out(diodebackward_9_out));
  NFET nfet_14 (.G(decoder_1_out_3), .D(nfet_14_d), .S(1'b0));
  DiodeBackward diodebackward_12 (.in(nfet_14_d), .out(diodebackward_9_out));
  PullUp pullup_3 (.out(diodebackward_9_out));
  NFET nfet_15 (.G(decoder_2_out_2), .D(diodebackward_9_out), .S(nfet_5_s));
  NFET nfet_16 (.G(decoder_1_out_0), .D(nfet_16_d), .S(1'b0));
  DiodeBackward diodebackward_13 (.in(nfet_16_d), .out(diodebackward_13_out));
  NFET nfet_17 (.G(decoder_1_out_1), .D(nfet_17_d), .S(1'b0));
  DiodeBackward diodebackward_14 (.in(nfet_17_d), .out(diodebackward_13_out));
  NFET nfet_18 (.G(decoder_1_out_2), .D(nfet_18_d), .S(1'b0));
  DiodeBackward diodebackward_15 (.in(nfet_18_d), .out(diodebackward_13_out));
  NFET nfet_19 (.G(decoder_1_out_3), .D(nfet_19_d), .S(1'b0));
  DiodeBackward diodebackward_16 (.in(nfet_19_d), .out(diodebackward_13_out));
  NFET nfet_20 (.G(decoder_2_out_3), .D(diodebackward_13_out), .S(nfet_5_s));
  PullUp pullup_4 (.out(diodebackward_13_out));
  assign Q = CS ? nfet_5_s : 1'bz;  // Driver driver_1
endmodule

/* Test case:
A_0 A_1 A_2 A_3 Q
 0   0   0   0  0
 0   0   0   1  0
 0   0   1   0  0
 0   0   1   1  0
 0   1   0   0  0
 0   1   0   1  0
 0   1   1   0  1
 0   1   1   1  0
 1   0   0   0  0
 1   0   0   1  1
 1   0   1   0  0
 1   0   1   1  0
 1   1   0   0  0
 1   1   0   1  0
 1   1   1   0  0
 1   1   1   1  0
*/
