// Digital circuit rom.dig as structural Verilog
module rom (
  input  A_0,
  input  A_1,
  input  A_2,
  input  A_3,
  input  CS,
  output Q
);

  wire dec_1_a, dec_1_b, dec_1_c, dec_1_d, dec_2_a, dec_2_b, dec_2_c, dec_2_d, nfet_1_d, nfet_5_s, nfet_14_d,
       pullup_2_out, pullup_3_out;

  dec dec_1 (._0(A_0), ._1(A_1), .a(dec_1_a), .b(dec_1_b), .c(dec_1_c), .d(dec_1_d));
  dec dec_2 (._0(A_2), ._1(A_3), .a(dec_2_a), .b(dec_2_b), .c(dec_2_c), .d(dec_2_d));
  NFET nfet_1 (.G(dec_1_a), .D(nfet_1_d), .S(1'b0));
  NFET nfet_2 (.G(dec_1_b), .D(nfet_1_d), .S(1'b0));
  NFET nfet_3 (.G(dec_1_c), .D(nfet_1_d), .S(1'b0));
  NFET nfet_4 (.G(dec_1_d), .D(nfet_1_d), .S(1'b0));
  PullUp pullup_1 (.out(nfet_1_d));
  NFET nfet_5 (.G(dec_2_a), .D(nfet_1_d), .S(nfet_5_s));
  PullUp pullup_2 (.out(pullup_2_out));
  NFET nfet_6 (.G(dec_1_a), .D(pullup_2_out), .S(1'b0));
  NFET nfet_7 (.G(dec_1_b), .D(pullup_2_out), .S(1'b0));
  NFET nfet_8 (.G(dec_1_d), .D(pullup_2_out), .S(1'b0));
  NFET nfet_9 (.G(dec_2_b), .D(pullup_2_out), .S(nfet_5_s));
  PullUp pullup_3 (.out(pullup_3_out));
  NFET nfet_10 (.G(dec_1_a), .D(pullup_3_out), .S(1'b0));
  NFET nfet_11 (.G(dec_1_c), .D(pullup_3_out), .S(1'b0));
  NFET nfet_12 (.G(dec_1_d), .D(pullup_3_out), .S(1'b0));
  NFET nfet_13 (.G(dec_2_c), .D(pullup_3_out), .S(nfet_5_s));
  NFET nfet_14 (.G(dec_1_a), .D(nfet_14_d), .S(1'b0));
  NFET nfet_15 (.G(dec_1_b), .D(nfet_14_d), .S(1'b0));
  NFET nfet_16 (.G(dec_1_c), .D(nfet_14_d), .S(1'b0));
  NFET nfet_17 (.G(dec_1_d), .D(nfet_14_d), .S(1'b0));
  NFET nfet_18 (.G(dec_2_d), .D(nfet_14_d), .S(nfet_5_s));
  PullUp pullup_4 (.out(nfet_14_d));
  assign Q = CS ? nfet_5_s : 1'bz;  // Driver driver_1

  // Notes on the sheet:
  //   CS: default 1
endmodule

/* Test case:
A_0 A_1 A_2 A_3 Q
 0   0   0   0  0
 0   0   0   1  0
 0   0   1   0  0
 0   0   1   1  0
 0   1   0   0  0
 0   1   0   1  0
 0   1   1   0  1
 0   1   1   1  0
 1   0   0   0  0
 1   0   0   1  1
 1   0   1   0  0
 1   0   1   1  0
 1   1   0   0  0
 1   1   0   1  0
 1   1   1   0  0
 1   1   1   1  0
*/
