// Digital circuit sram.dig as structural Verilog
// 16-Bit Statisches RAM.
// Unter der Speichermatrix findet sich die 
// Schreiblogik jeweils einmal für jede Spalte in der 
// Speichermatrix.
module sram (
  input  D_In,
  input  R0,
  input  R1,
  input  C0,
  input  C1,
  input  WE,
  output D_Out
);

  wire decoder_1_out_0, decoder_1_out_1, decoder_1_out_2, decoder_1_out_3, demultiplexer_1_out_0,
       demultiplexer_1_out_1, demultiplexer_1_out_2, demultiplexer_1_out_3, nfet_2_d, nfet_2_s, nfet_3_s,
       nfet_4_s, nfet_5_s, nfet_6_s, nfet_7_s, nfet_8_s, nfet_9_s, nfet_10_s, nfet_12_s, nfet_13_s,
       nfet_14_s, nfet_16_s, nfet_18_s, nfet_20_s, nfet_22_d, nfet_22_s, nfet_23_s, nfet_24_s, nfet_25_s,
       nfet_27_s, nfet_28_s, nfet_29_s, nfet_30_s, nfet_31_s, nfet_33_s, nfet_34_s, nfet_35_s, nfet_36_s,
       nfet_37_s, nfet_41_s, nfet_44_d, nfet_44_s, nfet_45_s, nfet_46_s, nfet_47_s, nfet_48_s, nfet_49_s,
       nfet_50_s, nfet_51_s, nfet_52_s, nfet_54_s, nfet_55_s, nfet_56_s, nfet_58_s, nfet_60_s, nfet_62_s,
       nfet_64_d, nfet_64_s, nfet_65_s, nfet_66_s, nfet_67_s, nfet_69_s, nfet_70_s, nfet_71_s, nfet_72_s,
       nfet_73_s, nfet_75_s, nfet_76_s, nfet_77_s, nfet_78_s, nfet_79_s, nfet_83_s, pfet_1_d, pfet_2_d,
       pfet_3_d, pfet_4_d, pfet_5_d, pfet_6_d, pfet_12_d, pfet_14_d, pfet_15_d, pfet_16_d, pfet_17_d,
       pfet_18_d, pfet_19_d, pfet_25_d, pfet_27_d, pfet_28_d, pfet_29_d, pfet_30_d, pfet_31_d, pfet_32_d,
       pfet_38_d, pfet_40_d, pfet_41_d, pfet_42_d, pfet_43_d, pfet_44_d, pfet_45_d, pfet_51_d, pullup_1_out,
       pullup_2_out, pullup_3_out, pullup_4_out, pullup_5_out, pullup_6_out, pullup_7_out, pullup_8_out,
       pullup_9_out, pullup_10_out, pullup_11_out, pullup_12_out, pullup_13_out, pullup_14_out,
       pullup_15_out, pullup_16_out, pullup_17_out, pullup_18_out, pullup_19_out, pullup_20_out,
       pullup_21_out, pullup_22_out, pullup_23_out, pullup_24_out, pullup_25_out, pullup_26_out,
       pullup_27_out, pullup_28_out, pullup_29_out, pullup_30_out, pullup_31_out, pullup_32_out;

  Decoder #(.Selector_Bits(2)) decoder_1 (
    .sel({R1, R0}), .out_0(decoder_1_out_0), .out_1(decoder_1_out_1), .out_2(decoder_1_out_2),
    .out_3(decoder_1_out_3));
  Demultiplexer #(.Selector_Bits(2)) demultiplexer_1 (
    .sel({C1, C0}), .in(WE), .out_0(demultiplexer_1_out_0), .out_1(demultiplexer_1_out_1),
    .out_2(demultiplexer_1_out_2), .out_3(demultiplexer_1_out_3));
  PFET pfet_1 (.G(demultiplexer_1_out_0), .S(1'b1), .D(pfet_1_d));
  NFET nfet_1 (.G(demultiplexer_1_out_0), .D(pfet_1_d), .S(1'b0));
  NFET nfet_2 (.G(decoder_1_out_0), .D(nfet_2_d), .S(nfet_2_s));
  NFET nfet_3 (.G(decoder_1_out_1), .D(nfet_2_d), .S(nfet_3_s));
  NFET nfet_4 (.G(decoder_1_out_2), .D(nfet_2_d), .S(nfet_4_s));
  NFET nfet_5 (.G(decoder_1_out_3), .D(nfet_2_d), .S(nfet_5_s));
  PullUp pullup_1 (.out(pullup_1_out));
  LED led_1 (.in(pfet_2_d));
  PFET pfet_2 (.G(nfet_2_s), .S(pullup_1_out), .D(pfet_2_d));
  NFET nfet_6 (.G(nfet_2_s), .D(pfet_2_d), .S(nfet_6_s));
  PullDown pulldown_1 (.out(nfet_6_s));
  PullUp pullup_2 (.out(pullup_2_out));
  LED led_2 (.in(pfet_3_d));
  PFET pfet_3 (.G(nfet_3_s), .S(pullup_2_out), .D(pfet_3_d));
  NFET nfet_7 (.G(nfet_3_s), .D(pfet_3_d), .S(nfet_7_s));
  PullDown pulldown_2 (.out(nfet_7_s));
  PullUp pullup_3 (.out(pullup_3_out));
  LED led_3 (.in(pfet_4_d));
  PFET pfet_4 (.G(nfet_4_s), .S(pullup_3_out), .D(pfet_4_d));
  NFET nfet_8 (.G(nfet_4_s), .D(pfet_4_d), .S(nfet_8_s));
  PullDown pulldown_3 (.out(nfet_8_s));
  PullUp pullup_4 (.out(pullup_4_out));
  LED led_4 (.in(pfet_5_d));
  PFET pfet_5 (.G(nfet_5_s), .S(pullup_4_out), .D(pfet_5_d));
  NFET nfet_9 (.G(nfet_5_s), .D(pfet_5_d), .S(nfet_9_s));
  PullDown pulldown_4 (.out(nfet_9_s));
  PFET pfet_6 (.G(pfet_1_d), .S(1'b1), .D(pfet_6_d));
  PFET pfet_7 (.G(D_In), .S(pfet_6_d), .D(nfet_2_d));
  NFET nfet_10 (.G(D_In), .D(nfet_2_d), .S(nfet_10_s));
  NFET nfet_11 (.G(demultiplexer_1_out_0), .D(nfet_10_s), .S(1'b0));
  PullUp pullup_5 (.out(pullup_5_out));
  PFET pfet_8 (.G(pfet_2_d), .S(pullup_5_out), .D(nfet_2_s));
  NFET nfet_12 (.G(pfet_2_d), .D(nfet_2_s), .S(nfet_12_s));
  NFET nfet_13 (.G(decoder_1_out_0), .D(pfet_2_d), .S(nfet_13_s));
  PullDown pulldown_5 (.out(nfet_12_s));
  PullUp pullup_6 (.out(pullup_6_out));
  PFET pfet_9 (.G(pfet_3_d), .S(pullup_6_out), .D(nfet_3_s));
  NFET nfet_14 (.G(pfet_3_d), .D(nfet_3_s), .S(nfet_14_s));
  NFET nfet_15 (.G(decoder_1_out_1), .D(pfet_3_d), .S(nfet_13_s));
  PullDown pulldown_6 (.out(nfet_14_s));
  PullUp pullup_7 (.out(pullup_7_out));
  PFET pfet_10 (.G(pfet_4_d), .S(pullup_7_out), .D(nfet_4_s));
  NFET nfet_16 (.G(pfet_4_d), .D(nfet_4_s), .S(nfet_16_s));
  NFET nfet_17 (.G(decoder_1_out_2), .D(pfet_4_d), .S(nfet_13_s));
  PullDown pulldown_7 (.out(nfet_16_s));
  PullUp pullup_8 (.out(pullup_8_out));
  PFET pfet_11 (.G(pfet_5_d), .S(pullup_8_out), .D(nfet_5_s));
  NFET nfet_18 (.G(pfet_5_d), .D(nfet_5_s), .S(nfet_18_s));
  NFET nfet_19 (.G(decoder_1_out_3), .D(pfet_5_d), .S(nfet_13_s));
  PullDown pulldown_8 (.out(nfet_18_s));
  PFET pfet_12 (.G(pfet_1_d), .S(1'b1), .D(pfet_12_d));
  PFET pfet_13 (.G(nfet_2_d), .S(pfet_12_d), .D(nfet_13_s));
  NFET nfet_20 (.G(nfet_2_d), .D(nfet_13_s), .S(nfet_20_s));
  NFET nfet_21 (.G(demultiplexer_1_out_0), .D(nfet_20_s), .S(1'b0));
  NFET nfet_22 (.G(decoder_1_out_0), .D(nfet_22_d), .S(nfet_22_s));
  NFET nfet_23 (.G(decoder_1_out_1), .D(nfet_22_d), .S(nfet_23_s));
  NFET nfet_24 (.G(decoder_1_out_2), .D(nfet_22_d), .S(nfet_24_s));
  NFET nfet_25 (.G(decoder_1_out_3), .D(nfet_22_d), .S(nfet_25_s));
  PFET pfet_14 (.G(demultiplexer_1_out_1), .S(1'b1), .D(pfet_14_d));
  NFET nfet_26 (.G(demultiplexer_1_out_1), .D(pfet_14_d), .S(1'b0));
  PullUp pullup_9 (.out(pullup_9_out));
  PFET pfet_15 (.G(nfet_22_s), .S(pullup_9_out), .D(pfet_15_d));
  NFET nfet_27 (.G(nfet_22_s), .D(pfet_15_d), .S(nfet_27_s));
  PullDown pulldown_9 (.out(nfet_27_s));
  PullUp pullup_10 (.out(pullup_10_out));
  PFET pfet_16 (.G(nfet_23_s), .S(pullup_10_out), .D(pfet_16_d));
  NFET nfet_28 (.G(nfet_23_s), .D(pfet_16_d), .S(nfet_28_s));
  PullDown pulldown_10 (.out(nfet_28_s));
  PullUp pullup_11 (.out(pullup_11_out));
  PFET pfet_17 (.G(nfet_24_s), .S(pullup_11_out), .D(pfet_17_d));
  NFET nfet_29 (.G(nfet_24_s), .D(pfet_17_d), .S(nfet_29_s));
  PullDown pulldown_11 (.out(nfet_29_s));
  PullUp pullup_12 (.out(pullup_12_out));
  PFET pfet_18 (.G(nfet_25_s), .S(pullup_12_out), .D(pfet_18_d));
  NFET nfet_30 (.G(nfet_25_s), .D(pfet_18_d), .S(nfet_30_s));
  PullDown pulldown_12 (.out(nfet_30_s));
  PFET pfet_19 (.G(pfet_14_d), .S(1'b1), .D(pfet_19_d));
  PFET pfet_20 (.G(D_In), .S(pfet_19_d), .D(nfet_22_d));
  NFET nfet_31 (.G(D_In), .D(nfet_22_d), .S(nfet_31_s));
  NFET nfet_32 (.G(demultiplexer_1_out_1), .D(nfet_31_s), .S(1'b0));
  PullUp pullup_13 (.out(pullup_13_out));
  LED led_5 (.in(pfet_15_d));
  PFET pfet_21 (.G(pfet_15_d), .S(pullup_13_out), .D(nfet_22_s));
  NFET nfet_33 (.G(pfet_15_d), .D(nfet_22_s), .S(nfet_33_s));
  PullDown pulldown_13 (.out(nfet_33_s));
  PullUp pullup_14 (.out(pullup_14_out));
  LED led_6 (.in(pfet_16_d));
  PFET pfet_22 (.G(pfet_16_d), .S(pullup_14_out), .D(nfet_23_s));
  NFET nfet_34 (.G(pfet_16_d), .D(nfet_23_s), .S(nfet_34_s));
  PullDown pulldown_14 (.out(nfet_34_s));
  PullUp pullup_15 (.out(pullup_15_out));
  LED led_7 (.in(pfet_17_d));
  PFET pfet_23 (.G(pfet_17_d), .S(pullup_15_out), .D(nfet_24_s));
  NFET nfet_35 (.G(pfet_17_d), .D(nfet_24_s), .S(nfet_35_s));
  PullDown pulldown_15 (.out(nfet_35_s));
  PullUp pullup_16 (.out(pullup_16_out));
  LED led_8 (.in(pfet_18_d));
  PFET pfet_24 (.G(pfet_18_d), .S(pullup_16_out), .D(nfet_25_s));
  NFET nfet_36 (.G(pfet_18_d), .D(nfet_25_s), .S(nfet_36_s));
  PullDown pulldown_16 (.out(nfet_36_s));
  NFET nfet_37 (.G(decoder_1_out_0), .D(pfet_15_d), .S(nfet_37_s));
  NFET nfet_38 (.G(decoder_1_out_1), .D(pfet_16_d), .S(nfet_37_s));
  NFET nfet_39 (.G(decoder_1_out_2), .D(pfet_17_d), .S(nfet_37_s));
  NFET nfet_40 (.G(decoder_1_out_3), .D(pfet_18_d), .S(nfet_37_s));
  PFET pfet_25 (.G(pfet_14_d), .S(1'b1), .D(pfet_25_d));
  PFET pfet_26 (.G(nfet_22_d), .S(pfet_25_d), .D(nfet_37_s));
  NFET nfet_41 (.G(nfet_22_d), .D(nfet_37_s), .S(nfet_41_s));
  NFET nfet_42 (.G(demultiplexer_1_out_1), .D(nfet_41_s), .S(1'b0));
  PFET pfet_27 (.G(demultiplexer_1_out_2), .S(1'b1), .D(pfet_27_d));
  NFET nfet_43 (.G(demultiplexer_1_out_2), .D(pfet_27_d), .S(1'b0));
  NFET nfet_44 (.G(decoder_1_out_0), .D(nfet_44_d), .S(nfet_44_s));
  NFET nfet_45 (.G(decoder_1_out_1), .D(nfet_44_d), .S(nfet_45_s));
  NFET nfet_46 (.G(decoder_1_out_2), .D(nfet_44_d), .S(nfet_46_s));
  NFET nfet_47 (.G(decoder_1_out_3), .D(nfet_44_d), .S(nfet_47_s));
  PullUp pullup_17 (.out(pullup_17_out));
  LED led_9 (.in(pfet_28_d));
  PFET pfet_28 (.G(nfet_44_s), .S(pullup_17_out), .D(pfet_28_d));
  NFET nfet_48 (.G(nfet_44_s), .D(pfet_28_d), .S(nfet_48_s));
  PullDown pulldown_17 (.out(nfet_48_s));
  PullUp pullup_18 (.out(pullup_18_out));
  LED led_10 (.in(pfet_29_d));
  PFET pfet_29 (.G(nfet_45_s), .S(pullup_18_out), .D(pfet_29_d));
  NFET nfet_49 (.G(nfet_45_s), .D(pfet_29_d), .S(nfet_49_s));
  PullDown pulldown_18 (.out(nfet_49_s));
  PullUp pullup_19 (.out(pullup_19_out));
  LED led_11 (.in(pfet_30_d));
  PFET pfet_30 (.G(nfet_46_s), .S(pullup_19_out), .D(pfet_30_d));
  NFET nfet_50 (.G(nfet_46_s), .D(pfet_30_d), .S(nfet_50_s));
  PullDown pulldown_19 (.out(nfet_50_s));
  PullUp pullup_20 (.out(pullup_20_out));
  LED led_12 (.in(pfet_31_d));
  PFET pfet_31 (.G(nfet_47_s), .S(pullup_20_out), .D(pfet_31_d));
  NFET nfet_51 (.G(nfet_47_s), .D(pfet_31_d), .S(nfet_51_s));
  PullDown pulldown_20 (.out(nfet_51_s));
  PFET pfet_32 (.G(pfet_27_d), .S(1'b1), .D(pfet_32_d));
  PFET pfet_33 (.G(D_In), .S(pfet_32_d), .D(nfet_44_d));
  NFET nfet_52 (.G(D_In), .D(nfet_44_d), .S(nfet_52_s));
  NFET nfet_53 (.G(demultiplexer_1_out_2), .D(nfet_52_s), .S(1'b0));
  PullUp pullup_21 (.out(pullup_21_out));
  PFET pfet_34 (.G(pfet_28_d), .S(pullup_21_out), .D(nfet_44_s));
  NFET nfet_54 (.G(pfet_28_d), .D(nfet_44_s), .S(nfet_54_s));
  NFET nfet_55 (.G(decoder_1_out_0), .D(pfet_28_d), .S(nfet_55_s));
  PullDown pulldown_21 (.out(nfet_54_s));
  PullUp pullup_22 (.out(pullup_22_out));
  PFET pfet_35 (.G(pfet_29_d), .S(pullup_22_out), .D(nfet_45_s));
  NFET nfet_56 (.G(pfet_29_d), .D(nfet_45_s), .S(nfet_56_s));
  NFET nfet_57 (.G(decoder_1_out_1), .D(pfet_29_d), .S(nfet_55_s));
  PullDown pulldown_22 (.out(nfet_56_s));
  PullUp pullup_23 (.out(pullup_23_out));
  PFET pfet_36 (.G(pfet_30_d), .S(pullup_23_out), .D(nfet_46_s));
  NFET nfet_58 (.G(pfet_30_d), .D(nfet_46_s), .S(nfet_58_s));
  NFET nfet_59 (.G(decoder_1_out_2), .D(pfet_30_d), .S(nfet_55_s));
  PullDown pulldown_23 (.out(nfet_58_s));
  PullUp pullup_24 (.out(pullup_24_out));
  PFET pfet_37 (.G(pfet_31_d), .S(pullup_24_out), .D(nfet_47_s));
  NFET nfet_60 (.G(pfet_31_d), .D(nfet_47_s), .S(nfet_60_s));
  NFET nfet_61 (.G(decoder_1_out_3), .D(pfet_31_d), .S(nfet_55_s));
  PullDown pulldown_24 (.out(nfet_60_s));
  PFET pfet_38 (.G(pfet_27_d), .S(1'b1), .D(pfet_38_d));
  PFET pfet_39 (.G(nfet_44_d), .S(pfet_38_d), .D(nfet_55_s));
  NFET nfet_62 (.G(nfet_44_d), .D(nfet_55_s), .S(nfet_62_s));
  NFET nfet_63 (.G(demultiplexer_1_out_2), .D(nfet_62_s), .S(1'b0));
  NFET nfet_64 (.G(decoder_1_out_0), .D(nfet_64_d), .S(nfet_64_s));
  NFET nfet_65 (.G(decoder_1_out_1), .D(nfet_64_d), .S(nfet_65_s));
  NFET nfet_66 (.G(decoder_1_out_2), .D(nfet_64_d), .S(nfet_66_s));
  NFET nfet_67 (.G(decoder_1_out_3), .D(nfet_64_d), .S(nfet_67_s));
  PFET pfet_40 (.G(demultiplexer_1_out_3), .S(1'b1), .D(pfet_40_d));
  NFET nfet_68 (.G(demultiplexer_1_out_3), .D(pfet_40_d), .S(1'b0));
  PullUp pullup_25 (.out(pullup_25_out));
  PFET pfet_41 (.G(nfet_64_s), .S(pullup_25_out), .D(pfet_41_d));
  NFET nfet_69 (.G(nfet_64_s), .D(pfet_41_d), .S(nfet_69_s));
  PullDown pulldown_25 (.out(nfet_69_s));
  PullUp pullup_26 (.out(pullup_26_out));
  PFET pfet_42 (.G(nfet_65_s), .S(pullup_26_out), .D(pfet_42_d));
  NFET nfet_70 (.G(nfet_65_s), .D(pfet_42_d), .S(nfet_70_s));
  PullDown pulldown_26 (.out(nfet_70_s));
  PullUp pullup_27 (.out(pullup_27_out));
  PFET pfet_43 (.G(nfet_66_s), .S(pullup_27_out), .D(pfet_43_d));
  NFET nfet_71 (.G(nfet_66_s), .D(pfet_43_d), .S(nfet_71_s));
  PullDown pulldown_27 (.out(nfet_71_s));
  PullUp pullup_28 (.out(pullup_28_out));
  PFET pfet_44 (.G(nfet_67_s), .S(pullup_28_out), .D(pfet_44_d));
  NFET nfet_72 (.G(nfet_67_s), .D(pfet_44_d), .S(nfet_72_s));
  PullDown pulldown_28 (.out(nfet_72_s));
  PFET pfet_45 (.G(pfet_40_d), .S(1'b1), .D(pfet_45_d));
  PFET pfet_46 (.G(D_In), .S(pfet_45_d), .D(nfet_64_d));
  NFET nfet_73 (.G(D_In), .D(nfet_64_d), .S(nfet_73_s));
  NFET nfet_74 (.G(demultiplexer_1_out_3), .D(nfet_73_s), .S(1'b0));
  PullUp pullup_29 (.out(pullup_29_out));
  LED led_13 (.in(pfet_41_d));
  PFET pfet_47 (.G(pfet_41_d), .S(pullup_29_out), .D(nfet_64_s));
  NFET nfet_75 (.G(pfet_41_d), .D(nfet_64_s), .S(nfet_75_s));
  PullDown pulldown_29 (.out(nfet_75_s));
  PullUp pullup_30 (.out(pullup_30_out));
  LED led_14 (.in(pfet_42_d));
  PFET pfet_48 (.G(pfet_42_d), .S(pullup_30_out), .D(nfet_65_s));
  NFET nfet_76 (.G(pfet_42_d), .D(nfet_65_s), .S(nfet_76_s));
  PullDown pulldown_30 (.out(nfet_76_s));
  PullUp pullup_31 (.out(pullup_31_out));
  LED led_15 (.in(pfet_43_d));
  PFET pfet_49 (.G(pfet_43_d), .S(pullup_31_out), .D(nfet_66_s));
  NFET nfet_77 (.G(pfet_43_d), .D(nfet_66_s), .S(nfet_77_s));
  PullDown pulldown_31 (.out(nfet_77_s));
  PullUp pullup_32 (.out(pullup_32_out));
  LED led_16 (.in(pfet_44_d));
  PFET pfet_50 (.G(pfet_44_d), .S(pullup_32_out), .D(nfet_67_s));
  NFET nfet_78 (.G(pfet_44_d), .D(nfet_67_s), .S(nfet_78_s));
  PullDown pulldown_32 (.out(nfet_78_s));
  NFET nfet_79 (.G(decoder_1_out_0), .D(pfet_41_d), .S(nfet_79_s));
  NFET nfet_80 (.G(decoder_1_out_1), .D(pfet_42_d), .S(nfet_79_s));
  NFET nfet_81 (.G(decoder_1_out_2), .D(pfet_43_d), .S(nfet_79_s));
  NFET nfet_82 (.G(decoder_1_out_3), .D(pfet_44_d), .S(nfet_79_s));
  PFET pfet_51 (.G(pfet_40_d), .S(1'b1), .D(pfet_51_d));
  PFET pfet_52 (.G(nfet_64_d), .S(pfet_51_d), .D(nfet_79_s));
  NFET nfet_83 (.G(nfet_64_d), .D(nfet_79_s), .S(nfet_83_s));
  NFET nfet_84 (.G(demultiplexer_1_out_3), .D(nfet_83_s), .S(1'b0));
  Multiplexer #(.Selector_Bits(2)) multiplexer_1 (
    .sel({C1, C0}), .in_0(nfet_13_s), .in_1(nfet_37_s), .in_2(nfet_55_s), .in_3(nfet_79_s), .out(D_Out));

  // Notes on the sheet:
  //   D_In: Dateneingang zum Schreiben der Bits.
  //   R0: Zeilenleitung Bit 0
  //   R1: Zeilenleitung Bit 1
  //   D_Out: Datenausgang zum Lesen der Bits.
  //   C0: Spaltenleitung Bit 0
  //   C1: Spaltenleitung Bit 1
  //   WE: Write-Enable.
  //   Geht diese Leitung auf Eins, wird der Dateneingang
  //   in der Speichermatrix gespeichert.
endmodule

/* Test case:
C0 C1 R0 R1 WE D_In D_Out


# write all cells to zero
0  0  0  0  0  0    0
0  0  0  0  1  0    0
0  0  0  0  0  0    0

0  0  0  1  0  0    0
0  0  0  1  1  0    0
0  0  0  1  0  0    0

0  0  1  0  0  0    0
0  0  1  0  1  0    0
0  0  1  0  0  0    0

0  0  1  1  0  0    0
0  0  1  1  1  0    0
0  0  1  1  0  0    0

0  1  0  0  0  0    0
0  1  0  0  1  0    0
0  1  0  0  0  0    0

0  1  0  1  0  0    0
0  1  0  1  1  0    0
0  1  0  1  0  0    0

0  1  1  0  0  0    0
0  1  1  0  1  0    0
0  1  1  0  0  0    0

0  1  1  1  0  0    0
0  1  1  1  1  0    0
0  1  1  1  0  0    0


1  0  0  0  0  0    0
1  0  0  0  1  0    0
1  0  0  0  0  0    0

1  0  0  1  0  0    0
1  0  0  1  1  0    0
1  0  0  1  0  0    0

1  0  1  0  0  0    0
1  0  1  0  1  0    0
1  0  1  0  0  0    0

1  0  1  1  0  0    0
1  0  1  1  1  0    0
1  0  1  1  0  0    0

1  1  0  0  0  0    0
1  1  0  0  1  0    0
1  1  0  0  0  0    0

1  1  0  1  0  0    0
1  1  0  1  1  0    0
1  1  0  1  0  0    0

1  1  1  0  0  0    0
1  1  1  0  1  0    0
1  1  1  0  0  0    0

1  1  1  1  0  0    0
1  1  1  1  1  0    0
1  1  1  1  0  0    0


#write cell 00 to 1

0  0  0  0  0  0    0
0  0  0  0  1  1    1
0  0  0  0  0  1    1
0  0  0  0  0  0    1

# cell 11 is still zero

0  1  0  1  0  0    0

# cell 00 is still 1

0  0  0  0  0  0    1
*/
