// Digital circuit sram_simple.dig as structural Verilog
module sram_simple (
  input  WL0,
  input  WE,
  input  Data,
  input  WL1,
  output D
);

  wire nfet_1_d, nfet_1_s, nfet_2_d, nfet_3_s, nfet_4_s, nfet_5_s, nfet_6_s, not_1_out, pfet_1_d, pfet_2_d,
       pullup_1_out, pullup_2_out, pullup_3_out, pullup_4_out;

  NFET nfet_1 (.G(WL1), .D(nfet_1_d), .S(nfet_1_s));
  NFET nfet_2 (.G(WL0), .D(nfet_2_d), .S(nfet_1_s));
  assign nfet_1_s = WE ? not_1_out : 1'bz;  // Driver driver_1
  not not_1 (not_1_out, Data);
  PullUp pullup_1 (.out(pullup_1_out));
  PFET pfet_1 (.G(nfet_1_d), .S(pullup_1_out), .D(pfet_1_d));
  NFET nfet_3 (.G(nfet_1_d), .D(pfet_1_d), .S(nfet_3_s));
  PullDown pulldown_1 (.out(nfet_3_s));
  PullUp pullup_2 (.out(pullup_2_out));
  PFET pfet_2 (.G(nfet_2_d), .S(pullup_2_out), .D(pfet_2_d));
  NFET nfet_4 (.G(nfet_2_d), .D(pfet_2_d), .S(nfet_4_s));
  PullDown pulldown_2 (.out(nfet_4_s));
  PullUp pullup_3 (.out(pullup_3_out));
  LED led_1 (.in(pfet_1_d));
  PFET pfet_3 (.G(pfet_1_d), .S(pullup_3_out), .D(nfet_1_d));
  NFET nfet_5 (.G(pfet_1_d), .D(nfet_1_d), .S(nfet_5_s));
  PullDown pulldown_3 (.out(nfet_5_s));
  PullUp pullup_4 (.out(pullup_4_out));
  LED led_2 (.in(pfet_2_d));
  PFET pfet_4 (.G(pfet_2_d), .S(pullup_4_out), .D(nfet_2_d));
  NFET nfet_6 (.G(pfet_2_d), .D(nfet_2_d), .S(nfet_6_s));
  PullDown pulldown_4 (.out(nfet_6_s));
  NFET nfet_7 (.G(WL1), .D(D), .S(pfet_1_d));
  NFET nfet_8 (.G(WL0), .D(D), .S(pfet_2_d));
  assign D = WE ? Data : 1'bz;  // Driver driver_2

  // Notes on the sheet:
  //   WL0: Wortleitung 0
  //   WE: Write Enable
  //   Data: Data Input
  //   D: Data Output
  //   WL1: Wortleitung 1
endmodule
