// Digital circuit Adder8bit.dig as structural Verilog
// Ein 8-Bit Addierer, welcher aus zwei 4-Bit 
// CLA-Addierern aufgebaut ist.
module Adder8bit (
  input  [7:0] A,
  input  [7:0] B,
  input  C_i_1,
  output [7:0] S,
  output C
);

  FullAdderCLA fulladdercla_1 ();
  FullAdderCLA fulladdercla_2 ();

  // Notes on the sheet:
  //   A: Erstes zu addierendes 8-Bit Wort.
  //   B: Zweites zu addierendes 8-Bit Wort.
  //   S: Die 8-Bit der Summe.
  //   C: Übertrag der Addition
  //   C_i_1: Übertrag aus dem vorhergehenden Addierer.
endmodule

/* Test case:
C_i-1 A B    C   S
for(1<<16) 0 (n>>8) (n&255) ((n>>8)+(n&255)>255) (((n>>8)+(n&255))&255)
for(1<<16) 1 (n>>8) (n&255) ((n>>8)+(n&255)+1>255) (((n>>8)+(n&255)+1)&255)
*/
