// Digital circuit Bus.dig as structural Verilog
// Einfache Schaltung die eine Adressdecodierung 
// zeigt. Der Zähler erzeugt eine 5-Bit Zahl.
// Die unteren drei Bit werden als Adresse an alle 
// ROM-Bausteine ausgegeben. Die oberen zwei Bits
// werden verwendet um über den Adressdecoder 
// einen der vier ROM-Bausteine auszuwählen, welcher dann
// sein Datenwort an den Datenbus legt. Durch den 
// Adressdecoder verhalten sich die vier ROM-Bausteine wie
// ein einziger viermal so großer ROM-Baustein.
// Alle Ausgänge der ROMs liegen auf einem Datenbus. Dies ist
// möglich, da immer nur der Ausgang eines der vier ROMs aktiv 
// ist. Die jeweils anderen Ausgänge sind hochohmig.
module Bus (
  input  Clock,
  output [7:0] Data
);

  wire decoder_1_out_0, decoder_1_out_1, decoder_1_out_2, decoder_1_out_3;
  wire [4:0] Address_out;

  Counter #(.Bits(5)) Address (.en(Clock), .C(1'b1), .clr(1'b0), .out(Address_out));  // open: ovf
  Decoder #(.Selector_Bits(2)) decoder_1 (
    .sel(Address_out[4:3]), .out_0(decoder_1_out_0), .out_1(decoder_1_out_1), .out_2(decoder_1_out_2),
    .out_3(decoder_1_out_3));
  ROM #(.AddrBits(3), .Bits(8), .Addr_Bits(3)) rom_1 (.A(Address_out[2:0]), .sel(decoder_1_out_0), .D(Data));
  ROM #(.AddrBits(3), .Bits(8), .Addr_Bits(3)) rom_2 (.A(Address_out[2:0]), .sel(decoder_1_out_1), .D(Data));
  ROM #(.AddrBits(3), .Bits(8), .Addr_Bits(3)) rom_3 (.A(Address_out[2:0]), .sel(decoder_1_out_2), .D(Data));
  ROM #(.AddrBits(3), .Bits(8), .Addr_Bits(3)) rom_4 (.A(Address_out[2:0]), .sel(decoder_1_out_3), .D(Data));

  // Notes on the sheet:
  //   Clock: Hz: 2
  //   contents of rom_1 (hex, n*v repeats v):
  //   44,69,65,73,20,69,73,74
  //   contents of rom_2 (hex, n*v repeats v):
  //   20,65,69,6e,20,6c,61,6e
  //   contents of rom_3 (hex, n*v repeats v):
  //   67,65,72,20,54,65,73,74
  //   contents of rom_4 (hex, n*v repeats v):
  //   74,65,78,74,2e,20,20,20
endmodule

/* Test case:
Clock Data
  0    0x44
  c    0x69
  c    0x65
  c    0x73
  c    0x20
  c    0x69
  c    0x73
  c    0x74

  c    0x20
  c    0x65
  c    0x69
  c    0x6E
  c    0x20
  c    0x6C
  c    0x61
  c    0x6E

  c    0x67
  c    0x65
  c    0x72
  c    0x20
  c    0x54
  c    0x65
  c    0x73
  c    0x74

  c    0x74
  c    0x65
  c    0x78
  c    0x74
  c    0x2E
  c    0x20
  c    0x20
  c    0x20

# repeat first block
  c    0x44
  c    0x69
  c    0x65
  c    0x73
  c    0x20
  c    0x69
  c    0x73
  c    0x74
*/
