// Digital circuit Comp.dig as structural Verilog
module Comp (
  input  P,
  input  Q,
  output P_lt_Q,
  output P_eq_Q,
  output P_gt_Q
);

  wire not_1_out, not_2_out;

  not not_1 (not_1_out, P);
  not not_2 (not_2_out, Q);
  and and_1 (P_lt_Q, not_1_out, Q);
  and and_2 (P_gt_Q, P, not_2_out);
  nor nor_1 (P_eq_Q, P_lt_Q, P_gt_Q);
endmodule
