// Digital circuit Comp7485.dig as structural Verilog
// Comparator which corresponds to the function of a 74x85. 
// The three inputs with the Compare bits are output directly 
// if the P and Q bits are equal.
// {{de Komparator welcher der Funktion eines
// 74x85 entspricht. Die drei Eingänge mit den
// Vergleichsbits werden direkt wieder ausgegeben,
// wenn die jeweiligen P und Q-Bits übereinstimmen.}}
module Comp7485 (
  input  P_0,
  input  P_1,
  input  P_2,
  input  P_3,
  input  P_lt_Q_i,
  input  P_eq_Q_i,
  input  P_gt_Q_i,
  input  Q_0,
  input  Q_1,
  input  Q_2,
  input  Q_3,
  output P_lt_Q,
  output P_eq_Q,
  output P_gt_Q
);

  wire and_1_out, and_2_out, and_3_out, and_4_out, and_5_out, and_6_out, and_7_out, and_8_out, and_9_out,
       and_10_out, xnor_1_out, xnor_2_out, xnor_3_out, xnor_4_out;

  xnor xnor_1 (xnor_1_out, Q_0, P_0);
  xnor xnor_2 (xnor_2_out, Q_1, P_1);
  xnor xnor_3 (xnor_3_out, Q_2, P_2);
  xnor xnor_4 (xnor_4_out, Q_3, P_3);
  and and_1 (and_1_out, ~Q_3, P_3);  // And
  and and_2 (and_2_out, xnor_4_out, ~Q_2, P_2);  // And
  and and_3 (and_3_out, xnor_4_out, xnor_3_out, ~Q_1, P_1);  // And
  and and_4 (and_4_out, xnor_4_out, xnor_3_out, xnor_2_out, ~Q_0, P_0);  // And
  and and_5 (and_5_out, xnor_4_out, xnor_3_out, xnor_2_out, xnor_1_out, P_gt_Q_i);
  and and_6 (and_6_out, P_lt_Q_i, xnor_4_out, xnor_3_out, xnor_2_out, xnor_1_out);
  and and_7 (and_7_out, Q_3, ~P_3);  // And
  and and_8 (and_8_out, xnor_4_out, Q_2, ~P_2);  // And
  and and_9 (and_9_out, xnor_4_out, xnor_3_out, Q_1, ~P_1);  // And
  and and_10 (and_10_out, xnor_4_out, xnor_3_out, xnor_2_out, Q_0, ~P_0);  // And
  or or_1 (P_gt_Q, and_1_out, and_2_out, and_3_out, and_4_out, and_5_out);
  and and_11 (P_eq_Q, xnor_4_out, xnor_3_out, P_eq_Q_i, xnor_2_out, xnor_1_out);
  or or_2 (P_lt_Q, and_6_out, and_7_out, and_8_out, and_9_out, and_10_out);

  // Notes on the sheet:
  //   P_eq_Q_i: default 1
endmodule

/* Test case:
   P<Q_i P=Q_i P>Q_i  P_3 P_2 P_1 P_0   Q_3 Q_2 Q_1 Q_0  P<Q   P=Q   P>Q
loop(P,16)
  loop(Q,16)
    0    1     0      bits(4,P)         bits(4,Q)        (P<Q) (P=Q) (P>Q)
  end loop
end loop

loop (i,16)
  loop (z,16)
    bits(3,z)         bits(4,i)         bits(4,i)        bits(3,z)
  end loop
end loop
*/
