// Digital circuit CompEN.dig as structural Verilog
module CompEN (
  input  EN,
  input  P,
  input  Q,
  output P_lt_Q,
  output P_eq_Q,
  output P_gt_Q
);

  wire and_1_out, and_2_out, comp_1_p_eq_q;

  and and_1 (and_1_out, P, EN);
  and and_2 (and_2_out, EN, Q);
  Comp comp_1 (.P(and_1_out), .Q(and_2_out), .P_lt_Q(P_lt_Q), .P_eq_Q(comp_1_p_eq_q), .P_gt_Q(P_gt_Q));
  and and_3 (P_eq_Q, comp_1_p_eq_q, EN);
endmodule
