// Digital circuit DaddaMultiplier.dig as structural Verilog
module DaddaMultiplier (
  input  [7:0] A,
  input  [7:0] B,
  output [15:0] Y
);

  wire fulladder_1_p4, fulladder_1_p5, fulladder_2_p4, fulladder_2_p5, fulladder_3_p4, fulladder_3_p5,
       fulladder_4_p4, fulladder_4_p5, fulladder_5_p4, fulladder_5_p5, fulladder_6_p4, fulladder_6_p5,
       fulladder_7_p4, fulladder_7_p5, fulladder_8_p4, fulladder_8_p5, fulladder_9_p4, fulladder_9_p5,
       fulladder_10_p4, fulladder_10_p5, fulladder_11_p4, fulladder_11_p5, fulladder_12_p4, fulladder_12_p5,
       fulladder_13_p4, fulladder_13_p5, fulladder_14_p4, fulladder_14_p5, fulladder_15_p4, fulladder_15_p5,
       fulladder_16_p4, fulladder_16_p5, fulladder_17_p4, fulladder_17_p5, fulladder_18_p4, fulladder_18_p5,
       fulladder_19_p4, fulladder_19_p5, fulladder_20_p4, fulladder_20_p5, fulladder_21_p4, fulladder_21_p5,
       fulladder_22_p4, fulladder_22_p5, fulladder_23_p4, fulladder_23_p5, fulladder_24_p4, fulladder_24_p5,
       halfadder_1_p3, halfadder_1_p4, halfadder_2_p3, halfadder_2_p4, halfadder_3_p3, halfadder_3_p4,
       halfadder_4_p3, halfadder_4_p4, halfadder_5_p3, halfadder_5_p4, halfadder_6_p3, halfadder_6_p4;
  wire [6:0] and_8_out;
  wire [7:0] and_3_out, and_4_out, and_5_out, and_6_out, and_7_out, bitextender_1_out, bitextender_2_out,
       bitextender_3_out, bitextender_4_out, bitextender_5_out, bitextender_6_out, bitextender_7_out,
       bitextender_8_out;
  wire [7:1] and_2_out_2;
  wire [7:3] and_1_out_2;
  wire [13:0] and_1_out, and_2_out;

  BitExtender #(.inputBits(1), .outputBits(8)) bitextender_1 (.in(B[0]), .out(bitextender_1_out));
  BitExtender #(.inputBits(1), .outputBits(8)) bitextender_2 (.in(B[1]), .out(bitextender_2_out));
  BitExtender #(.inputBits(1), .outputBits(8)) bitextender_3 (.in(B[2]), .out(bitextender_3_out));
  BitExtender #(.inputBits(1), .outputBits(8)) bitextender_4 (.in(B[3]), .out(bitextender_4_out));
  BitExtender #(.inputBits(1), .outputBits(8)) bitextender_5 (.in(B[4]), .out(bitextender_5_out));
  BitExtender #(.inputBits(1), .outputBits(8)) bitextender_6 (.in(B[5]), .out(bitextender_6_out));
  BitExtender #(.inputBits(1), .outputBits(8)) bitextender_7 (.in(B[6]), .out(bitextender_7_out));
  BitExtender #(.inputBits(1), .outputBits(8)) bitextender_8 (.in(B[7]), .out(bitextender_8_out));
  assign {and_1_out_2, and_1_out[1:0], Y[0]} = A & bitextender_1_out;  // And and_1, 8 bits wide
  assign {and_2_out_2, and_2_out[0]} = A & bitextender_2_out;  // And and_2, 8 bits wide
  assign and_3_out = A & bitextender_3_out;  // And and_3, 8 bits wide
  assign and_4_out = A & bitextender_4_out;  // And and_4, 8 bits wide
  assign and_5_out = A & bitextender_5_out;  // And and_5, 8 bits wide
  assign and_6_out = A & bitextender_6_out;  // And and_6, 8 bits wide
  assign and_7_out = A & bitextender_7_out;  // And and_7, 8 bits wide
  assign {and_2_out[13], and_8_out} = A & bitextender_8_out;  // And and_8, 8 bits wide
  // HalfAdder halfadder_1: pin names not known; wires that end beside it: and_1_out_2[6], and_2_out_2[5], halfadder_1_p3, halfadder_1_p4
  // FullAdder fulladder_1: pin names not known; wires that end beside it: and_1_out_2[7], and_2_out_2[6], and_3_out[5], fulladder_1_p4, fulladder_1_p5
  // HalfAdder halfadder_2: pin names not known; wires that end beside it: and_5_out[3], and_6_out[2], halfadder_2_p3, halfadder_2_p4
  // FullAdder fulladder_2: pin names not known; wires that end beside it: and_2_out_2[7], and_3_out[6], and_4_out[5], fulladder_2_p4, fulladder_2_p5
  // HalfAdder halfadder_3: pin names not known; wires that end beside it: and_6_out[3], and_7_out[2], halfadder_3_p3, halfadder_3_p4
  // FullAdder fulladder_3: pin names not known; wires that end beside it: and_3_out[7], and_4_out[6], and_5_out[5], fulladder_3_p4, fulladder_3_p5
  // HalfAdder halfadder_4: pin names not known; wires that end beside it: and_1_out_2[4], and_2_out_2[3], halfadder_4_p3, halfadder_4_p4
  // FullAdder fulladder_4: pin names not known; wires that end beside it: and_1_out_2[5], and_2_out_2[4], and_3_out[3], fulladder_4_p4, fulladder_4_p5
  // HalfAdder halfadder_5: pin names not known; wires that end beside it: and_5_out[1], and_6_out[0], halfadder_5_p3, halfadder_5_p4
  // FullAdder fulladder_5: pin names not known; wires that end beside it: halfadder_1_p3, and_4_out[3], and_3_out[4], fulladder_5_p4, fulladder_5_p5
  // FullAdder fulladder_6: pin names not known; wires that end beside it: and_5_out[2], and_6_out[1], and_7_out[0], fulladder_6_p4, fulladder_6_p5
  // FullAdder fulladder_7: pin names not known; wires that end beside it: halfadder_1_p4, fulladder_1_p4, and_4_out[4], fulladder_7_p4, fulladder_7_p5
  // FullAdder fulladder_8: pin names not known; wires that end beside it: halfadder_2_p3, and_7_out[1], and_8_out[0], fulladder_8_p4, fulladder_8_p5
  // FullAdder fulladder_9: pin names not known; wires that end beside it: fulladder_1_p5, halfadder_2_p4, fulladder_2_p4, fulladder_9_p4, fulladder_9_p5
  // FullAdder fulladder_10: pin names not known; wires that end beside it: and_5_out[4], halfadder_3_p3, and_8_out[1], fulladder_10_p4, fulladder_10_p5
  // FullAdder fulladder_11: pin names not known; wires that end beside it: fulladder_2_p5, halfadder_3_p4, fulladder_3_p4, fulladder_11_p4, fulladder_11_p5
  // FullAdder fulladder_12: pin names not known; wires that end beside it: and_6_out[4], and_7_out[3], and_8_out[2], fulladder_12_p4, fulladder_12_p5
  // FullAdder fulladder_13: pin names not known; wires that end beside it: fulladder_3_p5, and_4_out[7], and_5_out[6], fulladder_13_p4, fulladder_13_p5
  // FullAdder fulladder_14: pin names not known; wires that end beside it: and_6_out[5], and_7_out[4], and_8_out[3], fulladder_14_p4, fulladder_14_p5
  // FullAdder fulladder_15: pin names not known; wires that end beside it: and_5_out[7], and_6_out[6], and_7_out[5], fulladder_15_p4, fulladder_15_p5
  // HalfAdder halfadder_6: pin names not known; wires that end beside it: and_3_out[1], and_4_out[0], halfadder_6_p3, halfadder_6_p4
  // FullAdder fulladder_16: pin names not known; wires that end beside it: halfadder_4_p3, and_5_out[0], and_3_out[2], fulladder_16_p4, fulladder_16_p5
  // FullAdder fulladder_17: pin names not known; wires that end beside it: fulladder_4_p4, halfadder_4_p4, and_4_out[2], fulladder_17_p4, fulladder_17_p5
  // FullAdder fulladder_18: pin names not known; wires that end beside it: fulladder_4_p5, halfadder_5_p4, fulladder_5_p4, fulladder_18_p4, fulladder_18_p5
  // FullAdder fulladder_19: pin names not known; wires that end beside it: fulladder_5_p5, fulladder_6_p5, fulladder_7_p4, fulladder_19_p4, fulladder_19_p5
  // FullAdder fulladder_20: pin names not known; wires that end beside it: fulladder_7_p5, fulladder_8_p5, fulladder_9_p4, fulladder_20_p4, fulladder_20_p5
  // FullAdder fulladder_21: pin names not known; wires that end beside it: fulladder_9_p5, fulladder_10_p5, fulladder_11_p4, fulladder_21_p4, fulladder_21_p5
  // FullAdder fulladder_22: pin names not known; wires that end beside it: fulladder_12_p5, fulladder_11_p5, fulladder_13_p4, fulladder_22_p4, fulladder_22_p5
  // FullAdder fulladder_23: pin names not known; wires that end beside it: fulladder_13_p5, fulladder_14_p5, fulladder_15_p4, fulladder_23_p4, fulladder_23_p5
  // FullAdder fulladder_24: pin names not known; wires that end beside it: fulladder_15_p5, and_6_out[7], and_7_out[6], fulladder_24_p4, fulladder_24_p5
  // HalfAdder halfadder_7: pin names not known; wires that end beside it: and_2_out_2[1], and_3_out[0], and_2_out[1], and_1_out[2]
  // FullAdder fulladder_25: pin names not known; wires that end beside it: and_1_out_2[3], and_2_out_2[2], halfadder_6_p3, and_2_out[2], and_1_out[3]
  // FullAdder fulladder_26: pin names not known; wires that end beside it: halfadder_6_p4, fulladder_16_p4, and_4_out[1], and_2_out[3], and_1_out[4]
  // FullAdder fulladder_27: pin names not known; wires that end beside it: fulladder_16_p5, fulladder_17_p4, halfadder_5_p3, and_2_out[4], and_1_out[5]
  // FullAdder fulladder_28: pin names not known; wires that end beside it: fulladder_17_p5, fulladder_18_p4, fulladder_6_p4, and_2_out[5], and_1_out[6]
  // FullAdder fulladder_29: pin names not known; wires that end beside it: fulladder_18_p5, fulladder_19_p4, fulladder_8_p4, and_2_out[6], and_1_out[7]
  // FullAdder fulladder_30: pin names not known; wires that end beside it: fulladder_19_p5, fulladder_20_p4, fulladder_10_p4, and_2_out[7], and_1_out[8]
  // FullAdder fulladder_31: pin names not known; wires that end beside it: fulladder_20_p5, fulladder_21_p4, fulladder_12_p4, and_2_out[8], and_1_out[9]
  // FullAdder fulladder_32: pin names not known; wires that end beside it: fulladder_21_p5, fulladder_22_p4, fulladder_14_p4, and_2_out[9], and_1_out[10]
  // FullAdder fulladder_33: pin names not known; wires that end beside it: fulladder_22_p5, fulladder_23_p4, and_8_out[4], and_2_out[10], and_1_out[11]
  // FullAdder fulladder_34: pin names not known; wires that end beside it: fulladder_23_p5, fulladder_24_p4, and_8_out[5], and_2_out[11], and_1_out[12]
  // FullAdder fulladder_35: pin names not known; wires that end beside it: fulladder_24_p5, and_7_out[7], and_8_out[6], and_2_out[12], and_1_out[13]
  Add #(.Bits(14)) add_1 (.a(and_1_out), .b(and_2_out), .c_i(1'b0), .s(Y[14:1]), .c_o(Y[15]));
endmodule

/* Test case:
A B Y
loop (A,256)
loop (B,256)
(A) (B) (A*B)
end loop
end loop
*/
