// Digital circuit FullAddSub_RC.dig as structural Verilog
module FullAddSub_RC (
  input  A_0,
  input  B_0,
  input  A_1,
  input  B_1,
  input  A_2,
  input  B_2,
  input  A_3,
  input  B_3,
  input  S,
  output S_0,
  output S_1,
  output S_2,
  output S_3,
  output C_3
);

  wire fulladder_1_c_i, fulladder_2_c_i, fulladder_3_c_i, xor_1_out, xor_2_out, xor_3_out, xor_4_out;

  FullAdder fulladder_1 (.A_i(A_0), .B_i(xor_1_out), .C_i_1(S), .S_i(S_0), .C_i(fulladder_1_c_i));
  xor xor_1 (xor_1_out, B_0, S);
  FullAdder fulladder_2 (.A_i(A_1), .B_i(xor_2_out), .C_i_1(fulladder_1_c_i), .S_i(S_1), .C_i(fulladder_2_c_i));
  xor xor_2 (xor_2_out, B_1, S);
  FullAdder fulladder_3 (.A_i(A_2), .B_i(xor_3_out), .C_i_1(fulladder_2_c_i), .S_i(S_2), .C_i(fulladder_3_c_i));
  xor xor_3 (xor_3_out, B_2, S);
  FullAdder fulladder_4 (.A_i(A_3), .B_i(xor_4_out), .C_i_1(fulladder_3_c_i), .S_i(S_3), .C_i(C_3));
  xor xor_4 (xor_4_out, B_3, S);
endmodule

/* Test case:
            S   A_3 A_2 A_1 A_0  B_3 B_2 B_1 B_0  S_3 S_2 S_1 S_0
loop(A,16)
  loop(B,16)
0 bits(4,A) bits(4,B) bits(4,A+B)
1 bits(4,A) bits(4,B) bits(4,A-B)
  end loop
end loop
*/
