// Digital circuit FullAdder.dig as structural Verilog
module FullAdder (
  input  A_i,
  input  B_i,
  input  C_i_1,
  output C_i,
  output S_i
);

  wire and_1_out, and_2_out, xor_1_out;

  and and_1 (and_1_out, A_i, B_i);
  xor xor_1 (xor_1_out, A_i, B_i);
  and and_2 (and_2_out, xor_1_out, C_i_1);
  xor xor_2 (S_i, xor_1_out, C_i_1);
  or or_1 (C_i, and_1_out, and_2_out);

  // Notes on the sheet:
  //   A_i: Erstes zu addierendes Bit.
  //   B_i: Zweites zu addierendes Bit.
  //   C_i_1: Übertragsbit der Vorgängerschaltung.
  //   C_i: Übertragsbit
  //   S_i: Summe
endmodule

/* Test case:
A_i B_i C_i-1 C_i S_i
 0   0   0     0   0
 0   0   1     0   1
 0   1   0     0   1
 0   1   1     1   0
 1   0   0     0   1
 1   0   1     1   0
 1   1   0     1   0
 1   1   1     1   1
*/
