// Digital circuit FullAdderCLA.dig as structural Verilog
// An adder implemented according to the carry-look-ahead method.
// {{de Ein Addierer der nach dem carry-look-ahead 
// Verfahren implementiert ist.}}
module FullAdderCLA (
  input  C_i_1,
  input  A_0,
  input  A_1,
  input  A_2,
  input  A_3,
  input  B_0,
  input  B_1,
  input  B_2,
  input  B_3,
  output S_0,
  output S_1,
  output S_2,
  output S_3,
  output C_i
);

  wire and_1_out, and_2_out, and_3_out, and_4_out, and_5_out, and_6_out, and_7_out, and_8_out, and_9_out,
       and_10_out, and_11_out, and_12_out, and_13_out, and_14_out, or_1_out, or_2_out, or_3_out, or_4_out,
       or_5_out, or_6_out, or_8_out, xor_1_out, xor_2_out, xor_3_out, xor_4_out;

  or or_1 (or_1_out, A_3, B_3);
  and and_1 (and_1_out, A_3, B_3);
  or or_2 (or_2_out, A_2, B_2);
  and and_2 (and_2_out, A_2, B_2);
  or or_3 (or_3_out, A_1, B_1);
  and and_3 (and_3_out, A_1, B_1);
  or or_4 (or_4_out, A_0, B_0);
  and and_4 (and_4_out, A_0, B_0);
  and and_5 (and_5_out, C_i_1, or_4_out, or_3_out, or_2_out, or_1_out);
  and and_6 (and_6_out, and_4_out, or_1_out, or_2_out, or_3_out);
  and and_7 (and_7_out, and_3_out, or_2_out, or_1_out);
  and and_8 (and_8_out, or_1_out, and_2_out);
  xor xor_1 (xor_1_out, or_1_out, and_1_out);
  and and_9 (and_9_out, C_i_1, or_4_out, or_3_out, or_2_out);
  and and_10 (and_10_out, or_3_out, or_2_out, and_4_out);
  and and_11 (and_11_out, or_2_out, and_3_out);
  xor xor_2 (xor_2_out, or_2_out, and_2_out);
  and and_12 (and_12_out, C_i_1, or_4_out, or_3_out);
  and and_13 (and_13_out, or_3_out, and_4_out);
  xor xor_3 (xor_3_out, or_3_out, and_3_out);
  and and_14 (and_14_out, or_4_out, C_i_1);
  xor xor_4 (xor_4_out, or_4_out, and_4_out);
  or or_5 (or_5_out, and_12_out, and_13_out, and_3_out);
  or or_6 (or_6_out, and_14_out, and_4_out);
  or or_7 (C_i, and_5_out, and_6_out, and_7_out, and_8_out, and_1_out);
  or or_8 (or_8_out, and_9_out, and_10_out, and_11_out, and_2_out);
  xor xor_5 (S_3, xor_1_out, or_8_out);
  xor xor_6 (S_2, xor_2_out, or_5_out);
  xor xor_7 (S_1, xor_3_out, or_6_out);
  xor xor_8 (S_0, xor_4_out, C_i_1);

  // Notes on the sheet:
  //   C_i_1: The carry of adding the low order bits. If the 
  //   least significant bits are added, this input is zero.
  //   {{de Der Übetrag vom Addierer welcher die 
  //   niederwertigeren Bits addiert. Werden die 
  //   niederwertigsten Bits addiert, ist dieser Eingang 
  //   Null.}}
  //   A_0: The 0. bit of the first value to add.
  //   {{de Das 0. Bit des ersten zu addierenden Wertes.}}
  //   A_1: The 1. bit of the first value to add.
  //   {{de Das 1. Bit des ersten zu addierenden Wertes.}}
  //   S_0: The 0. bit of the sum.
  //   {{de Das 0. Bit der Summe.}}
  //   A_2: The 2. bit of the first value to add.
  //   {{de Das 2. Bit des ersten zu addierenden Wertes.}}
  //   A_3: The 3. bit of the first value to add.
  //   {{de Das 3. Bit des ersten zu addierenden 
  //   Wertes.}}
  //   S_1: The 1. bit of the sum.
  //   {{de Das 1. Bit der Summe.}}
  //   S_2: The 2. bit of the sum.
  //   {{de Das 2. Bit der Summe.}}
  //   B_0: The 0. bit of the second value to add.
  //   {{de Das 0. Bit des zweiten zu addierenden Wertes.}}
  //   B_1: The 1. bit of the second value to add.
  //   {{de Das 1. Bit des zweiten zu addierenden Wertes.}}
  //   B_2: The 2. bit of the second value to add.
  //   {{de Das 2. Bit des zweiten zu addierenden Wertes.}}
  //   B_3: The 3. bit of the second value to add.
  //   {{de Das 3. Bit des zweiten zu addierenden Wertes.}}
  //   S_3: The 3. bit of the sum.
  //   {{de Das 3. Bit der Summe.}}
  //   C_i: The carry bit, which is passed to the adiator for the 
  //   next most significant bits.
  //   {{de Das Übertragsbit, welches an den Adiierer für die
  //   nächst höherwertigen Bits weitergegeben wird.}}
endmodule

/* Test case:
# A complete test of all 512 possible additions
#
# All created test vectors are shown in the result table.

C_{i-1}  A_3 A_2 A_1 A_0  B_3 B_2 B_1 B_0  C_i S_3 S_2 S_1 S_0

loop(a,16)
 loop(b,16)
  0    bits(4,a)        bits(4,b)        bits(5,a+b)
  1    bits(4,a)        bits(4,b)        bits(5,a+b+1)
 end loop
end loop
*/
