// Digital circuit FullSubNaive.dig as structural Verilog
module FullSubNaive (
  input  A,
  input  B,
  input  BO_i_1,
  output S,
  output BO_i
);

  wire and_1_out, and_2_out, and_3_out, and_4_out, and_5_out, and_6_out, and_7_out, not_1_out, not_2_out,
       not_3_out;

  not not_1 (not_1_out, A);
  not not_2 (not_2_out, B);
  not not_3 (not_3_out, BO_i_1);
  and and_1 (and_1_out, not_1_out, not_2_out, BO_i_1);
  and and_2 (and_2_out, not_1_out, B, not_3_out);
  and and_3 (and_3_out, A, not_2_out, not_3_out);
  and and_4 (and_4_out, A, B, BO_i_1);
  and and_5 (and_5_out, not_1_out, BO_i_1);
  and and_6 (and_6_out, not_1_out, B);
  and and_7 (and_7_out, B, BO_i_1);
  or or_1 (S, and_1_out, and_2_out, and_3_out, and_4_out);
  or or_2 (BO_i, and_5_out, and_6_out, and_7_out);
endmodule
