// Digital circuit FullSubRC.dig as structural Verilog
module FullSubRC (
  input  A_0,
  input  B_0,
  input  A_1,
  input  B_1,
  input  A_2,
  input  B_2,
  input  A_3,
  input  B_3,
  input  C__1,
  output S_0,
  output S_1,
  output S_2,
  output S_3,
  output C_3
);

  wire fullsub_1_p3, fullsub_2_p3, fullsub_3_p3;

  // FullSub fullsub_1: pin names not known; wires that end beside it: A_3, B_3, fullsub_1_p3, C_3, S_3
  // FullSub fullsub_2: pin names not known; wires that end beside it: A_2, B_2, fullsub_2_p3, fullsub_1_p3, S_2
  // FullSub fullsub_3: pin names not known; wires that end beside it: A_1, B_1, fullsub_3_p3, fullsub_2_p3, S_1
  // FullSub fullsub_4: pin names not known; wires that end beside it: A_0, B_0, C__1, fullsub_3_p3, S_0
endmodule
