// Digital circuit MultiplyTest.dig as structural Verilog
// Einfache Schaltung um den Multiplikator
// auszuprobieren.
module MultiplyTest (
  input  [3:0] P,
  input  [3:0] Q
);

  wire [3:0] multiply_1_p9, multiply_1_p13;

  Seven_Seg_Hex seven_seg_hex_1 (.d(Q), .dp(1'b0));
  Seven_Seg_Hex seven_seg_hex_2 (.d(P), .dp(1'b0));
  // Multiply multiply_1: pin names not known; wires that end beside it: P[0], P[1], P[2], P[3], Q[0], Q[1], Q[2], Q[3], multiply_1_p9[0], multiply_1_p9[1], multiply_1_p9[2], multiply_1_p9[3], multiply_1_p13[0], multiply_1_p13[1], multiply_1_p13[2], multiply_1_p13[3]
  Seven_Seg_Hex seven_seg_hex_3 (.d(multiply_1_p13), .dp(1'b0));
  Seven_Seg_Hex seven_seg_hex_4 (.d(multiply_1_p9), .dp(1'b0));

  // Notes on the sheet:
  //   P: Erste zu multiplizierende 4-Bit Zahl.
  //   Q: Zweite zu multiplizierende 4-Bit Zahl.
  //   *
  //   =
endmodule
