// Digital circuit barrelShifter2.dig as structural Verilog
module barrelShifter2 (
  input  [1:0] D,
  input  [1:0] sh
);


  // Notes on the sheet:
  //   A BarrelShifter implemented using component creation.
  //   {{de Ein BarrelShifter implementiert durch Bauteilerzeugung.}}
endmodule

/* Code that sets the parameters or builds the circuit:
sh:=bitsNeededFor(args.dataBits)-1;

circuit:="";
if (args.direction="right") {
      circuit="shift-fixed-right-inc.dig";
} else {
      if (args.direction="arith") {
          circuit="shift-fixed-arith-right-inc.dig";
      } else {
          if (args.direction="left") {
              circuit="shift-fixed-left-inc.dig";
          } else {
              panic("only \"left\", \"right\" or \"arith\" is allowed as direction, not \""+args.direction+"\"!");
          }
      }
}


for (i:=0;i<sh;i++) {
    x:= i*5+2;
    s:=addComponent(circuit,x,0);
    s.shift:=1<<i;

    addWire(x+3,1,x+5,0);

    addWire(0,i+5,x-1,i+5);
    addWire(x-1,i+5,x-1,2);
    addWire(x-1,2,x,2);
}

o:=addComponent("Out",sh*5+2,0);
o.Bits=args.dataBits;
o.Label="Out";
*/

/* Code that sets the parameters or builds the circuit:
dataBits:=16;
direction:="left";
*/
