// Digital circuit shift-inc.dig as structural Verilog
module shift_inc (
  input  [15:0] D_in,
  input  [3:0] sh,
  output [15:0] D
);

  wire shift_fixed_left_inc_1_p3;

  // shift_fixed_left_inc #(.generic("dataBits:=16; shift:=8; if (isPresent(args)) { dataBits = args.dataBits; shift = 1<<(args.shiftBits-1); setCircuit(args.circuit); }")) shift_fixed_left_inc_1: pin names not known; wires that end beside it: D_in, sh[3], shift_fixed_left_inc_1_p3
  // shift_inc #(.generic("dataBits:=16; shiftBits:=3; circuit:=\"shift-fixed-left-inc.dig\"; if (isPresent(args)) { dataBits = args.dataBits; if (args.shiftBits=2) { export shift := 1; setCircuit(args.circuit); } else { shiftBits = args.shiftBits-1; circuit=args.circuit; } }")) shift_inc_1: pin names not known; wires that end beside it: shift_fixed_left_inc_1_p3, sh[2:0], D
endmodule
