// Digital circuit TinyFPGA_BX_SOS.dig as structural Verilog
module TinyFPGA_BX_SOS (
  input  CLK,
  output LED,
  output USBPU
);

  wire [4:0] counter_1_out;

  Counter #(.Bits(5)) counter_1 (.en(1'b1), .C(CLK), .clr(1'b0), .out(counter_1_out));  // open: ovf
  ROM #(.AddrBits(5)) SOS (.A(counter_1_out), .sel(1'b1), .D(LED));

  assign USBPU = 1'b0;

  // Notes on the sheet:
  //   CLK: Hz: 5
  //   contents of SOS (hex, n*v repeats v):
  //   0,1,0,1,0,1,0,1,1,1,0,1,1,1,0,1,1,1,0,1,0,1,0,1
endmodule
