// Digital circuit 7483Real.dig as structural Verilog
// 4-bit binary full adder, real gates
module _7483Real (
  input  C0,
  input  B1,
  input  B2,
  input  B3,
  input  B4,
  input  A1,
  input  A2,
  input  A3,
  input  A4,
  input  VCC,
  input  GND,
  output S1,
  output S2,
  output S3,
  output S4,
  output C4
);

  wire and_1_out, and_2_out, and_3_out, and_4_out, and_5_out, and_6_out, and_7_out, and_8_out, and_9_out,
       and_10_out, and_11_out, and_12_out, and_13_out, and_14_out, or_1_out, or_2_out, or_3_out, or_4_out,
       or_5_out, or_6_out, or_8_out, xor_1_out, xor_2_out, xor_3_out, xor_4_out;

  PowerSupply powersupply_1 (.VDD(VCC), .GND(GND));
  or or_1 (or_1_out, B4, A4);
  and and_1 (and_1_out, B4, A4);
  or or_2 (or_2_out, B3, A3);
  and and_2 (and_2_out, B3, A3);
  or or_3 (or_3_out, B2, A2);
  and and_3 (and_3_out, B2, A2);
  or or_4 (or_4_out, B1, A1);
  and and_4 (and_4_out, B1, A1);
  and and_5 (and_5_out, C0, or_4_out, or_3_out, or_2_out, or_1_out);
  and and_6 (and_6_out, and_4_out, or_1_out, or_2_out, or_3_out);
  and and_7 (and_7_out, and_3_out, or_2_out, or_1_out);
  and and_8 (and_8_out, or_1_out, and_2_out);
  xor xor_1 (xor_1_out, or_1_out, and_1_out);
  and and_9 (and_9_out, C0, or_4_out, or_3_out, or_2_out);
  and and_10 (and_10_out, or_3_out, or_2_out, and_4_out);
  and and_11 (and_11_out, or_2_out, and_3_out);
  xor xor_2 (xor_2_out, or_2_out, and_2_out);
  and and_12 (and_12_out, C0, or_4_out, or_3_out);
  and and_13 (and_13_out, or_3_out, and_4_out);
  xor xor_3 (xor_3_out, or_3_out, and_3_out);
  and and_14 (and_14_out, or_4_out, C0);
  xor xor_4 (xor_4_out, or_4_out, and_4_out);
  or or_5 (or_5_out, and_12_out, and_13_out, and_3_out);
  or or_6 (or_6_out, and_14_out, and_4_out);
  or or_7 (C4, and_5_out, and_6_out, and_7_out, and_8_out, and_1_out);
  or or_8 (or_8_out, and_9_out, and_10_out, and_11_out, and_2_out);
  xor xor_5 (S4, xor_1_out, or_8_out);
  xor xor_6 (S3, xor_2_out, or_5_out);
  xor xor_7 (S2, xor_3_out, or_6_out);
  xor xor_8 (S1, xor_4_out, C0);

  // Notes on the sheet:
  //   C0: pin 13
  //   B1: pin 11
  //   B2: pin 7
  //   S1: pin 9
  //   B3: pin 4
  //   B4: pin 16
  //   S2: pin 6
  //   S3: pin 2
  //   A1: pin 10
  //   A2: pin 8
  //   A3: pin 3
  //   A4: pin 1
  //   S4: pin 15
  //   C4: pin 14
  //   VCC: pin 5, default 1
  //   GND: pin 12
endmodule

/* Test case:
# A complete test of all 512 possible additions
#

C0   A4 A3 A2 A1   B4 B3 B2 B1  C4 S4 S3 S2 S1
loop(A,16)
  loop(B,16)
0    bits(4,A)     bits(4,B)    bits(5,A+B)
1    bits(4,A)     bits(4,B)    bits(5,A+B+1)
  end loop
end loop
*/
