// Digital circuit 7485.dig as structural Verilog
// 4-bit comparator
module _7485 (
  input  P_0,
  input  P_1,
  input  P_2,
  input  P_3,
  input  P_lt_Q_i,
  input  P_eq_Q_i,
  input  P_gt_Q_i,
  input  Q_0,
  input  Q_1,
  input  Q_2,
  input  Q_3,
  input  VCC,
  input  GND,
  output P_lt_Q,
  output P_eq_Q,
  output P_gt_Q
);

  wire comparator_1_eq, comparator_1_gt, comparator_1_lt;

  PowerSupply powersupply_1 (.VDD(VCC), .GND(GND));
  Comparator #(.Bits(4)) comparator_1 (
    .a({P_3, P_2, P_1, P_0}), .b({Q_3, Q_2, Q_1, Q_0}), .gt(comparator_1_gt), .eq(comparator_1_eq),
    .lt(comparator_1_lt));
  Multiplexer multiplexer_1 (.sel(comparator_1_eq), .in_0(comparator_1_gt), .in_1(P_gt_Q_i), .out(P_gt_Q));
  Multiplexer multiplexer_2 (.sel(comparator_1_eq), .in_0(comparator_1_eq), .in_1(P_eq_Q_i), .out(P_eq_Q));
  Multiplexer multiplexer_3 (.sel(comparator_1_eq), .in_0(comparator_1_lt), .in_1(P_lt_Q_i), .out(P_lt_Q));

  // Notes on the sheet:
  //   P_0: pin 10
  //   P_1: pin 12
  //   P_2: pin 13
  //   P_3: pin 15
  //   P_lt_Q_i: pin 2
  //   P_eq_Q_i: pin 3
  //   P_gt_Q_i: pin 4
  //   Q_0: pin 9
  //   Q_1: pin 11
  //   Q_2: pin 14
  //   Q_3: pin 1
  //   P_lt_Q: pin 7
  //   P_eq_Q: pin 6
  //   P_gt_Q: pin 5
  //   VCC: pin 16, default 1
  //   GND: pin 8
endmodule

/* Test case:
   P<Q_i P=Q_i P>Q_i  P_3 P_2 P_1 P_0   Q_3 Q_2 Q_1 Q_0  P<Q   P=Q   P>Q
loop(P,16)
  loop(Q,16)
    0    1     0      bits(4,P)         bits(4,Q)        (P<Q) (P=Q) (P>Q)
  end loop
end loop

loop (i,16)
  loop (n,8)
    bits(3,n)         bits(4,i)         bits(4,i)        bits(3,n)
  end loop
end loop
*/
