// Digital circuit 74238.dig as structural Verilog
// 3-line to 8-line decoder/demultiplexer
module _74238 (
  input  A,
  input  C,
  input  B,
  input  G,
  input  nGB,
  input  nGA,
  input  VCC,
  input  GND,
  output Y0,
  output Y1,
  output Y2,
  output Y3,
  output Y4,
  output Y5,
  output Y6,
  output Y7
);

  wire and_1_out, not_1_out, not_2_out;

  PowerSupply powersupply_1 (.VDD(VCC), .GND(GND));
  not not_1 (not_1_out, nGB);
  not not_2 (not_2_out, nGA);
  and and_1 (and_1_out, G, not_1_out, not_2_out);
  Demultiplexer #(.Selector_Bits(3)) demultiplexer_1 (
    .sel({C, B, A}), .in(and_1_out), .out_0(Y0), .out_1(Y1), .out_2(Y2), .out_3(Y3), .out_4(Y4), .out_5(Y5),
    .out_6(Y6), .out_7(Y7));

  // Notes on the sheet:
  //   A: pin 1
  //   C: pin 3
  //   B: pin 2
  //   G: pin 6
  //   nGB: pin 5
  //   nGA: pin 4
  //   Y0: pin 15
  //   Y1: pin 14
  //   Y2: pin 13
  //   Y3: pin 12
  //   Y4: pin 11
  //   Y5: pin 10
  //   Y6: pin 9
  //   Y7: pin 7
  //   VCC: pin 16, default 1
  //   GND: pin 8
endmodule

/* Test case:
~GA ~GB G A B C Y0 Y1 Y2 Y3 Y4 Y5 Y6 Y7
1 X X X X X 0 0 0 0 0 0 0 0
X 1 X X X X 0 0 0 0 0 0 0 0
X X 0 X X X 0 0 0 0 0 0 0 0
0 0 1 0 0 0 1 0 0 0 0 0 0 0
0 0 1 1 0 0 0 1 0 0 0 0 0 0
0 0 1 0 1 0 0 0 1 0 0 0 0 0
0 0 1 1 1 0 0 0 0 1 0 0 0 0
0 0 1 0 0 1 0 0 0 0 1 0 0 0
0 0 1 1 0 1 0 0 0 0 0 1 0 0
0 0 1 0 1 1 0 0 0 0 0 0 1 0
0 0 1 1 1 1 0 0 0 0 0 0 0 1
*/
