// Digital circuit 74247.dig as structural Verilog
// BCD to 7-segment decoder, active low, tails on 6 and 9
module _74247 (
  input  A,
  input  B,
  input  C,
  input  D,
  input  nRBI,
  input  nLT,
  input  VCC,
  input  GND,
  output nRBO,
  output a_2,
  output b_2,
  output c_2,
  output d_2,
  output e,
  output f,
  output g
);

  wire and_1_out, and_2_out, and_3_out, and_4_out, and_5_out, and_6_out, and_7_out, and_8_out, and_9_out,
       and_10_out, and_11_out, and_12_out, and_13_out, and_14_out, and_15_out, and_16_out, and_17_out,
       and_18_out, delay_1_out, delay_2_out, nand_1_out, nand_2_out, nand_3_out, nand_4_out, nand_5_out,
       nand_6_out, nand_7_out, nor_1_out, nor_2_out, nor_3_out, nor_4_out, nor_5_out, nor_6_out, nor_7_out,
       not_1_out, not_2_out;

  PowerSupply powersupply_1 (.VDD(VCC), .GND(GND));
  nand nand_1 (nand_1_out, A, delay_1_out);
  nand nand_2 (nand_2_out, B, delay_1_out);
  nand nand_3 (nand_3_out, C, delay_1_out);
  not not_1 (not_1_out, D);
  and and_1 (and_1_out, delay_1_out, not_2_out, not_1_out, nand_3_out, nand_2_out, nand_1_out);
  Delay delay_1 (.in(nLT), .out(delay_1_out));
  not not_2 (not_2_out, nRBI);
  PullUp pullup_1 (.out(nRBO));
  NFET nfet_1 (.G(and_1_out), .D(nRBO), .S(1'b0));
  nand nand_4 (nand_4_out, nand_1_out, nRBO);
  nand nand_5 (nand_5_out, nand_2_out, nRBO);
  nand nand_6 (nand_6_out, nand_3_out, nRBO);
  nand nand_7 (nand_7_out, not_1_out, nRBO);
  and and_2 (and_2_out, nand_5_out, nand_7_out);
  and and_3 (and_3_out, nand_1_out, nand_2_out, nand_6_out);
  and and_4 (and_4_out, nand_4_out, nand_2_out, nand_3_out, not_1_out);
  and and_5 (and_5_out, nand_5_out, nand_7_out);
  and and_6 (and_6_out, nand_4_out, nand_2_out, nand_6_out);
  and and_7 (and_7_out, nand_1_out, nand_5_out, nand_6_out);
  and and_8 (and_8_out, nand_6_out, nand_7_out);
  and and_9 (and_9_out, nand_1_out, nand_5_out, nand_3_out);
  and and_10 (and_10_out, nand_4_out, nand_2_out, nand_3_out, not_1_out);
  and and_11 (and_11_out, nand_1_out, nand_2_out, nand_6_out);
  and and_12 (and_12_out, nand_4_out, nand_5_out, nand_6_out);
  Delay delay_2 (.in(nand_4_out), .out(delay_2_out));
  and and_13 (and_13_out, nand_2_out, nand_6_out);
  and and_14 (and_14_out, nand_4_out, nand_5_out);
  and and_15 (and_15_out, nand_5_out, nand_3_out);
  and and_16 (and_16_out, nand_4_out, nand_3_out, not_1_out);
  and and_17 (and_17_out, nand_4_out, nand_5_out, nand_6_out);
  and and_18 (and_18_out, nand_2_out, nand_3_out, not_1_out, delay_1_out);
  nor nor_1 (nor_1_out, and_2_out, and_3_out, and_4_out);
  nor nor_2 (nor_2_out, and_5_out, and_6_out, and_7_out);
  nor nor_3 (nor_3_out, and_8_out, and_9_out);
  nor nor_4 (nor_4_out, and_10_out, and_11_out, and_12_out);
  nor nor_5 (nor_5_out, delay_2_out, and_13_out);
  nor nor_6 (nor_6_out, and_14_out, and_15_out, and_16_out);
  nor nor_7 (nor_7_out, and_17_out, and_18_out);
  not not_3 (a_2, nor_1_out);
  not not_4 (b_2, nor_2_out);
  not not_5 (c_2, nor_3_out);
  not not_6 (d_2, nor_4_out);
  not not_7 (e, nor_5_out);
  not not_8 (f, nor_6_out);
  not not_9 (g, nor_7_out);

  // Notes on the sheet:
  //   A: Bit 0, pin 7
  //   B: Bit 1, pin 1
  //   C: Bit 2, pin 2
  //   D: Bit 3, pin 6
  //   nRBO: ripple blanking output (LOW active), pin 4
  //   nRBI: ripple blanking input (LOW active), pin 5
  //   a_2: pin 13
  //   b_2: pin 12
  //   c_2: pin 11
  //   d_2: pin 10
  //   e: pin 9
  //   f: pin 15
  //   g: pin 14
  //   nLT: lamp test, pin 3
  //   VCC: pin 16, default 1
  //   GND: pin 8
endmodule

/* Test case:
~LT ~RBI D C B A ~RBO  a b c d e f g 
 1    1  0 0 0 0   1   0 0 0 0 0 0 1

 1    x  0 0 0 1   1   1 0 0 1 1 1 1
 1    x  0 0 1 0   1   0 0 1 0 0 1 0
 1    x  0 0 1 1   1   0 0 0 0 1 1 0
 1    x  0 1 0 0   1   1 0 0 1 1 0 0
 1    x  0 1 0 1   1   0 1 0 0 1 0 0 
 1    x  0 1 1 0   1   0 1 0 0 0 0 0 
 1    x  0 1 1 1   1   0 0 0 1 1 1 1
 1    x  1 0 0 0   1   0 0 0 0 0 0 0
 1    x  1 0 0 1   1   0 0 0 0 1 0 0
 1    x  1 0 1 0   1   1 1 1 0 0 1 0
 1    x  1 0 1 1   1   1 1 0 0 1 1 0
 1    x  1 1 0 0   1   1 0 1 1 1 0 0
 1    x  1 1 0 1   1   0 1 1 0 1 0 0
 1    x  1 1 1 0   1   1 1 1 0 0 0 0
 1    x  1 1 1 1   1   1 1 1 1 1 1 1

#x    x  x x x x   0   1 1 1 1 1 1 1
 1    0  0 0 0 0   0   1 1 1 1 1 1 1
 0    x  x x x x   1   0 0 0 0 0 0 0
*/
