// Digital circuit 7489.dig as structural Verilog
// 64-bit RAM
module _7489 (
  input  A0,
  input  A1,
  input  A2,
  input  A3,
  input  D1,
  input  D2,
  input  D3,
  input  D4,
  input  nWE,
  input  nME,
  input  VCC,
  input  GND,
  output S4,
  output S1,
  output S2,
  output S3
);

  wire and_1_out, not_1_out, not_2_out, or_1_out;
  wire [3:0] not_3_out, ramdualport_d;

  not not_1 (not_1_out, nWE);
  not not_2 (not_2_out, nME);
  PowerSupply powersupply_1 (.VDD(VCC), .GND(GND));
  and and_1 (and_1_out, not_1_out, not_2_out);
  or or_1 (or_1_out, not_1_out, not_2_out);
  RAMDualPort #(.AddrBits(4), .Bits(4), .Addr_Bits(4)) ramdualport (
    .A({A3, A2, A1, A0}), .Din({D4, D3, D2, D1}), .str(and_1_out), .C(and_1_out), .ld(or_1_out),
    .D(ramdualport_d));
  assign not_3_out = ~ramdualport_d;  // Not not_3, 4 bits wide
  assign {S4, S3, S2, S1} = or_1_out ? not_3_out : 4'bz;  // Driver driver_1

  // Notes on the sheet:
  //   S4: pin 11
  //   S1: pin 5
  //   S2: pin 7
  //   S3: pin 9
  //   A0: pin 1
  //   A1: pin 15
  //   A2: pin 14
  //   A3: pin 13
  //   D1: pin 4
  //   D2: pin 6
  //   D3: pin 10
  //   D4: pin 12
  //   nWE: pin 3
  //   nME: pin 2
  //   VCC: pin 16, default 1
  //   GND: pin 8
endmodule
