// Digital circuit 74299.dig as structural Verilog
// 8-Input Universal Shift/Storage Register
// with Common Parallel I/O Pins
module _74299 (
  input  DSR,
  input  S0,
  input  S1,
  input  nOE1,
  input  nOE2,
  input  CP,
  input  nMR,
  input  DSL,
  input  VCC,
  input  GND,
  input  I_O0,
  input  I_O1,
  input  I_O2,
  input  I_O3,
  input  I_O4,
  input  I_O5,
  input  I_O6,
  input  I_O7,
  output Q0,
  output Q7
);

  wire and_1_out, d_ff_as_2_q, d_ff_as_3_q, d_ff_as_4_q, d_ff_as_5_q, d_ff_as_6_q, d_ff_as_7_q,
       multiplexer_1_out, multiplexer_2_out, multiplexer_3_out, multiplexer_4_out, multiplexer_5_out,
       multiplexer_6_out, multiplexer_7_out, multiplexer_8_out, nand_1_out, not_1_out, not_2_out, not_3_out;

  not not_1 (not_1_out, nOE1);
  not not_2 (not_2_out, nOE2);
  PowerSupply powersupply_1 (.VDD(VCC), .GND(GND));
  not not_3 (not_3_out, nMR);
  nand nand_1 (nand_1_out, S1, S0);
  and and_1 (and_1_out, nand_1_out, not_1_out, not_2_out);
  Multiplexer #(.Selector_Bits(2)) multiplexer_1 (
    .sel({S1, S0}), .in_0(Q0), .in_1(DSR), .in_2(d_ff_as_2_q), .in_3(I_O0), .out(multiplexer_1_out));
  Multiplexer #(.Selector_Bits(2)) multiplexer_2 (
    .sel({S1, S0}), .in_0(d_ff_as_2_q), .in_1(Q0), .in_2(d_ff_as_3_q), .in_3(I_O1), .out(multiplexer_2_out));
  Multiplexer #(.Selector_Bits(2)) multiplexer_3 (
    .sel({S1, S0}), .in_0(d_ff_as_3_q), .in_1(d_ff_as_2_q), .in_2(d_ff_as_4_q), .in_3(I_O2),
    .out(multiplexer_3_out));
  Multiplexer #(.Selector_Bits(2)) multiplexer_4 (
    .sel({S1, S0}), .in_0(d_ff_as_4_q), .in_1(d_ff_as_3_q), .in_2(d_ff_as_5_q), .in_3(I_O3),
    .out(multiplexer_4_out));
  Multiplexer #(.Selector_Bits(2)) multiplexer_5 (
    .sel({S1, S0}), .in_0(d_ff_as_5_q), .in_1(d_ff_as_4_q), .in_2(d_ff_as_6_q), .in_3(I_O4),
    .out(multiplexer_5_out));
  Multiplexer #(.Selector_Bits(2)) multiplexer_6 (
    .sel({S1, S0}), .in_0(d_ff_as_6_q), .in_1(d_ff_as_5_q), .in_2(d_ff_as_7_q), .in_3(I_O5),
    .out(multiplexer_6_out));
  Multiplexer #(.Selector_Bits(2)) multiplexer_7 (
    .sel({S1, S0}), .in_0(d_ff_as_7_q), .in_1(d_ff_as_6_q), .in_2(Q7), .in_3(I_O6), .out(multiplexer_7_out));
  Multiplexer #(.Selector_Bits(2)) multiplexer_8 (
    .sel({S1, S0}), .in_0(Q7), .in_1(d_ff_as_7_q), .in_2(DSL), .in_3(I_O7), .out(multiplexer_8_out));
  D_FF_AS d_ff_as_1 (.Set(1'b0), .D(multiplexer_1_out), .C(CP), .Clr(not_3_out), .Q(Q0));  // open: nQ
  D_FF_AS d_ff_as_2 (.Set(1'b0), .D(multiplexer_2_out), .C(CP), .Clr(not_3_out), .Q(d_ff_as_2_q));  // open: nQ
  D_FF_AS d_ff_as_3 (.Set(1'b0), .D(multiplexer_3_out), .C(CP), .Clr(not_3_out), .Q(d_ff_as_3_q));  // open: nQ
  D_FF_AS d_ff_as_4 (.Set(1'b0), .D(multiplexer_4_out), .C(CP), .Clr(not_3_out), .Q(d_ff_as_4_q));  // open: nQ
  D_FF_AS d_ff_as_5 (.Set(1'b0), .D(multiplexer_5_out), .C(CP), .Clr(not_3_out), .Q(d_ff_as_5_q));  // open: nQ
  D_FF_AS d_ff_as_6 (.Set(1'b0), .D(multiplexer_6_out), .C(CP), .Clr(not_3_out), .Q(d_ff_as_6_q));  // open: nQ
  D_FF_AS d_ff_as_7 (.Set(1'b0), .D(multiplexer_7_out), .C(CP), .Clr(not_3_out), .Q(d_ff_as_7_q));  // open: nQ
  D_FF_AS d_ff_as_8 (.Set(1'b0), .D(multiplexer_8_out), .C(CP), .Clr(not_3_out), .Q(Q7));  // open: nQ
  assign I_O0 = and_1_out ? Q0 : 1'bz;  // Driver driver_1
  assign I_O1 = and_1_out ? d_ff_as_2_q : 1'bz;  // Driver driver_2
  assign I_O2 = and_1_out ? d_ff_as_3_q : 1'bz;  // Driver driver_3
  assign I_O3 = and_1_out ? d_ff_as_4_q : 1'bz;  // Driver driver_4
  assign I_O4 = and_1_out ? d_ff_as_5_q : 1'bz;  // Driver driver_5
  assign I_O5 = and_1_out ? d_ff_as_6_q : 1'bz;  // Driver driver_6
  assign I_O6 = and_1_out ? d_ff_as_7_q : 1'bz;  // Driver driver_7
  assign I_O7 = and_1_out ? Q7 : 1'bz;  // Driver driver_8

  // Notes on the sheet:
  //   DSR: pin 11
  //   S0: pin 1
  //   S1: pin 19
  //   nOE1: pin 2, default 1
  //   nOE2: pin 3, default 1
  //   CP: pin 12
  //   Q0: pin 8
  //   nMR: pin 9, default 1
  //   Q7: pin 17
  //   DSL: pin 18
  //   VCC: pin 20, default 1
  //   GND: pin 10
  //   I_O0: pin 7
  //   I_O1: pin 13
  //   I_O2: pin 6
  //   I_O3: pin 14
  //   I_O4: pin 5
  //   I_O5: pin 15
  //   I_O6: pin 4
  //   I_O7: pin 16
endmodule

/* Test case shift:
CP S1 S0 ~OE1 ~OE2 DSL I/O7 I/O6 I/O5 I/O4 I/O3 I/O2 I/O1 I/O0 DSR I/O7_out I/O6_out I/O5_out I/O4_out I/O3_out I/O2_out I/O1_out I/O0_out
# left
c  1  1    1    1   0   0    0    0    0    0    0    0    0    0   0 0 0 0 0 0 0 0
c  1  0    1    1   1   0    0    0    0    0    0    0    0    0   0 0 0 0 0 0 0 0
0  0  0    0    0   1   z    z    z    z    z    z    z    z    0   1 0 0 0 0 0 0 0
c  1  0    0    0   0   z    z    z    z    z    z    z    z    0   0 1 0 0 0 0 0 0
c  1  0    0    0   0   z    z    z    z    z    z    z    z    0   0 0 1 0 0 0 0 0
c  1  0    0    0   0   z    z    z    z    z    z    z    z    0   0 0 0 1 0 0 0 0
c  1  0    0    0   0   z    z    z    z    z    z    z    z    0   0 0 0 0 1 0 0 0
c  1  0    0    0   0   z    z    z    z    z    z    z    z    0   0 0 0 0 0 1 0 0
c  1  0    0    0   0   z    z    z    z    z    z    z    z    0   0 0 0 0 0 0 1 0
c  1  0    0    0   0   z    z    z    z    z    z    z    z    0   0 0 0 0 0 0 0 1
c  1  0    0    0   0   z    z    z    z    z    z    z    z    0   0 0 0 0 0 0 0 0

# right
c  1  1    1    1   0   0    0    0    0    0    0    0    0    0   0 0 0 0 0 0 0 0
c  0  1    1    1   0   0    0    0    0    0    0    0    0    1   0 0 0 0 0 0 0 0
0  0  0    0    0   0   z    z    z    z    z    z    z    z    1   0 0 0 0 0 0 0 1
c  0  1    0    0   0   z    z    z    z    z    z    z    z    0   0 0 0 0 0 0 1 0
c  0  1    0    0   0   z    z    z    z    z    z    z    z    0   0 0 0 0 0 1 0 0
c  0  1    0    0   0   z    z    z    z    z    z    z    z    0   0 0 0 0 1 0 0 0
c  0  1    0    0   0   z    z    z    z    z    z    z    z    0   0 0 0 1 0 0 0 0
c  0  1    0    0   0   z    z    z    z    z    z    z    z    0   0 0 1 0 0 0 0 0
c  0  1    0    0   0   z    z    z    z    z    z    z    z    0   0 1 0 0 0 0 0 0
c  0  1    0    0   0   z    z    z    z    z    z    z    z    0   1 0 0 0 0 0 0 0
c  0  1    0    0   0   z    z    z    z    z    z    z    z    0   0 0 0 0 0 0 0 0
*/

/* Test case load:
CP S1 S0 ~MR ~OE1 ~OE2 DSL I/O7 I/O6 I/O5 I/O4 I/O3 I/O2 I/O1 I/O0 DSR I/O7_out I/O6_out I/O5_out I/O4_out I/O3_out I/O2_out I/O1_out I/O0_out
# load
c  1  1   1    1    1   0   1    1    1    1    1    1    1    1    0   1 1 1 1 1 1 1 1
0  0  0   1    1    1   0   z    z    z    z    z    z    z    z    0   z z z z z z z z
0  0  0   1    0    0   0   z    z    z    z    z    z    z    z    0   1 1 1 1 1 1 1 1

c  1  1   1    1    1   0   0    1    0    1    0    1    0    1    0   0 1 0 1 0 1 0 1
0  0  0   1    1    1   0   z    z    z    z    z    z    z    z    0   z z z z z z z z
0  0  0   1    0    0   0   z    z    z    z    z    z    z    z    0   0 1 0 1 0 1 0 1

c  1  1   1    1    1   0   1    0    1    0    1    0    1    0    0   1 0 1 0 1 0 1 0
0  0  0   1    1    1   0   z    z    z    z    z    z    z    z    0   z z z z z z z z
0  0  0   1    0    0   0   z    z    z    z    z    z    z    z    0   1 0 1 0 1 0 1 0

#clear
c  1  1   1    1    1   0   1    1    1    1    1    1    1    1    0   1 1 1 1 1 1 1 1
0  0  0   1    0    0   0   z    z    z    z    z    z    z    z    0   1 1 1 1 1 1 1 1
0  0  0   0    0    0   0   z    z    z    z    z    z    z    z    0   0 0 0 0 0 0 0 0
*/
