// Digital circuit GAL2v3.dig as structural Verilog
module GAL2v3 (
  input  A,
  input  B,
  input  C,
  output Y_0,
  output Y_1,
  output Y_2
);

  wire dideblabla_1_p1, dideblabla_1_p3, dideblabla_3_p2, dideblabla_5_p2, dideblabla_7_p2, dideblabla_9_p2,
       dideblabla_11_p2, dideblabla_13_p2, dideblabla_15_p2, dideblabla_17_p2, dideblabla_19_p2,
       dideblabla_21_p2, dideblabla_23_p2, dideblabla_25_p2, dideblabla_27_p2, MC0_q, MC1_q, MC2_q,
       not_1_out, not_2_out, not_3_out, not_4_out, not_5_out, or_1_out, or_2_out, or_3_out, pullup_16_out,
       pullup_17_out, pullup_18_out;

  not not_1 (not_1_out, A);
  // Dideblabla #(.Blown("true")) dideblabla_1: pin names not known; wires that end beside it: dideblabla_1_p1, A, dideblabla_1_p3
  // Dideblabla #(.Blown("true")) dideblabla_2: pin names not known; wires that end beside it: dideblabla_1_p1, not_1_out, dideblabla_1_p3
  // Dideblabla dideblabla_3: pin names not known; wires that end beside it: A, dideblabla_3_p2
  // Dideblabla dideblabla_4: pin names not known; wires that end beside it: not_1_out, dideblabla_3_p2
  // Dideblabla dideblabla_5: pin names not known; wires that end beside it: A, dideblabla_5_p2
  // Dideblabla dideblabla_6: pin names not known; wires that end beside it: not_1_out, dideblabla_5_p2
  // Dideblabla dideblabla_7: pin names not known; wires that end beside it: A, dideblabla_7_p2
  // Dideblabla dideblabla_8: pin names not known; wires that end beside it: not_1_out, dideblabla_7_p2
  // Dideblabla dideblabla_9: pin names not known; wires that end beside it: A, dideblabla_9_p2
  // Dideblabla dideblabla_10: pin names not known; wires that end beside it: not_1_out, dideblabla_9_p2
  // Dideblabla #(.Blown("true")) dideblabla_11: pin names not known; wires that end beside it: A, dideblabla_11_p2
  // Dideblabla #(.Blown("true")) dideblabla_12: pin names not known; wires that end beside it: not_1_out, dideblabla_11_p2
  // Dideblabla #(.Blown("true")) dideblabla_13: pin names not known; wires that end beside it: A, dideblabla_13_p2
  // Dideblabla #(.Blown("true")) dideblabla_14: pin names not known; wires that end beside it: not_1_out, dideblabla_13_p2
  // Dideblabla dideblabla_15: pin names not known; wires that end beside it: A, dideblabla_15_p2
  // Dideblabla dideblabla_16: pin names not known; wires that end beside it: not_1_out, dideblabla_15_p2
  // Dideblabla dideblabla_17: pin names not known; wires that end beside it: A, dideblabla_17_p2
  // Dideblabla dideblabla_18: pin names not known; wires that end beside it: not_1_out, dideblabla_17_p2
  // Dideblabla dideblabla_19: pin names not known; wires that end beside it: A, dideblabla_19_p2
  // Dideblabla dideblabla_20: pin names not known; wires that end beside it: not_1_out, dideblabla_19_p2
  // Dideblabla #(.Blown("true")) dideblabla_21: pin names not known; wires that end beside it: A, dideblabla_21_p2
  // Dideblabla #(.Blown("true")) dideblabla_22: pin names not known; wires that end beside it: not_1_out, dideblabla_21_p2
  // Dideblabla #(.Blown("true")) dideblabla_23: pin names not known; wires that end beside it: A, dideblabla_23_p2
  // Dideblabla #(.Blown("true")) dideblabla_24: pin names not known; wires that end beside it: not_1_out, dideblabla_23_p2
  // Dideblabla #(.Blown("true")) dideblabla_25: pin names not known; wires that end beside it: A, dideblabla_25_p2
  // Dideblabla #(.Blown("true")) dideblabla_26: pin names not known; wires that end beside it: not_1_out, dideblabla_25_p2
  // Dideblabla dideblabla_27: pin names not known; wires that end beside it: A, dideblabla_27_p2
  // Dideblabla dideblabla_28: pin names not known; wires that end beside it: not_1_out, dideblabla_27_p2
  // Dideblabla dideblabla_29: pin names not known; wires that end beside it: A
  // Dideblabla dideblabla_30: pin names not known; wires that end beside it: not_1_out
  not not_2 (not_2_out, B);
  // Dideblabla #(.Blown("true")) dideblabla_31: pin names not known; wires that end beside it: dideblabla_1_p1, B, dideblabla_1_p3
  // Dideblabla #(.Blown("true")) dideblabla_32: pin names not known; wires that end beside it: dideblabla_1_p1, not_2_out, dideblabla_1_p3
  // Dideblabla dideblabla_33: pin names not known; wires that end beside it: B, dideblabla_3_p2
  // Dideblabla dideblabla_34: pin names not known; wires that end beside it: not_2_out, dideblabla_3_p2
  // Dideblabla dideblabla_35: pin names not known; wires that end beside it: B, dideblabla_5_p2
  // Dideblabla dideblabla_36: pin names not known; wires that end beside it: not_2_out, dideblabla_5_p2
  // Dideblabla dideblabla_37: pin names not known; wires that end beside it: B, dideblabla_7_p2
  // Dideblabla dideblabla_38: pin names not known; wires that end beside it: not_2_out, dideblabla_7_p2
  // Dideblabla dideblabla_39: pin names not known; wires that end beside it: B, dideblabla_9_p2
  // Dideblabla dideblabla_40: pin names not known; wires that end beside it: not_2_out, dideblabla_9_p2
  // Dideblabla #(.Blown("true")) dideblabla_41: pin names not known; wires that end beside it: B, dideblabla_11_p2
  // Dideblabla #(.Blown("true")) dideblabla_42: pin names not known; wires that end beside it: not_2_out, dideblabla_11_p2
  // Dideblabla #(.Blown("true")) dideblabla_43: pin names not known; wires that end beside it: B, dideblabla_13_p2
  // Dideblabla #(.Blown("true")) dideblabla_44: pin names not known; wires that end beside it: not_2_out, dideblabla_13_p2
  // Dideblabla dideblabla_45: pin names not known; wires that end beside it: B, dideblabla_15_p2
  // Dideblabla dideblabla_46: pin names not known; wires that end beside it: not_2_out, dideblabla_15_p2
  // Dideblabla dideblabla_47: pin names not known; wires that end beside it: B, dideblabla_17_p2
  // Dideblabla dideblabla_48: pin names not known; wires that end beside it: not_2_out, dideblabla_17_p2
  // Dideblabla dideblabla_49: pin names not known; wires that end beside it: B, dideblabla_19_p2
  // Dideblabla dideblabla_50: pin names not known; wires that end beside it: not_2_out, dideblabla_19_p2
  // Dideblabla #(.Blown("true")) dideblabla_51: pin names not known; wires that end beside it: B, dideblabla_21_p2
  // Dideblabla #(.Blown("true")) dideblabla_52: pin names not known; wires that end beside it: not_2_out, dideblabla_21_p2
  // Dideblabla #(.Blown("true")) dideblabla_53: pin names not known; wires that end beside it: B, dideblabla_23_p2
  // Dideblabla #(.Blown("true")) dideblabla_54: pin names not known; wires that end beside it: not_2_out, dideblabla_23_p2
  // Dideblabla #(.Blown("true")) dideblabla_55: pin names not known; wires that end beside it: B, dideblabla_25_p2
  // Dideblabla #(.Blown("true")) dideblabla_56: pin names not known; wires that end beside it: not_2_out, dideblabla_25_p2
  // Dideblabla dideblabla_57: pin names not known; wires that end beside it: B, dideblabla_27_p2
  // Dideblabla dideblabla_58: pin names not known; wires that end beside it: not_2_out, dideblabla_27_p2
  // Dideblabla dideblabla_59: pin names not known; wires that end beside it: B
  // Dideblabla dideblabla_60: pin names not known; wires that end beside it: not_2_out
  not not_3 (not_3_out, Y_0);
  // Dideblabla #(.Blown("true")) dideblabla_61: pin names not known; wires that end beside it: dideblabla_1_p1, Y_0, dideblabla_1_p3
  // Dideblabla dideblabla_62: pin names not known; wires that end beside it: dideblabla_1_p1, not_3_out, dideblabla_1_p3
  // Dideblabla dideblabla_63: pin names not known; wires that end beside it: Y_0, dideblabla_3_p2
  // Dideblabla dideblabla_64: pin names not known; wires that end beside it: not_3_out, dideblabla_3_p2
  // Dideblabla dideblabla_65: pin names not known; wires that end beside it: Y_0, dideblabla_5_p2
  // Dideblabla dideblabla_66: pin names not known; wires that end beside it: not_3_out, dideblabla_5_p2
  // Dideblabla dideblabla_67: pin names not known; wires that end beside it: Y_0, dideblabla_7_p2
  // Dideblabla dideblabla_68: pin names not known; wires that end beside it: not_3_out, dideblabla_7_p2
  // Dideblabla dideblabla_69: pin names not known; wires that end beside it: Y_0, dideblabla_9_p2
  // Dideblabla dideblabla_70: pin names not known; wires that end beside it: not_3_out, dideblabla_9_p2
  // Dideblabla dideblabla_71: pin names not known; wires that end beside it: Y_0, dideblabla_11_p2
  // Dideblabla #(.Blown("true")) dideblabla_72: pin names not known; wires that end beside it: not_3_out, dideblabla_11_p2
  // Dideblabla #(.Blown("true")) dideblabla_73: pin names not known; wires that end beside it: Y_0, dideblabla_13_p2
  // Dideblabla dideblabla_74: pin names not known; wires that end beside it: not_3_out, dideblabla_13_p2
  // Dideblabla dideblabla_75: pin names not known; wires that end beside it: Y_0, dideblabla_15_p2
  // Dideblabla dideblabla_76: pin names not known; wires that end beside it: not_3_out, dideblabla_15_p2
  // Dideblabla dideblabla_77: pin names not known; wires that end beside it: Y_0, dideblabla_17_p2
  // Dideblabla dideblabla_78: pin names not known; wires that end beside it: not_3_out, dideblabla_17_p2
  // Dideblabla dideblabla_79: pin names not known; wires that end beside it: Y_0, dideblabla_19_p2
  // Dideblabla dideblabla_80: pin names not known; wires that end beside it: not_3_out, dideblabla_19_p2
  // Dideblabla dideblabla_81: pin names not known; wires that end beside it: Y_0, dideblabla_21_p2
  // Dideblabla #(.Blown("true")) dideblabla_82: pin names not known; wires that end beside it: not_3_out, dideblabla_21_p2
  // Dideblabla #(.Blown("true")) dideblabla_83: pin names not known; wires that end beside it: Y_0, dideblabla_23_p2
  // Dideblabla dideblabla_84: pin names not known; wires that end beside it: not_3_out, dideblabla_23_p2
  // Dideblabla #(.Blown("true")) dideblabla_85: pin names not known; wires that end beside it: Y_0, dideblabla_25_p2
  // Dideblabla #(.Blown("true")) dideblabla_86: pin names not known; wires that end beside it: not_3_out, dideblabla_25_p2
  // Dideblabla dideblabla_87: pin names not known; wires that end beside it: Y_0, dideblabla_27_p2
  // Dideblabla dideblabla_88: pin names not known; wires that end beside it: not_3_out, dideblabla_27_p2
  // Dideblabla dideblabla_89: pin names not known; wires that end beside it: Y_0
  // Dideblabla dideblabla_90: pin names not known; wires that end beside it: not_3_out
  not not_4 (not_4_out, Y_1);
  // Dideblabla #(.Blown("true")) dideblabla_91: pin names not known; wires that end beside it: dideblabla_1_p1, Y_1, dideblabla_1_p3
  // Dideblabla #(.Blown("true")) dideblabla_92: pin names not known; wires that end beside it: dideblabla_1_p1, not_4_out, dideblabla_1_p3
  // Dideblabla dideblabla_93: pin names not known; wires that end beside it: Y_1, dideblabla_3_p2
  // Dideblabla dideblabla_94: pin names not known; wires that end beside it: not_4_out, dideblabla_3_p2
  // Dideblabla dideblabla_95: pin names not known; wires that end beside it: Y_1, dideblabla_5_p2
  // Dideblabla dideblabla_96: pin names not known; wires that end beside it: not_4_out, dideblabla_5_p2
  // Dideblabla dideblabla_97: pin names not known; wires that end beside it: Y_1, dideblabla_7_p2
  // Dideblabla dideblabla_98: pin names not known; wires that end beside it: not_4_out, dideblabla_7_p2
  // Dideblabla dideblabla_99: pin names not known; wires that end beside it: Y_1, dideblabla_9_p2
  // Dideblabla dideblabla_100: pin names not known; wires that end beside it: not_4_out, dideblabla_9_p2
  // Dideblabla #(.Blown("true")) dideblabla_101: pin names not known; wires that end beside it: Y_1, dideblabla_11_p2
  // Dideblabla dideblabla_102: pin names not known; wires that end beside it: not_4_out, dideblabla_11_p2
  // Dideblabla dideblabla_103: pin names not known; wires that end beside it: Y_1, dideblabla_13_p2
  // Dideblabla #(.Blown("true")) dideblabla_104: pin names not known; wires that end beside it: not_4_out, dideblabla_13_p2
  // Dideblabla dideblabla_105: pin names not known; wires that end beside it: Y_1, dideblabla_15_p2
  // Dideblabla dideblabla_106: pin names not known; wires that end beside it: not_4_out, dideblabla_15_p2
  // Dideblabla dideblabla_107: pin names not known; wires that end beside it: Y_1, dideblabla_17_p2
  // Dideblabla dideblabla_108: pin names not known; wires that end beside it: not_4_out, dideblabla_17_p2
  // Dideblabla dideblabla_109: pin names not known; wires that end beside it: Y_1, dideblabla_19_p2
  // Dideblabla dideblabla_110: pin names not known; wires that end beside it: not_4_out, dideblabla_19_p2
  // Dideblabla dideblabla_111: pin names not known; wires that end beside it: Y_1, dideblabla_21_p2
  // Dideblabla #(.Blown("true")) dideblabla_112: pin names not known; wires that end beside it: not_4_out, dideblabla_21_p2
  // Dideblabla #(.Blown("true")) dideblabla_113: pin names not known; wires that end beside it: Y_1, dideblabla_23_p2
  // Dideblabla #(.Blown("true")) dideblabla_114: pin names not known; wires that end beside it: not_4_out, dideblabla_23_p2
  // Dideblabla #(.Blown("true")) dideblabla_115: pin names not known; wires that end beside it: Y_1, dideblabla_25_p2
  // Dideblabla dideblabla_116: pin names not known; wires that end beside it: not_4_out, dideblabla_25_p2
  // Dideblabla dideblabla_117: pin names not known; wires that end beside it: Y_1, dideblabla_27_p2
  // Dideblabla dideblabla_118: pin names not known; wires that end beside it: not_4_out, dideblabla_27_p2
  // Dideblabla dideblabla_119: pin names not known; wires that end beside it: Y_1
  // Dideblabla dideblabla_120: pin names not known; wires that end beside it: not_4_out
  not not_5 (not_5_out, Y_2);
  // Dideblabla #(.Blown("true")) dideblabla_121: pin names not known; wires that end beside it: dideblabla_1_p1, Y_2, dideblabla_1_p3
  // Dideblabla #(.Blown("true")) dideblabla_122: pin names not known; wires that end beside it: dideblabla_1_p1, not_5_out, dideblabla_1_p3
  // Dideblabla dideblabla_123: pin names not known; wires that end beside it: Y_2, dideblabla_3_p2
  // Dideblabla dideblabla_124: pin names not known; wires that end beside it: not_5_out, dideblabla_3_p2
  // Dideblabla dideblabla_125: pin names not known; wires that end beside it: Y_2, dideblabla_5_p2
  // Dideblabla dideblabla_126: pin names not known; wires that end beside it: not_5_out, dideblabla_5_p2
  // Dideblabla dideblabla_127: pin names not known; wires that end beside it: Y_2, dideblabla_7_p2
  // Dideblabla dideblabla_128: pin names not known; wires that end beside it: not_5_out, dideblabla_7_p2
  // Dideblabla dideblabla_129: pin names not known; wires that end beside it: Y_2, dideblabla_9_p2
  // Dideblabla dideblabla_130: pin names not known; wires that end beside it: not_5_out, dideblabla_9_p2
  // Dideblabla #(.Blown("true")) dideblabla_131: pin names not known; wires that end beside it: Y_2, dideblabla_11_p2
  // Dideblabla #(.Blown("true")) dideblabla_132: pin names not known; wires that end beside it: not_5_out, dideblabla_11_p2
  // Dideblabla #(.Blown("true")) dideblabla_133: pin names not known; wires that end beside it: Y_2, dideblabla_13_p2
  // Dideblabla #(.Blown("true")) dideblabla_134: pin names not known; wires that end beside it: not_5_out, dideblabla_13_p2
  // Dideblabla dideblabla_135: pin names not known; wires that end beside it: Y_2, dideblabla_15_p2
  // Dideblabla dideblabla_136: pin names not known; wires that end beside it: not_5_out, dideblabla_15_p2
  // Dideblabla dideblabla_137: pin names not known; wires that end beside it: Y_2, dideblabla_17_p2
  // Dideblabla dideblabla_138: pin names not known; wires that end beside it: not_5_out, dideblabla_17_p2
  // Dideblabla dideblabla_139: pin names not known; wires that end beside it: Y_2, dideblabla_19_p2
  // Dideblabla dideblabla_140: pin names not known; wires that end beside it: not_5_out, dideblabla_19_p2
  // Dideblabla #(.Blown("true")) dideblabla_141: pin names not known; wires that end beside it: Y_2, dideblabla_21_p2
  // Dideblabla dideblabla_142: pin names not known; wires that end beside it: not_5_out, dideblabla_21_p2
  // Dideblabla dideblabla_143: pin names not known; wires that end beside it: Y_2, dideblabla_23_p2
  // Dideblabla #(.Blown("true")) dideblabla_144: pin names not known; wires that end beside it: not_5_out, dideblabla_23_p2
  // Dideblabla dideblabla_145: pin names not known; wires that end beside it: Y_2, dideblabla_25_p2
  // Dideblabla #(.Blown("true")) dideblabla_146: pin names not known; wires that end beside it: not_5_out, dideblabla_25_p2
  // Dideblabla dideblabla_147: pin names not known; wires that end beside it: Y_2, dideblabla_27_p2
  // Dideblabla dideblabla_148: pin names not known; wires that end beside it: not_5_out, dideblabla_27_p2
  // Dideblabla dideblabla_149: pin names not known; wires that end beside it: Y_2
  // Dideblabla dideblabla_150: pin names not known; wires that end beside it: not_5_out
  PullUp pullup_1 (.out(dideblabla_1_p1));
  PullUp pullup_2 (.out(dideblabla_1_p3));
  PullUp pullup_3 (.out(dideblabla_3_p2));
  PullUp pullup_4 (.out(dideblabla_5_p2));
  PullUp pullup_5 (.out(dideblabla_7_p2));
  PullUp pullup_6 (.out(dideblabla_9_p2));
  PullUp pullup_7 (.out(dideblabla_11_p2));
  PullUp pullup_8 (.out(dideblabla_13_p2));
  PullUp pullup_9 (.out(dideblabla_15_p2));
  PullUp pullup_10 (.out(dideblabla_17_p2));
  PullUp pullup_11 (.out(dideblabla_19_p2));
  PullUp pullup_12 (.out(dideblabla_21_p2));
  PullUp pullup_13 (.out(dideblabla_23_p2));
  PullUp pullup_14 (.out(dideblabla_25_p2));
  PullUp pullup_15 (.out(dideblabla_27_p2));
  or or_1 (or_1_out, dideblabla_1_p1, dideblabla_1_p3, dideblabla_3_p2, dideblabla_5_p2, dideblabla_7_p2);
  or or_2 (or_2_out, dideblabla_9_p2, dideblabla_11_p2, dideblabla_13_p2, dideblabla_15_p2, dideblabla_17_p2);
  or or_3 (or_3_out, dideblabla_19_p2, dideblabla_21_p2, dideblabla_23_p2, dideblabla_25_p2, dideblabla_27_p2);
  D_FF MC0 (.D(or_1_out), .C(C), .Q(MC0_q));  // open: nQ
  D_FF MC1 (.D(or_2_out), .C(C), .Q(MC1_q));  // open: nQ
  D_FF MC2 (.D(or_3_out), .C(C), .Q(MC2_q));  // open: nQ
  Multiplexer multiplexer_1 (.sel(pullup_16_out), .in_0(or_1_out), .in_1(MC0_q), .out(Y_0));
  Multiplexer multiplexer_2 (.sel(pullup_17_out), .in_0(or_2_out), .in_1(MC1_q), .out(Y_1));
  Multiplexer multiplexer_3 (.sel(pullup_18_out), .in_0(or_3_out), .in_1(MC2_q), .out(Y_2));
  PullUp pullup_16 (.out(pullup_16_out));
  // Dideblabla #(.Blown("true")) dideblabla_151: pin names not known; wires that end beside it: pullup_16_out, 1'b0
  PullUp pullup_17 (.out(pullup_17_out));
  // Dideblabla #(.Blown("true")) dideblabla_152: pin names not known; wires that end beside it: pullup_17_out, 1'b0
  PullUp pullup_18 (.out(pullup_18_out));
  // Dideblabla #(.Blown("true")) dideblabla_153: pin names not known; wires that end beside it: pullup_18_out, 1'b0
endmodule

/* Test case Counter:
A B C   Y_2 Y_1 Y_0
0 0 0   0   0   0
0 0 C   0   0   1
0 0 C   0   1   0
0 0 C   0   1   1
0 0 C   1   0   0
0 0 C   1   0   1
0 0 C   1   1   0
0 0 C   1   1   1
0 0 C   0   0   0
*/
