// Digital circuit WiredOr.dig as structural Verilog
// Sogenanntes Wired-OR. Ein Oder-Gatter welches 
// mit Dioden und einem Pull-Down Widerstand 
// aufgebaut ist.
module WiredOr (
  input  A,
  input  B,
  output Y
);

  // DiodeForeward diodeforeward_1: pin names not known; wires that end beside it: A, Y
  // DiodeForeward diodeforeward_2: pin names not known; wires that end beside it: B, Y
  PullDown pulldown_1 (.out(Y));

  // Notes on the sheet:
  //   A: Erster Eingang des OR-Gatters.
  //   B: Zweiter Eingang des OR-Gatters.
  //   Y: Das Ergebnis der OR-Verknüpfung.
endmodule

/* Test case:
A B Y
0 0 0
0 1 1
0 Z 0
1 0 1
1 1 1
1 Z 1
Z 0 0
Z 1 1
Z Z 0
*/
