// Digital circuit LSR.dig as structural Verilog
// Rechts schieben. Also eine Division durch Zwei.
// Das Carry-Bit wird dabei oben eingeschoben. Und
// das niederwertigste Bit wird als neues Carry-Bit 
// Ausgegeben.
module LSR (
  input  [15:0] Di,
  input  Ci,
  output [15:0] Do,
  output Co
);


  assign Co = Di[0];
  assign Do = {Ci, Di[15:1]};

  // Notes on the sheet:
  //   Di: Dateneingang
  //   Ci: Carry-Eingang
  //   Do: Datenausgang
  //   Co: Carry-Ausgang
endmodule
