// Digital circuit Control.dig as structural Verilog
// Leitwerk für einen einfachen Prozessor.
module Control (
  input  [6:0] Op,
  output stPC,
  output WE,
  output imm,
  output absJmp,
  output [2:0] muxB,
  output srcToD,
  output muxA,
  output ALUToBus,
  output [4:0] ALUop,
  output [2:0] Branch,
  output st,
  output ld,
  output ioW,
  output ioR
);

  wire [5:0] multiplexer_1_out;
  wire [23:20] Logic_d;

  Multiplexer #(.Bits(6)) multiplexer_1 (.sel(Op[6]), .in_0(Op[5:0]), .in_1({6{1'b0}}), .out(multiplexer_1_out));
  ROM #(.Bits(24), .Addr_Bits(6)) Logic (
    .A(multiplexer_1_out), .sel(1'b1),
    .D({Logic_d[23:22], srcToD, Logic_d[20], ioR, ioW, Branch, ALUop, muxA, stPC, WE, ALUToBus, absJmp, muxB, st, ld}));
  Break #(.Cycles(600000)) Break (.brk(Logic_d[20]));

  assign imm = Op[6];

  // Notes on the sheet:
  //   Op: Der Opcode incl. Immediate Bit
  //   stPC: Programm Counter in Register Speichern
  //   WE: Wert am Datenbus in Register speichern
  //   imm: Aktiviert das Speichern der Konstanten
  //   absJmp: absoluten Sprung auslösen
  //   muxB: Selektor für Mux B
  //   srcToD: SourceRegister auf Datenbus legen
  //   muxA: Selector für Mux A
  //   ALUToBus: ALU auf den Datenbus legen
  //   ALUop: Operation der ALU
  //   Branch: Art des bedingten Sprunges
  //   st: Ram speichert Daten vom Datenbus
  //   ld: Ram gibt Daten auf den Datenbus
  //   ioW: Es wird auf die IO geschrieben
  //   ioR: Es wird IO gelesen
  //   contents of Logic (hex, n*v repeats v):
  //   63
  //   0
  //   192
  //   1216
  //   17600
  //   2240
  //   18624
  //   3264
  //   4288
  //   5312
  //   196
  //   212
  //   1220
  //   1236
  //   17604
  //   17620
  //   2244
  //   2260
  //   18628
  //   18644
  //   3268
  //   3284
  //   4292
  //   4308
  //   5316
  //   5332
  //   11456
  //   11460
  //   11476
  //   2048
  //   2052
  //   2068
  //   6336
  //   7360
  //   22720
  //   23744
  //   8384
  //   9408
  //   10432
  //   2098186
  //   1673
  //   2097158
  //   2097182
  //   133
  //   149
  //   2098182
  //   1669
  //   32792
  //   65560
  //   98328
  //   163864
  //   196632
  //   229400
  //   420
  //   32
  //   36
  //   131096
  //   2359300
  //   2359324
  //   2360328
  //   524932
  //   524948
  //   525960
  //   1048576
  //   16
endmodule
