// Digital circuit FlagsRW.dig as structural Verilog
// Speichert die Prozessorflags
module FlagsRW (
  input  Zi,
  input  Ni,
  input  Ci,
  input  C,
  input  store,
  input  [15:0] A,
  input  IOR,
  input  IOW,
  input  [15:0] Data,
  output Zo,
  output No,
  output Co
);

  wire and_1_out, and_2_out, and_3_out, comparator_1_eq, multiplexer_1_out, multiplexer_2_out,
       multiplexer_3_out, or_1_out;

  PullDown #(.Bits(16)) pulldown_1 (.out(Data));
  Comparator #(.Bits(16)) comparator_1 (.a(A), .b({16{1'b0}}), .eq(comparator_1_eq));  // open: gt, lt
  and and_1 (and_1_out, IOW, comparator_1_eq);
  and and_2 (and_2_out, comparator_1_eq, IOR);
  Multiplexer multiplexer_1 (.sel(and_1_out), .in_0(Ci), .in_1(Data[0]), .out(multiplexer_1_out));
  Multiplexer multiplexer_2 (.sel(and_1_out), .in_0(Zi), .in_1(Data[1]), .out(multiplexer_2_out));
  Multiplexer multiplexer_3 (.sel(and_1_out), .in_0(Ni), .in_1(Data[2]), .out(multiplexer_3_out));
  or or_1 (or_1_out, store, and_1_out);
  and and_3 (and_3_out, C, or_1_out);
  D_FF d_ff_1 (.D(multiplexer_1_out), .C(and_3_out), .Q(Co));  // open: nQ
  D_FF d_ff_2 (.D(multiplexer_2_out), .C(and_3_out), .Q(Zo));  // open: nQ
  D_FF d_ff_3 (.D(multiplexer_3_out), .C(and_3_out), .Q(No));  // open: nQ
  assign Data = and_2_out ? {{13{1'b0}}, No, Zo, Co} : 16'bz;  // Driver driver_1

  // Notes on the sheet:
  //   IOR: IOR
endmodule
