// Digital circuit HDLExample.dig as structural Verilog
// Example of a processor that can be exported to VHDL.
// {{de Beispiel für einen Prozessor, der zu VHDL exportiert werden kann.}}
module HDLExample (
  input  Clock,
  input  reset,
  input  U,
  input  D,
  input  R,
  input  L,
  output Y0,
  output Y1,
  output Y2,
  output Y3,
  output Y4,
  output Y5,
  output Y6,
  output Y7,
  output Y8,
  output Y9,
  output Y10,
  output Y11,
  output Y12,
  output Y13,
  output Y14,
  output Y15
);

  wire ioR, processormux_1_iow;
  wire [15:0] adr, gpi_hdl_1_p7, processormux_1_d_out, processormux_1_pc, ROM_d;

  // GPI_HDL gpi_hdl_1: pin names not known; wires that end beside it: adr, ioR, U, L, R, D, gpi_hdl_1_p7, Y15
  ProcessorMux processormux_1 (
    .Instr(ROM_d), .Clock(Clock), .reset(reset), .D_in(gpi_hdl_1_p7), .PC(processormux_1_pc),
    .D_out(processormux_1_d_out), .Addr(adr), .ioR(ioR), .ioW(processormux_1_iow));
  ROM #(.AddrBits(16), .isProgramMemory("true"), .Bits(16), .Addr_Bits(16)) ROM (
    .A(processormux_1_pc), .sel(1'b1), .D(ROM_d));
  // GPO gpo_1: pin names not known; wires that end beside it: Y14, Y13, Y12, Y11, Y10, Y9, Y8, Y7, Y6, Y5, Y4, processormux_1_iow, Y3, Clock, Y2, adr, Y1, processormux_1_d_out, Y0

  // Notes on the sheet:
  //   Clock: pin W5, Hz: 200
  //   Y0: pin U16
  //   Y1: pin E19
  //   Y2: pin U19
  //   Y3: pin V19
  //   Y4: pin W18
  //   Y5: pin U15
  //   Y6: pin U14
  //   Y7: pin V14
  //   Y8: pin V13
  //   Y9: pin V3
  //   Y10: pin W3
  //   Y11: pin U3
  //   Y12: pin P3
  //   Y13: pin N3
  //   Y14: pin P1
  //   Y15: pin L1
  //   reset: pin U18
  //   U: pin T18
  //   D: pin U17
  //   R: pin T17
  //   L: pin W19
  //   Pin numbers are defined to match the BASYS3 FPGA board.
  //   {{de Die Pin-Nummern sind definiert für ein BASYS3 FPGA  Board.}}
  //   contents of ROM (hex, n*v repeats v):
  //   802e,1220,7800,5610,5200,3c00,5e0e,3c10,640c,210,2811,6422,210,2818,6431,210,2812,
  //   6404,210,2814,640c,6a02,801a,1220,1580,1491,7359,3e90,2081,6402,1580,1491,6fe1,8026,
  //   1220,1580,8000,1390,7359,4090,2081,6403,1580,8000,1390,6fd4,8032,1220,1491,14a0,7359,
  //   3ca0,6406,3e90,8000,3b90,65c9,14a1,6fc7,4090,3c91,65c4,14a0,6fc2,8045,1220,1484,9111,
  //   1290,7359,3e90,2081,6403,1484,9111,1290,6fb5
endmodule

/* Test case:
     reset  Clock U D L R Y15 Y14 Y13 Y12 Y11 Y10 Y9 Y8 Y7 Y6 Y5 Y4 Y3 Y2 Y1 Y0
           1    0 0 0 0 0  x   x    x  x   x   x   x  x  x  x  x  x  x  x  x  x
           1    1 0 0 0 0  x   x    x  x   x   x   x  x  x  x  x  x  x  x  x  x
           1    0 0 0 0 0  x   x    x  x   x   x   x  x  x  x  x  x  x  x  x  x
           0    0 0 0 0 0  x   x    x  x   x   x   x  x  x  x  x  x  x  x  x  x

repeat(12) 0    C 0 0 0 0  0   0    0  0   0   0   0  0  0  0  0  0  0  0  0  0

loop(i,15)
repeat(13) 0    C 0 0 0 0  bits(16,1<<i)
end loop

repeat(2)  0    C 0 0 0 0  bits(16,1<<14)

loop(i,15)
repeat(12) 0    C 0 0 0 0  bits(16,1<<(15-i))
end loop
*/
