// Digital circuit Terminal.dig as structural Verilog
// Terminal. Die Adresse ist 0x1F.
module Terminal (
  input  [15:0] D,
  input  [15:0] A,
  input  C,
  input  W
);

  wire and_1_out, comparator_1_eq;

  Comparator #(.Bits(16)) comparator_1 (.a(A), .b(16'h1f), .eq(comparator_1_eq));  // open: gt, lt
  and and_1 (and_1_out, comparator_1_eq, C, W);
  Terminal terminal_1 (.D(D), .C(and_1_out));  // open: en

  // Notes on the sheet:
  //   D: Datenbus
  //   A: Addressbus
  //   C: Takt
  //   W: Write Enable
endmodule
