// Digital circuit Memory.dig as structural Verilog
module Memory (
  input  [15:0] A,
  input  C,
  input  str,
  input  ld,
  output [15:0] D
);

  wire and_1_out, and_2_out, and_3_out, not_1_out;

  not not_1 (not_1_out, A[15]);
  and and_1 (and_1_out, not_1_out, ld);
  and and_2 (and_2_out, A[15], str);
  and and_3 (and_3_out, A[15], ld);
  ROM #(.isProgramMemory("true"), .Bits(16), .Addr_Bits(15)) rom_1 (.A(A[14:0]), .sel(and_1_out), .D(D));
  RAMSinglePort #(.Bits(16), .Addr_Bits(15)) ramsingleport_1 (
    .A(A[14:0]), .str(and_2_out), .C(C), .ld(and_3_out), .D(D));

  // Notes on the sheet:
  //   contents of rom_1 (hex, n*v repeats v):
  //   140f,20e1,4ce0,20e1,14f7,4cef,6e03,5200,7c00,6ff6,20e1,4ced,2de,20e1,8002,5a0d,3c02,
  //   5c16,2001,20e1,4ce0,20e1,15f9,4cef,6ff1,ffff,59d0,8002,5a0d,2002,20e1,4ce0,20e1,8025,
  //   12f0,4cef,6fe5,ffff,5b1d,401,2ed,4ede,18e1,4efe,18e2,6a0f
endmodule
