// Digital circuit Processor.dig as structural Verilog
module Processor (
  input  Clock
);

  wire abs, ALU2D, alu_1_carry, alu_1_neg, alu_1_zero, branch_1_jmp, flags_1_co, flags_1_no, flags_1_zo,
       gpo_1_p1, gpo_1_p2, gpo_1_p3, gpo_1_p4, gpo_1_p5, gpo_1_p6, gpo_1_p7, gpo_1_p8, gpo_1_p9, gpo_1_p10,
       gpo_1_p11, gpo_1_p12, gpo_1_p14, gpo_1_p16, gpo_1_p18, gpo_1_p20, imm, ioR, ioW, ld, muxA, sf, src2D,
       st, stPC, WE;
  wire [2:0] br, muxB;
  wire [4:0] ALUop;
  wire [15:0] alu_1_y, driver_1_out, imreg_1_imm, multiplexer_1_out, multiplexer_2_out, pc_1_next, pc_1_pc,
       register_1_rdest, register_1_rsrc, rom_1_d, signext_1__5d, signext_1__5s, signext_1__9sd;

  PC pc_1 (.ALU(alu_1_y), .C(Clock), .abs(abs), .rel(branch_1_jmp), .Next(pc_1_next), .PC(pc_1_pc));
  ROM #(.Bits(16), .Addr_Bits(16)) rom_1 (.A(pc_1_pc), .sel(1'b1), .D(rom_1_d));
  assign driver_1_out = stPC ? pc_1_next : 16'bz;  // Driver driver_1
  Control control_1 (
    .Op(rom_1_d[15:9]), .stPC(stPC), .WE(WE), .imm(imm), .absJmp(abs), .muxB(muxB), .srcToD(src2D),
    .muxA(muxA), .ALUToBus(ALU2D), .ALUop(ALUop), .storeFlags(sf), .Branch(br), .st(st), .ld(ld), .ioW(ioW),
    .ioR(ioR));
  Register register_1 (
    .WD(driver_1_out), .C(Clock), .src(rom_1_d[3:0]), .dest(rom_1_d[7:4]), .WE(WE), .Rdest(register_1_rdest),
    .Rsrc(register_1_rsrc));
  ImReg imreg_1 (.inst(rom_1_d), .en(imm), .C(Clock), .imm(imreg_1_imm));
  SignExt signext_1 (.inst(rom_1_d), ._5S(signext_1__5s), ._9SD(signext_1__9sd), ._5D(signext_1__5d));
  assign driver_1_out = src2D ? register_1_rsrc : 16'bz;  // Driver driver_2
  Multiplexer #(.Bits(16)) multiplexer_1 (
    .sel(muxA), .in_0(register_1_rdest), .in_1(register_1_rsrc), .out(multiplexer_1_out));
  Multiplexer #(.Selector_Bits(3), .Bits(16)) multiplexer_2 (
    .sel(muxB), .in_0(register_1_rsrc), .in_1(imreg_1_imm), .in_2({16{1'b0}}), .in_3(16'hff), .in_4(16'hfff),
    .in_5(signext_1__5s), .in_6(signext_1__9sd), .in_7(signext_1__5d), .out(multiplexer_2_out));
  LED led_1 (.in(gpo_1_p1));
  LED led_2 (.in(gpo_1_p3));
  LED led_3 (.in(gpo_1_p2));
  Branch branch_1 (.Z(flags_1_zo), .N(flags_1_no), .C(flags_1_co), .ctrl(br), .jmp(branch_1_jmp));
  LED led_4 (.in(gpo_1_p5));
  LED led_5 (.in(gpo_1_p4));
  ALU alu_1 (
    .A(multiplexer_1_out), .B(multiplexer_2_out), .Op(ALUop), .Ci(flags_1_co), .Y(alu_1_y),
    .Zero(alu_1_zero), .Neg(alu_1_neg), .Carry(alu_1_carry));
  LED led_6 (.in(gpo_1_p7));
  LED led_7 (.in(gpo_1_p6));
  Flags flags_1 (
    .Zi(alu_1_zero), .Ni(alu_1_neg), .Ci(alu_1_carry), .C(Clock), .store(sf), .Zo(flags_1_zo),
    .No(flags_1_no), .Co(flags_1_co));
  LED led_8 (.in(gpo_1_p9));
  LED led_9 (.in(gpo_1_p8));
  assign driver_1_out = ALU2D ? alu_1_y : 16'bz;  // Driver driver_3
  LED led_10 (.in(gpo_1_p11));
  LED led_11 (.in(gpo_1_p10));
  // GPO gpo_1: pin names not known; wires that end beside it: gpo_1_p1, gpo_1_p2, gpo_1_p3, gpo_1_p4, gpo_1_p5, gpo_1_p6, gpo_1_p7, gpo_1_p8, gpo_1_p9, gpo_1_p10, gpo_1_p11, gpo_1_p12, ioW, gpo_1_p14, Clock, gpo_1_p16, alu_1_y, gpo_1_p18, driver_1_out, gpo_1_p20
  LED led_12 (.in(gpo_1_p14));
  LED led_13 (.in(gpo_1_p12));
  RAMSinglePort #(.Bits(16), .Addr_Bits(16)) ramsingleport_1 (
    .A(alu_1_y), .str(st), .C(Clock), .ld(ld), .D(driver_1_out));
  Graphics graphics_1 (.A(alu_1_y), .R(ioR), .C(Clock), .W(ioW), .D(driver_1_out));
  Terminal terminal_1 (.D(driver_1_out), .A(alu_1_y), .C(Clock), .W(ioW));
  LED led_14 (.in(gpo_1_p18));
  LED led_15 (.in(gpo_1_p16));
  LED led_16 (.in(gpo_1_p20));

  // Other names for the same wires on the sheet: C = Clock

  // Notes on the sheet:
  //   Clock: Hz: 500000
  //   contents of rom_1 (hex, n*v repeats v):
  //   166
  //   5120
  //   5137
  //   32768
  //   4960
  //   33168
  //   4944
  //   5251
  //   5408
  //   5179
  //   8417
  //   5373
  //   19695
  //   28305
  //   6177
  //   8417
  //   5618
  //   19695
  //   28300
  //   8225
  //   6193
  //   8417
  //   5624
  //   19695
  //   28294
  //   8225
  //   8417
  //   32798
  //   4848
  //   19695
  //   28288
  //   6177
  //   6193
  //   8417
  //   32805
  //   4848
  //   19695
  //   28281
  //   28198
  //   5168
  //   5152
  //   5280
  //   8417
  //   32814
  //   4848
  //   19695
  //   28195
  //   8417
  //   32819
  //   4848
  //   19695
  //   28259
  //   15488
  //   24069
  //   15474
  //   24069
  //   15475
  //   24067
  //   28163
  //   15475
  //   25601
  //   5283
  //   650
  //   8417
  //   32835
  //   4848
  //   19695
  //   28251
  //   6177
  //   15652
  //   26082
  //   6193
  //   15668
  //   26078
  //   12433
  //   65535
  //   28681
  //   582
  //   613
  //   596
  //   31744
  //   28629
  //   5232
  //   8241
  //   8417
  //   32856
  //   4848
  //   19695
  //   28207
  //   6177
  //   8417
  //   32862
  //   4848
  //   19695
  //   28201
  //   6193
  //   8417
  //   32868
  //   4848
  //   19695
  //   28195
  //   6193
  //   8417
  //   32874
  //   4848
  //   19695
  //   28189
  //   8225
  //   8417
  //   32880
  //   4848
  //   19695
  //   28183
  //   8225
  //   8417
  //   32886
  //   4848
  //   19695
  //   28177
  //   8241
  //   8417
  //   32892
  //   4848
  //   19695
  //   28171
  //   8241
  //   8417
  //   32898
  //   4848
  //   19695
  //   28165
  //   6177
  //   6193
  //   20222
  //   6369
  //   27151
  //   15652
  //   25098
  //   15668
  //   25096
  //   579
  //   14148
  //   1090
  //   1093
  //   31364
  //   15488
  //   24065
  //   6257
  //   20222
  //   6369
  //   27151
  //   579
  //   14148
  //   1090
  //   1093
  //   31364
  //   20222
  //   6369
  //   27151
  //   579
  //   14148
  //   1090
  //   1094
  //   29768
  //   20222
  //   6369
  //   27151
  //   16
endmodule
