// Digital circuit ProcessorTest.dig as structural Verilog
module ProcessorTest (
  input  Clk
);

  Processor processor_1 (.Clock(Clk));

  // Notes on the sheet:
  //   Clk: Hz: 200
endmodule

/* Test case MOV:
# auto generated, do not modify
Clk R1 R2

init R1=3;
init R2=4;

# mov r2,r1
program(0x121)

C X X

# expects
# R1=3
# R2=3
0 3 3
*/

/* Test case ADD no carry:
# auto generated, do not modify
Clk Carry R2

init R1=3;
init R2=4;

# add r2,r1
program(0x221)

C X X

# expects
# Carry=0
# R2=7
0 0 7
*/

/* Test case ADD carry:
# auto generated, do not modify
Clk Carry R2

init R1=-1;
init R2=-1;

# add r2,r1
program(0x221)

C X X

# expects
# Carry=1
# R2=65534
0 1 65534
*/

/* Test case ADC no carry:
# auto generated, do not modify
Clk Carry R2

init R1=3;
init R2=4;

# adc r2,r1
program(0x321)

C X X

# expects
# Carry=0
# R2=7
0 0 7
*/

/* Test case ADC carry:
# auto generated, do not modify
Clk Carry R2

init R1=3;
init R2=4;
init Carry=1;

# adc r2,r1
program(0x321)

C X X

# expects
# Carry=0
# R2=8
0 0 8
*/

/* Test case ADC carry out:
# auto generated, do not modify
Clk Carry R2

init R1=-1;
init R2=-1;

# adc r2,r1
program(0x321)

C X X

# expects
# Carry=1
# R2=65534
0 1 65534
*/

/* Test case ADDI small:
# auto generated, do not modify
Clk R1

init R1=3;

# addi r1,4
program(0xc14)

C X

# expects
# R1=7
0 7
*/

/* Test case ADDI large:
# auto generated, do not modify
Clk R1

init R1=3;

# addi r1,20
program(0x8014,0xb10)

repeat (2) C X

# expects
# R1=23
0 23
*/

/* Test case ADCI small:
# auto generated, do not modify
Clk R1

init R1=3;

# adci r1,4
program(0xe14)

C X

# expects
# R1=7
0 7
*/

/* Test case ADCI large:
# auto generated, do not modify
Clk R1

init R1=3;

# adci r1,20
program(0x8014,0xd10)

repeat (2) C X

# expects
# R1=23
0 23
*/

/* Test case ADCI small, carry:
# auto generated, do not modify
Clk R1

init R1=3;
init Carry=1;

# adci r1,4
program(0xe14)

C X

# expects
# R1=8
0 8
*/

/* Test case ADCI large, carry:
# auto generated, do not modify
Clk R1

init R1=3;
init Carry=1;

# adci r1,20
program(0x8014,0xd10)

repeat (2) C X

# expects
# R1=24
0 24
*/

/* Test case SUB:
# auto generated, do not modify
Clk Carry R2

init R1=3;
init R2=4;

# sub r2,r1
program(0x421)

C X X

# expects
# Carry=0
# R2=1
0 0 1
*/

/* Test case SUB carry out:
# auto generated, do not modify
Clk Carry R2

init R1=4;
init R2=3;

# sub r2,r1
program(0x421)

C X X

# expects
# Carry=1
# R2=65535
0 1 65535
*/

/* Test case SBC:
# auto generated, do not modify
Clk Carry R2

init R1=3;
init R2=4;

# sbc r2,r1
program(0x521)

C X X

# expects
# Carry=0
# R2=1
0 0 1
*/

/* Test case SBC carry in:
# auto generated, do not modify
Clk Carry R2

init R1=3;
init R2=5;
init Carry=1;

# sbc r2,r1
program(0x521)

C X X

# expects
# Carry=0
# R2=1
0 0 1
*/

/* Test case SUBI small:
# auto generated, do not modify
Clk R1

init R1=4;

# subi r1,2
program(0x1012)

C X

# expects
# R1=2
0 2
*/

/* Test case SUBI large:
# auto generated, do not modify
Clk R1

init R1=30;

# subi r1,20
program(0x8014,0xf10)

repeat (2) C X

# expects
# R1=10
0 10
*/

/* Test case SBCI no carry, small:
# auto generated, do not modify
Clk R1

init R1=6;

# sbci r1,4
program(0x1214)

C X

# expects
# R1=2
0 2
*/

/* Test case SBCI no carry, large:
# auto generated, do not modify
Clk R1

init R1=30;

# sbci r1,20
program(0x8014,0x1110)

repeat (2) C X

# expects
# R1=10
0 10
*/

/* Test case SBCI carry in, small:
# auto generated, do not modify
Clk R1

init R1=6;
init Carry=1;

# sbci r1,4
program(0x1214)

C X

# expects
# R1=1
0 1
*/

/* Test case SBCI carry in, large:
# auto generated, do not modify
Clk R1

init R1=30;
init Carry=1;

# sbci r1,20
program(0x8014,0x1110)

repeat (2) C X

# expects
# R1=9
0 9
*/

/* Test case NOT:
# auto generated, do not modify
Clk R1

init R1=0;

# not r1
program(0x1a10)

C X

# expects
# R1=65535
0 65535
*/

/* Test case NEG:
# auto generated, do not modify
Clk R1

init R1=1;

# neg r1
program(0x1310)

C X

# expects
# R1=65535
0 65535
*/

/* Test case SWAP:
# auto generated, do not modify
Clk R1

init R1=4660;

# swap r1
# brk
program(0x2910,0x4400)

repeat (2) C X

# expects
# R1=13330
0 13330
*/

/* Test case SWAPN:
# auto generated, do not modify
Clk R1

init R1=4660;

# swapn r1
program(0x2a10)

C X

# expects
# R1=8515
0 8515
*/

/* Test case MUL:
# auto generated, do not modify
Clk R1 R0

init R0=7;
init R1=8;

# mul r0,r1
program(0x1b01)

C X X

# expects
# R1=8
# R0=56
0 8 56
*/

/* Test case LDI small:
# auto generated, do not modify
Clk R1


# ldi r1,5
program(0xa15)

C X

# expects
# R1=5
0 5
*/

/* Test case LDI small:
# auto generated, do not modify
Clk R1


# ldi r1,15
program(0xa1f)

C X

# expects
# R1=15
0 15
*/

/* Test case LDI large:
# auto generated, do not modify
Clk R1


# ldi r1,16
program(0x8010,0x910)

repeat (2) C X

# expects
# R1=16
0 16
*/

/* Test case LDI large:
# auto generated, do not modify
Clk R1


# ldi r1,0x8000
program(0x8000,0x911)

repeat (2) C X

# expects
# R1=32768
0 32768
*/

/* Test case LDS small:
# auto generated, do not modify
Clk R1 R2

memory mem(0)=6;
memory mem(1)=7;

# lds r1,0
# lds r2,1
program(0x3010,0x3021)

repeat (2) C X X

# expects
# R1=6
# R2=7
0 6 7
*/

/* Test case LDS large:
# auto generated, do not modify
Clk R1

memory mem(32768)=8;

# lds r1,0x8000
program(0x8000,0x2f11)

repeat (2) C X

# expects
# R1=8
0 8
*/

/* Test case STS small:
# auto generated, do not modify
Clk R2

init R1=7;

# sts 1,r1
# lds r2,1
program(0x2e11,0x3021)

repeat (2) C X

# expects
# R2=7
0 7
*/

/* Test case STS large:
# auto generated, do not modify
Clk R1

init R1=8;

# sts 0x8000,r1
# lds r2,0x8000
program(0x8000,0x2d11,0x8000,0x2f21)

repeat (4) C X

# expects
# R1=8
0 8
*/

/* Test case LD:
# auto generated, do not modify
Clk R0 R1

memory mem(1)=7;
memory mem(32768)=8;
init R2=1;
init R3=32768;

# ld r0,[r2]
# ld r1,[r3]
program(0x2c02,0x2c13)

repeat (2) C X X

# expects
# R0=7
# R1=8
0 7 8
*/

/* Test case LDD:
# auto generated, do not modify
Clk R0 R1

memory mem(3)=7;
memory mem(32768)=8;
init R2=1;
init R3=32770;

# ldd r0,[r2+2]
# ldd r1,[r3-2]
program(0x8002,0x3202,0xfffe,0x3213)

repeat (4) C X X

# expects
# R0=7
# R1=8
0 7 8
*/

/* Test case ST:
# auto generated, do not modify
Clk R0

init R1=1;
init R2=7;

# st [r1],r2
# lds r0,1
program(0x2b12,0x3001)

repeat (2) C X

# expects
# R0=7
0 7
*/

/* Test case STD:
# auto generated, do not modify
Clk R0 R1

init R2=4;
init R3=7;
init R4=8;

# std [r2+2],r3
# std [r2-2],r4
# lds r0,6
# lds r1,2
program(0x8002,0x3123,0xfffe,0x3124,0x3006,0x3012)

repeat (6) C X X

# expects
# R0=7
# R1=8
0 7 8
*/

/* Test case JMP short:
# auto generated, do not modify
Clk R0

init R0=2;

# jmp end
#  ldi r0, 1
# end: nop
program(0x3d01,0xa01,0x0)

repeat (3) C X

# expects
# R0=2
0 2
*/

/* Test case JMP short back:
# auto generated, do not modify
Clk R0

init PC=20;

# ldi r0,1
# .org 10
# code: ldi r0,3
# .org 20
# jmp code
#  ldi r0, 2
program(0xa01,0x0,0x0,0x0,0x0,0x0,0x0,0x0,0x0,0x0,0xa03,0x0,0x0,0x0,0x0,0x0,0x0,0x0,0x0,0x0,0x3df5,0xa02)

repeat (2) C X

# expects
# R0=3
0 3
*/

/* Test case JMP long:
# auto generated, do not modify
Clk R0


# jmp 130
#  ldi r0, 1
# .org 130
# ldi r0,2
program(0x8082,0x3c00,0xa01,0x0,0x0,0x0,0x0,0x0,0x0,0x0,0x0,0x0,0x0,0x0,0x0,0x0,0x0,0x0,0x0,0x0,0x0,0x0,0x0,0x0,0x0,0x0,0x0,0x0,0x0,0x0,0x0,0x0,0x0,0x0,0x0,0x0,0x0,0x0,0x0,0x0,0x0,0x0,0x0,0x0,0x0,0x0,0x0,0x0,0x0,0x0,0x0,0x0,0x0,0x0,0x0,0x0,0x0,0x0,0x0,0x0,0x0,0x0,0x0,0x0,0x0,0x0,0x0,0x0,0x0,0x0,0x0,0x0,0x0,0x0,0x0,0x0,0x0,0x0,0x0,0x0,0x0,0x0,0x0,0x0,0x0,0x0,0x0,0x0,0x0,0x0,0x0,0x0,0x0,0x0,0x0,0x0,0x0,0x0,0x0,0x0,0x0,0x0,0x0,0x0,0x0,0x0,0x0,0x0,0x0,0x0,0x0,0x0,0x0,0x0,0x0,0x0,0x0,0x0,0x0,0x0,0x0,0x0,0x0,0x0,0x0,0x0,0x0,0x0,0x0,0x0,0xa02)

repeat (3) C X

# expects
# R0=2
0 2
*/

/* Test case RCALL:
# auto generated, do not modify
Clk R0 RA

init R0=3;

# jmp end
# ldi r0, 1
# func: ldi r0,1
# rret ra
# ldi r0,2
# end: rcall ra,func
program(0x3d04,0xa01,0xa01,0x3b0f,0xa02,0x8002,0x3af0)

repeat (7) C X X

# expects
# R0=1
# RA=7
0 1 7
*/

/* Test case BRCS jmp:
# auto generated, do not modify
Clk R0

init Carry=1;
init R0=2;

# brcs end
#  ldi r0, 1
# end: nop
program(0x3401,0xa01,0x0)

repeat (3) C X

# expects
# R0=2
0 2
*/

/* Test case BRCS skip:
# auto generated, do not modify
Clk R0

init Carry=0;
init R0=2;

# brcs end
#  ldi r0, 1
# end: nop
program(0x3401,0xa01,0x0)

repeat (3) C X

# expects
# R0=1
0 1
*/

/* Test case BRCC jmp:
# auto generated, do not modify
Clk R0

init Carry=0;
init R0=2;

# brcc end
#  ldi r0, 1
# end: nop
program(0x3701,0xa01,0x0)

repeat (3) C X

# expects
# R0=2
0 2
*/

/* Test case BRCC skip:
# auto generated, do not modify
Clk R0

init Carry=1;
init R0=2;

# brcc end
#  ldi r0, 1
# end: nop
program(0x3701,0xa01,0x0)

repeat (3) C X

# expects
# R0=1
0 1
*/

/* Test case BRMI jmp:
# auto generated, do not modify
Clk R0

init Neg=1;
init R0=2;

# brmi end
#  ldi r0, 1
# end: nop
program(0x3601,0xa01,0x0)

repeat (3) C X

# expects
# R0=2
0 2
*/

/* Test case BRMI skip:
# auto generated, do not modify
Clk R0

init Neg=0;
init R0=2;

# brmi end
#  ldi r0, 1
# end: nop
program(0x3601,0xa01,0x0)

repeat (3) C X

# expects
# R0=1
0 1
*/

/* Test case BRPL jmp:
# auto generated, do not modify
Clk R0

init Neg=0;
init R0=2;

# brpl end
#  ldi r0, 1
# end: nop
program(0x3901,0xa01,0x0)

repeat (3) C X

# expects
# R0=2
0 2
*/

/* Test case BRPL skip:
# auto generated, do not modify
Clk R0

init Neg=1;
init R0=2;

# brpl end
#  ldi r0, 1
# end: nop
program(0x3901,0xa01,0x0)

repeat (3) C X

# expects
# R0=1
0 1
*/

/* Test case BREQ jmp:
# auto generated, do not modify
Clk R0

init Zero=1;
init R0=2;

# breq end
#  ldi r0, 1
# end: nop
program(0x3501,0xa01,0x0)

repeat (3) C X

# expects
# R0=2
0 2
*/

/* Test case BREQ skip:
# auto generated, do not modify
Clk R0

init Zero=0;
init R0=2;

# breq end
#  ldi r0, 1
# end: nop
program(0x3501,0xa01,0x0)

repeat (3) C X

# expects
# R0=1
0 1
*/

/* Test case BRNE jmp:
# auto generated, do not modify
Clk R0

init Zero=0;
init R0=2;

# brne end
#  ldi r0, 1
# end: nop
program(0x3801,0xa01,0x0)

repeat (3) C X

# expects
# R0=2
0 2
*/

/* Test case BRNE skip:
# auto generated, do not modify
Clk R0

init Zero=1;
init R0=2;

# brne end
#  ldi r0, 1
# end: nop
program(0x3801,0xa01,0x0)

repeat (3) C X

# expects
# R0=1
0 1
*/
