// Digital circuit ProcessorVonNeumann.dig as structural Verilog
// Simple processor based on the MIPS architecture. 
// It is a Von Neumann Two-Cycle CPU.
// {{de Einfacher Prozessor, der an die MIPS-Architektur 
// angelehnt ist. Es handelt sich um eine 
// Von Neumann Two-Cycle CPU.}}
module ProcessorVonNeumann (
  input  Clock
);

  wire abs, ALU2D, alu_1_carry, alu_1_neg, alu_1_zero, branch_1_jmp, C, C_in, flags_1_co, flags_1_no,
       flags_1_zo, imm, ioR, ioW, ld, muxA, S_in, sf, src2D, st, stPC, WE;
  wire [2:0] br, muxB;
  wire [4:0] ALUop;
  wire [15:0] alu_1_y, driver_1_out, imreg_1_imm, Instruction_q, multiplexer_1_out, multiplexer_2_out,
       multiplexer_3_out, pc_1_next, pc_1_pc, registeropt_1_p6, registeropt_1_p7, signext_1__5d,
       signext_1__5s, signext_1__9sd;

  PC pc_1 (.ALU(alu_1_y), .C(C), .abs(abs), .rel(branch_1_jmp), .Next(pc_1_next), .PC(pc_1_pc));
  Register #(.Bits(16)) Instruction (.D(driver_1_out), .C(C_in), .en(1'b1), .Q(Instruction_q));
  assign driver_1_out = stPC ? pc_1_next : 16'bz;  // Driver driver_1
  // RegisterOpt registeropt_1: pin names not known; wires that end beside it: driver_1_out, C, Instruction_q[3:0], Instruction_q[7:4], WE, registeropt_1_p6, registeropt_1_p7
  ImReg imreg_1 (.inst(Instruction_q), .en(imm), .C(C), .imm(imreg_1_imm));
  SignExt signext_1 (.inst(Instruction_q), ._5S(signext_1__5s), ._9SD(signext_1__9sd), ._5D(signext_1__5d));
  ControlTwoCycle controltwocycle_1 (
    .Op(Instruction_q[15:9]), .Clock(Clock), .stPC(stPC), .WE(WE), .imm(imm), .absJmp(abs), .muxB(muxB),
    .srcToD(src2D), .muxA(muxA), .ALUToBus(ALU2D), .ALUop(ALUop), .storeFlags(sf), .Branch(br), .st(st),
    .ld(ld), .ioW(ioW), .ioR(ioR), .C(C), .C_in(C_in), .S_in(S_in));
  assign driver_1_out = src2D ? registeropt_1_p7 : 16'bz;  // Driver driver_2
  Multiplexer #(.Bits(16)) multiplexer_1 (
    .sel(muxA), .in_0(registeropt_1_p6), .in_1(registeropt_1_p7), .out(multiplexer_1_out));
  Multiplexer #(.Selector_Bits(3), .Bits(16)) multiplexer_2 (
    .sel(muxB), .in_0(registeropt_1_p7), .in_1(imreg_1_imm), .in_2({16{1'b0}}), .in_3({16{1'b0}}),
    .in_4({16{1'b0}}), .in_5(signext_1__5s), .in_6(signext_1__9sd), .in_7(signext_1__5d),
    .out(multiplexer_2_out));
  Branch branch_1 (.Z(flags_1_zo), .N(flags_1_no), .C(flags_1_co), .ctrl(br), .jmp(branch_1_jmp));
  ALU alu_1 (
    .A(multiplexer_1_out), .B(multiplexer_2_out), .Op(ALUop), .Y(alu_1_y), .Zero(alu_1_zero),
    .Neg(alu_1_neg), .Carry(alu_1_carry), .Ci(flags_1_co));
  Flags flags_1 (
    .Zi(alu_1_zero), .Ni(alu_1_neg), .Ci(alu_1_carry), .C(C), .store(sf), .Zo(flags_1_zo), .No(flags_1_no),
    .Co(flags_1_co));
  assign driver_1_out = ALU2D ? alu_1_y : 16'bz;  // Driver driver_3
  Multiplexer #(.Bits(16)) multiplexer_3 (.sel(S_in), .in_0(alu_1_y), .in_1(pc_1_pc), .out(multiplexer_3_out));
  Memory memory_1 (.A(multiplexer_3_out), .C(st), .str(C), .ld(ld), .D(driver_1_out));
  LedMatrix ledmatrix_1 (.D(driver_1_out), .A(alu_1_y), .C(C), .W(ioW));

  // Notes on the sheet:
  //   Clock: Hz: 500000
endmodule
