// Digital circuit Rising.dig as structural Verilog
module Rising (
  input  Reset,
  input  Set,
  output Out
);

  wire not_1_out, or_1_out;

  or or_1 (or_1_out, Set, Out);
  and and_1 (Out, or_1_out, not_1_out);
  not not_1 (not_1_out, Reset);
endmodule
