// Digital circuit SWAPN.dig as structural Verilog
module SWAPN (
  input  [15:0] Di,
  output [15:0] Do
);

  // Pins of 1 and 16 bits meet at Di

  assign Do = {Di[11:8], Di[15:12], Di[3:0], Di[7:4]};
endmodule
