// Digital circuit ClockDiv.dig as structural Verilog
// Taktteiler. Hier wird der Takt durch zwei geteilt, und 
// es werden die Signale für den Speicherzugriff des 
// InstructionRegisters erzeugt. Jeweils abwechselnd 
// wird ein Befehlswort gelesen und dieses Befehlswort
// dann ausgeführt.
module ClockDiv (
  input  Clock,
  output S_in,
  output C_in,
  output C
);

  wire not_1_out, t_ff_1_nq;

  not not_1 (not_1_out, Clock);
  T_FF #(.withEnable("false")) t_ff_1 (.C(not_1_out), .Q(S_in), .nQ(t_ff_1_nq));
  and and_1 (C_in, Clock, S_in);
  and and_2 (C, t_ff_1_nq, Clock);

  // Notes on the sheet:
  //   S_in: Signal welches den Prozessor für das Lesen eines
  //   Befehlswortes konfiguriert.
  //   C_in: Taktsignal für das Lesen eines Befehlswortes
  //   C: Takt der das Ausführen eines Befehlswortes 
  //   steuert.
endmodule
