// Digital circuit ControlTwoCycle.dig as structural Verilog
// Leitwerk für einen einfachen Prozessor.
// Es arbeitet rein kombinatorisch, es handelt sich 
// also um ein einfaches Schaltwerk. 
// Da es vergleichsweise komplex ist (24 
// Ausgangsbits), wird es durch einen 
// entsprechenden ROM-Baustein 
// realisiert, und nicht durch 24 einzelne Schaltnetze.
module ControlTwoCycle (
  input  [6:0] Op,
  input  Clock,
  output stPC,
  output WE,
  output imm,
  output absJmp,
  output [2:0] muxB,
  output srcToD,
  output muxA,
  output ALUToBus,
  output [4:0] ALUop,
  output storeFlags,
  output [2:0] Branch,
  output st,
  output ld,
  output ioW,
  output ioR,
  output C,
  output C_in,
  output S_in
);

  wire not_1_out, or_1_out;
  wire [5:0] multiplexer_1_out;
  wire [23:0] Logic_d;

  ClockDiv clockdiv_1 (.Clock(Clock), .S_in(S_in), .C_in(C_in), .C(C));
  not not_1 (not_1_out, S_in);
  or or_1 (or_1_out, S_in, Op[6]);
  and and_1 (imm, Op[6], not_1_out);
  Multiplexer #(.Bits(6)) multiplexer_1 (.sel(or_1_out), .in_0(Op[5:0]), .in_1({6{1'b0}}), .out(multiplexer_1_out));
  ROM #(.AddrBits(6), .Bits(24), .Addr_Bits(6)) Logic (
    .A(multiplexer_1_out), .sel(1'b1),
    .D({Logic_d[23], storeFlags, srcToD, Logic_d[20], ioR, ioW, Branch, ALUop, muxA, stPC, WE, ALUToBus, absJmp, muxB, st, Logic_d[0]}));
  PullDown #(.Bits(24)) pulldown_1 (.out({Logic_d[23], storeFlags, srcToD, Logic_d[20], ioR, ioW, Branch, ALUop, muxA, stPC, WE, ALUToBus, absJmp, muxB, st, Logic_d[0]}));
  or or_2 (ld, S_in, Logic_d[0]);
  Break #(.Cycles(600000)) Break (.brk(Logic_d[20]));

  // Notes on the sheet:
  //   Op: Der Opcode incl. Immediate Bit
  //   stPC: Programm Counter in Register Speichern
  //   WE: Wert am Datenbus in Register speichern
  //   imm: Aktiviert das Speichern der Konstanten
  //   absJmp: absoluten Sprung auslösen
  //   muxB: Selektor für Mux B
  //   srcToD: SourceRegister auf Datenbus legen
  //   muxA: Selector für Mux A
  //   ALUToBus: ALU auf den Datenbus legen
  //   ALUop: Operation der ALU
  //   storeFlags: Wenn gesetzt führt die ALU eine arithmetische Operation aus, so dass die Flags gespeichert werden müssen.
  //   Branch: Art des bedingten Sprunges
  //   st: Ram speichert Daten vom Datenbus
  //   ld: Ram gibt Daten auf den Datenbus
  //   ioW: Es wird auf die IO geschrieben
  //   ioR: Es wird IO gelesen
  //   C: Taktsignal für das Ausführen eines Befehls.
  //   C_in: Taktsignal für das Laden eines neuen Befehls.
  //   S_in: Zeigt an, dass jetzt ein neuer Befehl 
  //   geladen werden soll.
  //   contents of Logic (hex, n*v repeats v):
  //   0,200080,4004c0,4044c0,4008c0,4048c0,400cc0,4010c0,4014c0,c4,d4,4004c4,4004d4,4044c4,
  //   4044d4,4008c4,4008d4,4048c4,4048d4,400cc4,400cd4,4010c4,4010d4,4014c4,4014d4,402cc0,
  //   402cc4,402cd4,400800,400804,400814,4018c0,401cc0,4058c0,405cc0,4020c0,24c0,28c0,20040a,
  //   689,200006,20001e,85,95,200406,685,8018,10018,18018,28018,30018,38018,1a4,20,24,20018,
  //   240004,24001c,240408,80284,80294,80688,100000,800020
endmodule
