// Digital circuit Flags.dig as structural Verilog
// Speichert die Prozessor-Flags. 
// Über den store-Eingang, kann der aktuelle Zustand
// der Flags gespeichert werden. Das Carry-Flag kann 
// dann für arithmetische Funktion genutzt werden,
// alle Flags für eine bedingte Verzweigung.
module Flags (
  input  Zi,
  input  Ni,
  input  Ci,
  input  C,
  input  store,
  output Zo,
  output No,
  output Co
);

  wire and_1_out;

  and and_1 (and_1_out, C, store);
  D_FF u_C (.D(Ci), .C(and_1_out), .Q(Co));  // open: nQ
  D_FF Z (.D(Zi), .C(and_1_out), .Q(Zo));  // open: nQ
  D_FF N (.D(Ni), .C(and_1_out), .Q(No));  // open: nQ

  // Notes on the sheet:
  //   Zi: Das Zero-Flag welches gespeichert werden soll.
  //   Zo: Gibt das gespeicherte Zero-Flag aus.
  //   Ni: Das Negative-Flag welches gespeichert werden soll.
  //   No: Gibt das gespeicherte Negative-Flag aus.
  //   Ci: Das Carry-Flag welches gespeichert werden soll.
  //   Co: Gibt das gespeicherte Carry-Flag aus.
  //   C: der Takteingang
  //   store: Der Eingang welcher das Speichern aktiviert. Es wird auf Eins gesetzt, wenn eine arithmetische Operation ausgeführt wird.
endmodule
