// Digital circuit FlagsRW.dig as structural Verilog
// Speichert die Prozessorflags. Im Gegensatz zur 
// einfachen Variante können bei diesem Modul
// die Flags per IO Operation gelesen und geschrieben
// werden. Die Flags finden sich an IO Adresse 0.
module FlagsRW (
  input  Zi,
  input  Ni,
  input  Ci,
  input  C,
  input  store,
  input  [15:0] A,
  input  IOR,
  input  IOW,
  input  [15:0] Data,
  output Zo,
  output No,
  output Co
);

  wire and_1_out, and_2_out, comparator_1_eq, or_1_out;
  wire [15:0] multiplexer_1_out;
  wire [15:3] register_1_q;

  Comparator #(.Bits(16)) comparator_1 (.a(A), .b({16{1'b0}}), .eq(comparator_1_eq));  // open: gt, lt
  and and_1 (and_1_out, IOW, comparator_1_eq);
  and and_2 (and_2_out, comparator_1_eq, IOR);
  Multiplexer #(.Bits(16)) multiplexer_1 (
    .sel(and_1_out), .in_0({{13{1'b0}}, Ni, Zi, Ci}), .in_1(Data), .out(multiplexer_1_out));
  or or_1 (or_1_out, store, and_1_out);
  Register #(.Bits(16)) register_1 (.D(multiplexer_1_out), .C(C), .en(or_1_out), .Q({register_1_q, No, Zo, Co}));
  assign Data = and_2_out ? {register_1_q, No, Zo, Co} : 16'bz;  // Driver driver_1

  // Notes on the sheet:
  //   Zi: Zero In
  //   Zo: Zero Out
  //   Ni: Negative In
  //   No: Negative Out
  //   Ci: Carry In
  //   Co: Carry Out
  //   C: Takt
  //   store: Speicherfreigabe für die Flags. Geht auf High, wenn
  //   eine arithmetische Funktion in der ALU ausgeführt
  //   wird. Nur diese setzen die Flags. Wird die ALU für
  //   die Adressbildung verwendet, werden die Flags nicht
  //   gespeichert.
  //   A: Adresse
  //   IOR: IO Read
  //   IOW: IO Write
endmodule
