// Digital circuit ImReg.dig as structural Verilog
// Register for storing large constants.
// There is a 1-bit command describing this register. 
// In this way, 15 bits can be stored (the 16th bit 
// activates the writing of this register and therefore 
// is always one). To store the missing 16th bit, a special 
// bit is available in each instruction word.
// {{de Register zum Speichern von großen Konstanten.
// Es existiert ein 1-Bit Befehl, welcher dieses Register
// beschreibt. Auf diese Weise können 15 Bits 
// gespeichert werden (das 16. Bit aktiviert das 
// Beschreiben dieses Registers und ist daher immer 
// Eins) Um das fehlende 16. Bit zu speichern, steht ein 
// spezielles Bit in jedem Befehlswort zur Verfügung.}}
module ImReg (
  input  [15:0] inst,
  input  en,
  input  C,
  output [15:0] imm
);

  Register #(.Bits(15)) u_imm (.D(inst[14:0]), .C(C), .en(en), .Q(imm[14:0]));

  assign imm[15] = inst[8];

  // Notes on the sheet:
  //   inst: the current instruction
  //   {{de Der aktuelle Befehl}}
  //   imm: The constant of register contents and bit 8.
  //   {{de Die Konstante aus Registerinhalt und Bit 8.}}
  //   en: enables storage
  //   {{de Speichern aktivieren}}
endmodule
