// Digital circuit Interrupt.dig as structural Verilog
// Simple interrupt controller.
// If an interrupt is triggered, the controller is disabled: no 
// further interrupts can be triggered. Setting the input reti 
// releases the interrupt controller.
// {{de Einfacher Interrupt-Controller.
// Wird ein Interrupt ausgelöst, wird der Controller
// gesperrt: Es können keine weiteren Interrupts
// ausgelöst werden. Erst der Eingang reti gibt den 
// Interrupt-Controller wieder frei.}}
module Interrupt (
  input  C,
  input  [15:0] Next,
  input  imm,
  input  reti,
  input  intr,
  output [15:0] retAddr,
  output iEn
);

  wire and_1_out, intLock_nq, intReq_q;

  JK_FF intLock (.J(and_1_out), .C(C), .K(reti), .nQ(intLock_nq));  // open: Q
  JK_FF intReq (.J(intr), .C(C), .K(iEn), .Q(intReq_q));  // open: nQ
  and and_1 (and_1_out, intLock_nq, ~imm, intReq_q);  // And
  Register #(.Bits(16)) u_retAddr (.D(Next), .C(C), .en(and_1_out), .Q(retAddr));
  D_FF u_iEn (.D(and_1_out), .C(C), .Q(iEn));  // open: nQ

  // Notes on the sheet:
  //   retAddr: Return Address {{de Return Adresse}}
  //   iEn: interrupt trigger used by the PC
  //   {{de Interrupt-Freigabe für PC}}
  //   Next: The next commands address, that 
  //   is the return address.
  //   {{de Der nächste Befehl, also die 
  //   Rücksprungadresse.}}
  //   imm: immediate register:
  //   If set, an interrupt is blocked.
  //   {{de Immediate Register:
  //   Wenn gesetzt, wird Interrupt verhindert.}}
  //   reti: return from interrupt. This signal is used to 
  //   release the interrupt controller.
  //   {{de return from interrupt. Über dieses Signal werden
  //   die Interrupts wieder freigegeben.}}
  //   intr: interrupt trigger {{de Interrupt Anforderung}}
endmodule
