// Digital circuit PCintr.dig as structural Verilog
// The program counter.
// Here the current program counter is stored.
// The various inputs can be used to influence how the 
// program counter is modified if a clock signal happens.
// {{de Der Programmzähler. 
// Hier wird der aktuelle Programmzähler gespeichert. 
// Über die verschiedenen Eingänge kann beeinflußt 
// werden, auf welche Weise der Programmzähler mit 
// dem Takt weiter geschaltet wird.}}
module PCintr (
  input  [15:0] ALU,
  input  C,
  input  abs,
  input  intr,
  input  rel,
  output [15:0] Next,
  output [15:0] PC,
  output [15:0] intRet
);

  wire Reset_out;
  wire [15:0] Add_ALU_s, multiplexer_1_out, multiplexer_3_out;

  Reset Reset (.out(Reset_out));
  Register #(.Bits(16), .isProgramCounter("true")) u_PC (.D(multiplexer_3_out), .C(~C), .en(Reset_out), .Q(PC));
  Add #(.Bits(16)) Add_One (.a(PC), .b(16'h1), .c_i(1'b0), .s(Next));  // open: c_o
  Add #(.Bits(16)) Add_ALU (.a(Next), .b(ALU), .c_i(1'b0), .s(Add_ALU_s));  // open: c_o
  Multiplexer #(.Bits(16)) multiplexer_1 (.sel(rel), .in_0(Next), .in_1(Add_ALU_s), .out(multiplexer_1_out));
  Multiplexer #(.Bits(16)) multiplexer_2 (.sel(abs), .in_0(multiplexer_1_out), .in_1(ALU), .out(intRet));
  Multiplexer #(.Bits(16)) multiplexer_3 (.sel(intr), .in_0(intRet), .in_1(16'h1000), .out(multiplexer_3_out));

  // Notes on the sheet:
  //   ALU: current ALU output
  //   {{de Aktuelle ALU-Ausgabe}}
  //   Next: Address of the next instruction to execute.
  //   {{de Adresse des nächsten auszuführenden Befehls}}
  //   PC: Programm Counter 
  //   {{de Programmzähler}}
  //   abs: triggers a absolute jump
  //   {{de absoluten Sprung auslösen}}
  //   intr: triggers an interrupt
  //   {{de Interrupt auslösen}}
  //   rel: triggers a relative jump
  //   {{de relativen Spung auslösen}}
  //   intRet: Address of the instruction to return to after an interrupt.
  //   {{de Die Adresse an die nach einem Interrupt zurückgekehrt werden muss.}}
endmodule
