// Digital circuit RegisterOpt.dig as structural Verilog
// In diesem Block befinden sich die 16 
// Prozessorregister.
module RegisterOpt (
  input  [15:0] WD,
  input  C,
  input  [3:0] src,
  input  [3:0] dest,
  input  WE,
  output [15:0] Rdest,
  output [15:0] Rsrc
);

  RegisterFile #(.AddrBits(4), .Bits(16)) registerfile_1 (
    .Din(WD), .we(WE), .Rw(dest), .C(C), .Ra(dest), .Rb(src), .Da(Rdest), .Db(Rsrc));

  // Notes on the sheet:
  //   WD: Daten die gespeichert werden sollen.
  //   Der hier anliegende Wert wird gespeichert, wenn 
  //   der Eingang WE auf 1 geschaltet wird.
  //   C: Takt. Geht der Takt auf High, und ist WE auf High 
  //   wird der Wert an WD im dem Register gespeichert,
  //   welches in dest angegeben ist.
  //   src: Nummer des Source Registers. Legt fest, welches 
  //   Register an Rsrc ausgegeben werden soll.
  //   dest: Nummer des Destignation Registers. Legt fest, 
  //   welches Register an Rdest ausgegeben werden soll.
  //   Zudem wird dieses Register beschrieben, wenn
  //   WE auf 1 gesetzt wird.
  //   WE: Das Speichern aktivieren. Wenn dieser Eingang auf 
  //   High geht, wird der Wert an WD in dem Register 
  //   gespeichert, welches in dest angegeben ist.
  //   Rdest: Inhalt des Destignation Registers.
  //   Welches Register ausgegeben wird, wird mittels 
  //   des Eingangs dest festgelegt.
  //   Rsrc: Inhalt des Source Registers. Welches Register
  //   ausgegeben wird, wird mittels des Einganges src
  //   festgelegt.
endmodule
