// Digital circuit SignExt.dig as structural Verilog
// Extracts small constants from the instruction word.
// There can be two 5-bit constants (the 4 bits of a register 
// together with bit 8 of the instruction word) and a 9-bit 
// constant (the 8 bits of both registers together with 
// bit 8 of the instruction word)
// {{de Extrahiert kleine Konstanten aus dem Befehlswort.
// Es können zwei 5-Bit Konstanten (Die 4 Bits eines 
// Registers zusammen mit Bit 8 des Befehlswortes)
// und eine 9-Bit Konstante (Die 8 Bits beider Register
// zusammen mit Bit 8 des Befehlswortes)}}
module SignExt (
  input  [15:0] inst,
  output [15:0] _4S,
  output [15:0] _8SD,
  output [15:0] _4D
);


  assign _4D = {{12{1'b0}}, inst[7:4]};
  assign _4S = {{12{1'b0}}, inst[3:0]};
  assign _8SD = {{9{inst[7]}}, inst[6:0]};

  // Notes on the sheet:
  //   inst: instruction word
  //   {{de Das Befehlswort}}
  //   _4S: The five bits taken from Rs and bit 8.
  //   {{de Die fünf Bit aus Rs und Bit 8}}
  //   _8SD: The nine bits taken from Rs,Rd and bit 8.
  //   {{de Die neun Bit aus Rs,Rd und Bit 8}}
  //   _4D: The five bits taken from Rd and bit 8.
  //   {{de Die fünf Bit aus Rd und Bit 8}}
endmodule
