// Digital circuit Counter-T.dig as structural Verilog
module Counter_T (
  input  C,
  output out_1,
  output out_3,
  output out_4,
  output out_5
);

  wire Q_0_nq, Q_1_nq, Q_2_nq;

  T_FF Q_0 (.T(C), .Q(out_1), .nQ(Q_0_nq));  // open: C
  T_FF Q_1 (.T(Q_0_nq), .Q(out_3), .nQ(Q_1_nq));  // open: C
  T_FF Q_2 (.T(Q_1_nq), .Q(out_4), .nQ(Q_2_nq));  // open: C
  T_FF Q_3 (.T(Q_2_nq), .Q(out_5));  // open: C, nQ

  // Notes on the sheet:
  //   C: Hz: 2
endmodule
