// Digital circuit D-TransmissionGate.dig as structural Verilog
module D_TransmissionGate (
  input  D,
  input  C,
  output nQ,
  output Q
);

  wire driver_1_out;

  assign driver_1_out = C ? D : 1'bz;  // Driver driver_1
  assign driver_1_out = ~C ? Q : 1'bz;  // DriverInvSel driverinvsel_1
  not not_1 (nQ, driver_1_out);
  not not_2 (Q, nQ);
endmodule
