// Digital circuit JK-MS.dig as structural Verilog
// Diskret aufgebautes Master-Slave JK-Flipflop.
// Das Master-Flipflop speichert bei einem High am 
// Taktsignal, das Slave-Flipflop bei Low am Taktsignal.
// Die obere und untere Rückkoppelleitung verhindern,
// das der verbotenen Zustand am Master-Flipflop
// auftritt..
module JK_MS (
  input  J,
  input  C,
  input  K,
  output Q,
  output nQ
);

  wire and_1_out, and_2_out, and_3_out, and_4_out, nor_1_out, nor_2_out, not_1_out;

  and and_1 (and_1_out, nQ, J, C);
  not not_1 (not_1_out, C);
  and and_2 (and_2_out, C, K, Q);
  nor nor_1 (nor_1_out, and_1_out, nor_2_out);
  nor nor_2 (nor_2_out, nor_1_out, and_2_out);
  and and_3 (and_3_out, nor_1_out, not_1_out);
  and and_4 (and_4_out, not_1_out, nor_2_out);
  nor nor_3 (Q, and_3_out, nQ);
  nor nor_4 (nQ, Q, and_4_out);

  // Notes on the sheet:
  //   J: Eingang zum Setzen des Flipflops.
  //   C: Takteingang
  //   Q: Das im Flipflop gespeicherte Bit.
  //   nQ: Das inverse gespeicherte Bit.
  //   K: Eingang zum Löschen des Flipflops.
endmodule

/* Test case:
C J K Q ~Q
C 1 0 1 0
C 0 0 1 0
C 0 1 0 1
C 0 0 0 1
C 1 1 1 0
C 1 1 0 1
C 1 1 1 0
C 1 1 0 1
*/
