// Digital circuit RS-MS-Simp.dig as structural Verilog
// Master Slave RS-Flipflop. 
// Aufgebaut aus zwei einfachen RS-Flipflops und einem 
// Inverter.
module RS_MS_Simp (
  input  R,
  input  C,
  input  S,
  output Q,
  output nQ
);

  wire not_1_out, rs_c_1_nq, rs_c_1_q;

  RS_C rs_c_1 (.S(S), .C(C), .R(R), .Q(rs_c_1_q), .nQ(rs_c_1_nq));
  not not_1 (not_1_out, C);
  RS_C rs_c_2 (.S(rs_c_1_q), .C(not_1_out), .R(rs_c_1_nq), .Q(Q), .nQ(nQ));

  // Notes on the sheet:
  //   R: Reset Eingang
  //   C: Clock
  //   Q: Das gespeicherte Bit.
  //   nQ: Das Inverse des gespeicherten Bits.
  //   S: Set Eingang
endmodule
