// Digital circuit multip_D_working_T.dig as structural Verilog
module multip_D_working_T (
  input  in_1,
  input  in_3,
  output out_2
);

  wire d_t_1_p3, d_t_2_p3;

  // D_T d_t_1: pin names not known; wires that end beside it: in_1, in_3, d_t_1_p3
  // D_T d_t_2: pin names not known; wires that end beside it: d_t_1_p3, in_3, d_t_2_p3
  // D_T d_t_3: pin names not known; wires that end beside it: d_t_2_p3, in_3, out_2
endmodule
