// Digital circuit splitter.dig as structural Verilog
module splitter (
  input  in_1,
  input  in_2,
  input  in_3
);

  LED led_1 (.in(in_2));
  LED led_2 (.in(in_1));
  LED led_3 (.in(in_3));
endmodule
