// Digital circuit Counter.dig as structural Verilog
module Counter (
  input  en,
  input  C,
  input  clr,
  output [3:0] out,
  output ovf
);

  wire add_1_c_o;
  wire [3:0] add_1_s, multiplexer_1_out, multiplexer_2_out;

  Add #(.Bits(4), .generic("this.Bits=orig.Bits;")) add_1 (
    .a(out), .b(4'b0001), .c_i(1'b0), .s(add_1_s), .c_o(add_1_c_o));
  Multiplexer #(.Bits(4), .generic("this.Bits=orig.Bits;")) multiplexer_1 (
    .sel(en), .in_0(out), .in_1(add_1_s), .out(multiplexer_1_out));
  Multiplexer #(.Bits(4), .generic("this.Bits=orig.Bits;")) multiplexer_2 (
    .sel(clr), .in_0(multiplexer_1_out), .in_1(4'b0000), .out(multiplexer_2_out));
  D_FF #(.Bits(4), .generic("this.Bits=orig.Bits;")) d_ff (.D(multiplexer_2_out), .C(C), .Q(out));  // open: nQ
  and and_1 (ovf, add_1_c_o, en);
endmodule
