// Digital circuit CounterPreset.dig as structural Verilog
module CounterPreset (
  input  en,
  input  C,
  input  dir,
  input  [3:0] in,
  input  ld,
  input  clr,
  output [3:0] out,
  output ovf
);

  wire and_1_out, comparator_1_eq, or_1_out;
  wire [3:0] add_1_s, multiplexer_1_out, multiplexer_2_out, multiplexer_3_out, multiplexer_4_out,
       multiplexer_5_out, multiplexer_6_out;

  Multiplexer #(.Bits(4), .generic("this.Bits=orig.Bits;")) multiplexer_1 (
    .sel(dir), .in_0(4'b0001), .in_1(4'b1111), .out(multiplexer_1_out));
  Add #(.Bits(4), .generic("this.Bits=orig.Bits;")) add_1 (
    .a(out), .b(multiplexer_1_out), .c_i(1'b0), .s(add_1_s));  // open: c_o
  and and_1 (and_1_out, dir, ~clr);  // And
  Multiplexer #(.Bits(4), .generic("this.Bits=orig.Bits;")) multiplexer_2 (
    .sel(dir), .in_0(4'b1111), .in_1(4'b0000), .out(multiplexer_2_out));
  Multiplexer #(.Bits(4), .generic("this.Bits=orig.Bits;")) multiplexer_3 (
    .sel(and_1_out), .in_0(4'b0000), .in_1(4'b1111), .out(multiplexer_3_out));
  Comparator #(.Bits(4), .generic("this.Bits=orig.Bits;")) comparator_1 (
    .a(out), .b(multiplexer_2_out), .eq(comparator_1_eq));  // open: gt, lt
  Multiplexer #(.Bits(4), .generic("this.Bits=orig.Bits;")) multiplexer_4 (
    .sel(en), .in_0(out), .in_1(add_1_s), .out(multiplexer_4_out));
  and and_2 (ovf, comparator_1_eq, en);
  Multiplexer #(.Bits(4), .generic("this.Bits=orig.Bits;")) multiplexer_5 (
    .sel(or_1_out), .in_0(multiplexer_4_out), .in_1(multiplexer_3_out), .out(multiplexer_5_out));
  or or_1 (or_1_out, clr, ovf);
  Multiplexer #(.Bits(4), .generic("this.Bits=orig.Bits;")) multiplexer_6 (
    .sel(ld), .in_0(multiplexer_5_out), .in_1(in), .out(multiplexer_6_out));
  D_FF #(.Bits(4), .generic("this.Bits=orig.Bits;")) d_ff (.D(multiplexer_6_out), .C(C), .Q(out));  // open: nQ

  // Notes on the sheet:
  //   C: Hz: 2
endmodule
