// Digital circuit T_FF.dig as structural Verilog
module T_FF (
  input  C,
  output Q,
  output nQ
);

  D_FF d_ff (.D(nQ), .C(C), .Q(Q), .nQ(nQ));

  // Notes on the sheet:
  //   C: Hz: 2
endmodule
