// Digital circuit T_FF_EN.dig as structural Verilog
module T_FF_EN (
  input  T,
  input  C,
  output Q,
  output nQ
);

  wire and_1_out, and_2_out, or_1_out;

  and and_1 (and_1_out, Q, ~T);  // And
  and and_2 (and_2_out, T, nQ);
  or or_1 (or_1_out, and_1_out, and_2_out);
  D_FF d_ff (.D(or_1_out), .C(C), .Q(Q), .nQ(nQ));

  // Notes on the sheet:
  //   C: Hz: 2
endmodule
