// Digital circuit inputInvert2.dig as structural Verilog
module inputInvert2 (
  input  A,
  input  B,
  input  C,
  output Y
);

  wire and_1_out;

  and and_1 (and_1_out, A, B);
  or or_1 (Y, ~and_1_out, C);  // Or
endmodule
