// Digital circuit nestedMSFF.dig as structural Verilog
module nestedMSFF (
  input  C,
  input  J,
  input  K,
  output Q
);

  // MS_JK ms_jk_1: pin names not known; wires that end beside it: J, C, K, Q
endmodule
