// Digital circuit Processor_fibonacci.dig as structural Verilog
module Processor_fibonacci (
  input  Clock
);

  wire alu_1_p6, alu_1_p7, alu_1_p8, branch_1_p5, control_1_p2, control_1_p3, control_1_p4, control_1_p5,
       control_1_p7, control_1_p8, control_1_p9, control_1_p10, control_1_p11, control_1_p12, control_1_p13,
       or_1_out;
  wire [2:0] control_1_p6;
  wire [3:0] rom_1_d, rom_1_d_2;
  wire [6:0] rom_1_d_4;
  wire [8:8] rom_1_d_3;
  wire [15:0] alu_1_p5, driver_1_out, imreg_1_imm, multiplexer_1_out, multiplexer_2_out, pc_1_next, pc_1_pc,
       register_1_rdest, register_1_rsrc, signext_1__5d, signext_1__5s, signext_1__9sd;

  ROM #(.showList("true"), .Bits(16), .Addr_Bits(16)) rom_1 (
    .A(pc_1_pc), .sel(1'b1), .D({rom_1_d_4, rom_1_d_3[8], rom_1_d_2, rom_1_d}));
  PC pc_1 (.ALU(alu_1_p5), .C(Clock), .abs(control_1_p5), .rel(branch_1_p5), .Next(pc_1_next), .PC(pc_1_pc));
  assign driver_1_out = control_1_p2 ? pc_1_next : 16'bz;  // Driver driver_1
  Register register_1 (
    .WD(driver_1_out), .C(Clock), .src(rom_1_d), .dest(rom_1_d_2), .WE(control_1_p3),
    .Rdest(register_1_rdest), .Rsrc(register_1_rsrc));
  ImReg imreg_1 (.inst({rom_1_d_4, rom_1_d_3[8], rom_1_d_2, rom_1_d}), .en(control_1_p4), .C(Clock), .imm(imreg_1_imm));
  // Control control_1: pin names not known; wires that end beside it: rom_1_d_4, control_1_p2, control_1_p3, control_1_p4, control_1_p5, control_1_p6, control_1_p7, control_1_p8, control_1_p9, control_1_p10, control_1_p11, control_1_p12, control_1_p13
  SignExt signext_1 (
    .inst({rom_1_d_4, rom_1_d_3[8], rom_1_d_2, rom_1_d}), ._5S(signext_1__5s), ._9SD(signext_1__9sd),
    ._5D(signext_1__5d));
  assign driver_1_out = or_1_out ? register_1_rsrc : 16'bz;  // Driver driver_2
  Multiplexer #(.Selector_Bits(3), .Bits(16)) multiplexer_1 (
    .sel(control_1_p6), .in_0(register_1_rsrc), .in_1(imreg_1_imm), .in_2({16{1'b0}}), .in_3(16'hff),
    .in_4(16'hfff), .in_5(signext_1__5s), .in_6(signext_1__9sd), .in_7(signext_1__5d), .out(multiplexer_1_out));
  Multiplexer #(.Bits(16)) multiplexer_2 (
    .sel(control_1_p7), .in_0(register_1_rdest), .in_1(register_1_rsrc), .out(multiplexer_2_out));
  or or_1 (or_1_out, control_1_p11, control_1_p13);
  // ALU alu_1: pin names not known; wires that end beside it: multiplexer_2_out, multiplexer_1_out, control_1_p9, Clock, alu_1_p5, alu_1_p6, alu_1_p7, alu_1_p8
  assign driver_1_out = control_1_p8 ? alu_1_p5 : 16'bz;  // Driver driver_3
  // Branch branch_1: pin names not known; wires that end beside it: alu_1_p6, alu_1_p7, alu_1_p8, control_1_p10, branch_1_p5
  RAMSinglePort #(.Bits(16), .Addr_Bits(16)) ramsingleport_1 (
    .A(alu_1_p5), .str(control_1_p11), .C(Clock), .ld(control_1_p12), .D(driver_1_out));

  // Notes on the sheet:
  //   Clock: Hz: 100
  //   contents of rom_1 (hex, n*v repeats v):
  //   46
  //   5135
  //   8417
  //   19680
  //   8417
  //   5367
  //   19695
  //   28163
  //   20992
  //   31744
  //   28662
  //   8417
  //   19693
  //   734
  //   8417
  //   32770
  //   23053
  //   15362
  //   23574
  //   8193
  //   8417
  //   19680
  //   8417
  //   5625
  //   19695
  //   28657
  //   65535
  //   22992
  //   32770
  //   23053
  //   8194
  //   8417
  //   19680
  //   8417
  //   32805
  //   4848
  //   19695
  //   28645
  //   65535
  //   23325
  //   1025
  //   749
  //   20190
  //   6369
  //   20222
  //   6370
  //   27151
  //   16
endmodule
