// Digital circuit shapes.dig as structural Verilog
module shapes (
  input  in_1,
  input  clk,
  output out_2
);

  // And and_1 is placed but not wired
  Multiplexer multiplexer_1 ();  // open: sel, in_0, in_1, out
  RS_FF rs_ff_1 ();  // open: S, C, R, Q, nQ
  Register register_1 ();  // open: D, C, en, Q
  Add add_1 ();  // open: a, b, c_i, s, c_o
  // NAnd nand_1 is placed but not wired
  Demultiplexer demultiplexer_1 ();  // open: sel, in, out_0, out_1
  JK_FF jk_ff_1 ();  // open: J, C, K, Q, nQ
  ROM rom_1 ();  // open: A, sel, D
  LED led_1 ();  // open: in
  Decoder decoder_1 ();  // open: sel, out_0, out_1
  RAMDualPort ramdualport_1 ();  // open: A, Din, str, C, ld, D
  Sub sub_1 ();  // open: a, b, c_i, s, c_o
  // Or or_1 is placed but not wired
  Delay delay_1 ();  // open: in, out
  D_FF d_ff_1 ();  // open: D, C, Q, nQ
  Mul mul_1 ();  // open: a, b, mul
  // NOr nor_1 is placed but not wired
  Button button_1 ();  // open: out
  // Probe on nothing
  Driver driver_1 ();  // open: in, en, out
  T_FF t_ff_1 ();  // open: T, C, Q, nQ
  RAMSinglePort ramsingleport_1 ();  // open: A, str, C, ld, D
  Seven_Seg seven_seg_1 ();  // open: a, b, c, d, e, f, g, dp
  Driver driver_2 ();  // open: in, en, out
  Counter counter_1 ();  // open: en, C, clr, out, ovf
  Comparator comparator_1 ();  // open: a, b, gt, eq, lt
  // XOr xor_1 is placed but not wired
  Seven_Seg_Hex seven_seg_hex_1 ();  // open: d, dp
  Reset reset_1 ();  // open: out
  Neg neg_1 ();  // open: in, out
  // XNOr xnor_1 is placed but not wired
  Break break_1 ();  // open: brk
  // Not not_1 is placed but not wired
  LookUpTable lookuptable_1 ();  // open: in0, in1, out
  DriverInvSel driverinvsel_1 ();  // open: in, en, out
  DriverInvSel driverinvsel_2 ();  // open: in, en, out
endmodule
