// Digital circuit HalfSub.dig as structural Verilog
module HalfSub (
  input  A,
  input  B,
  output S,
  output BO
);

  xor xor_1 (S, A, B);
  and and_1 (BO, ~A, B);  // And
endmodule

/* Test case:
A B BO S
0 0 0  0
0 1 1  1
1 0 0  1
1 1 0  0
*/
