// Digital circuit cmos10TFullAdder.dig as structural Verilog
// 10 Transistor Full Adder
// The drivers represent p-channel fets. Needed to 
// avoid the resistance problem 
// (see https://github.com/hneemann/Digital/issues/30).
module cmos10TFullAdder (
  input  A,
  input  B,
  input  C_i,
  output S,
  output C_o
);

  wire driverinvsel_1_out, nfet_1_s, pfet_1_d;

  assign driverinvsel_1_out = ~B ? A : 1'bz;  // DriverInvSel driverinvsel_1
  NFET nfet_1 (.G(B), .D(driverinvsel_1_out), .S(nfet_1_s));
  NFET nfet_2 (.G(A), .D(nfet_1_s), .S(1'b0));
  assign driverinvsel_1_out = ~A ? B : 1'bz;  // DriverInvSel driverinvsel_2
  PFET pfet_1 (.G(driverinvsel_1_out), .S(1'b1), .D(pfet_1_d));
  NFET nfet_3 (.G(driverinvsel_1_out), .D(pfet_1_d), .S(1'b0));
  PFET pfet_2 (.G(C_i), .S(driverinvsel_1_out), .D(S));
  NFET nfet_4 (.G(C_i), .D(S), .S(pfet_1_d));
  PFET pfet_3 (.G(pfet_1_d), .S(C_i), .D(C_o));
  NFET nfet_5 (.G(pfet_1_d), .D(C_o), .S(A));
endmodule

/* Test case:
 A   B   C_i  C_o  S
 0   0   0     0   0
 0   0   1     0   1
 0   1   0     0   1
 0   1   1     1   0
 1   0   0     0   1
 1   0   1     1   0
 1   1   0     1   0
 1   1   1     1   1



# transitions
0 0 0 0 0
0 0 1 0 1
0 0 0 0 0
0 1 0 0 1
0 0 0 0 0
0 1 1 1 0
0 0 0 0 0
1 0 0 0 1
0 0 0 0 0
1 0 1 1 0
0 0 0 0 0
1 1 0 1 0
0 0 0 0 0
1 1 1 1 1
0 0 0 0 0
0 0 1 0 1
0 1 0 0 1
0 0 1 0 1
0 1 1 1 0
0 0 1 0 1
1 0 0 0 1
0 0 1 0 1
1 0 1 1 0
0 0 1 0 1
1 1 0 1 0
0 0 1 0 1
1 1 1 1 1
0 0 1 0 1
0 1 0 0 1
0 1 1 1 0
0 1 0 0 1
1 0 0 0 1
0 1 0 0 1
1 0 1 1 0
0 1 0 0 1
1 1 0 1 0
0 1 0 0 1
1 1 1 1 1
0 1 0 0 1
0 1 1 1 0
1 0 0 0 1
0 1 1 1 0
1 0 1 1 0
0 1 1 1 0
1 1 0 1 0
0 1 1 1 0
1 1 1 1 1
0 1 1 1 0
1 0 0 0 1
1 0 1 1 0
1 0 0 0 1
1 1 0 1 0
1 0 0 0 1
1 1 1 1 1
1 0 0 0 1
1 0 1 1 0
1 1 0 1 0
1 0 1 1 0
1 1 1 1 1
1 0 1 1 0
1 1 0 1 0
1 1 1 1 1
1 1 0 1 0
*/
