// Digital circuit cmosSERFFullAdder.dig as structural Verilog
// Static Energy Recovery Full Adder (SERF)
// The drivers represent n-channel fets. Needed to 
// avoid the resistance problem 
// (see https://github.com/hneemann/Digital/issues/30).
module cmosSERFFullAdder (
  input  A,
  input  B,
  input  C_i,
  output S,
  output C_o
);

  wire pfet_1_d, pfet_2_d, pfet_3_d;

  PFET pfet_1 (.G(A), .S(1'b1), .D(pfet_1_d));
  PFET pfet_2 (.G(B), .S(pfet_1_d), .D(pfet_2_d));
  assign pfet_2_d = B ? A : 1'bz;  // Driver driver_1
  assign pfet_2_d = A ? B : 1'bz;  // Driver driver_2
  PFET pfet_3 (.G(C_i), .S(1'b1), .D(pfet_3_d));
  PFET pfet_4 (.G(pfet_2_d), .S(pfet_3_d), .D(S));
  assign S = pfet_2_d ? C_i : 1'bz;  // Driver driver_3
  assign S = C_i ? pfet_2_d : 1'bz;  // Driver driver_4
  PFET pfet_5 (.G(pfet_2_d), .S(C_i), .D(C_o));
  NFET nfet_1 (.G(pfet_2_d), .D(C_o), .S(A));
endmodule

/* Test case:
 A   B   C_i  C_o  S
 0   0   0     0   0
 0   0   1     0   1
 0   1   0     0   1
 0   1   1     1   0
 1   0   0     0   1
 1   0   1     1   0
 1   1   0     1   0
 1   1   1     1   1



# transitions
0 0 0 0 0
0 0 1 0 1
0 0 0 0 0
0 1 0 0 1
0 0 0 0 0
0 1 1 1 0
0 0 0 0 0
1 0 0 0 1
0 0 0 0 0
1 0 1 1 0
0 0 0 0 0
1 1 0 1 0
0 0 0 0 0
1 1 1 1 1
0 0 0 0 0
0 0 1 0 1
0 1 0 0 1
0 0 1 0 1
0 1 1 1 0
0 0 1 0 1
1 0 0 0 1
0 0 1 0 1
1 0 1 1 0
0 0 1 0 1
1 1 0 1 0
0 0 1 0 1
1 1 1 1 1
0 0 1 0 1
0 1 0 0 1
0 1 1 1 0
0 1 0 0 1
1 0 0 0 1
0 1 0 0 1
1 0 1 1 0
0 1 0 0 1
1 1 0 1 0
0 1 0 0 1
1 1 1 1 1
0 1 0 0 1
0 1 1 1 0
1 0 0 0 1
0 1 1 1 0
1 0 1 1 0
0 1 1 1 0
1 1 0 1 0
0 1 1 1 0
1 1 1 1 1
0 1 1 1 0
1 0 0 0 1
1 0 1 1 0
1 0 0 0 1
1 1 0 1 0
1 0 0 0 1
1 1 1 1 1
1 0 0 0 1
1 0 1 1 0
1 1 0 1 0
1 0 1 1 0
1 1 1 1 1
1 0 1 1 0
1 1 0 1 0
1 1 1 1 1
1 1 0 1 0
*/
