// Digital circuit pchan.dig as structural Verilog
module pchan (
  input  S,
  input  D,
  input  G,
  output s_2,
  output d_2
);

  PFET pfet_1 (.G(G), .S(S), .D(D));

  assign d_2 = D;
  assign s_2 = S;
endmodule

/* Test case:
S D G s d
1 z 1 1 z
z 1 1 z 1
1 z z 1 z
z 1 z z 1

# gate is low but fet is not conducting
# because source is not high
z 0 0 z 0
z z 0 z z
z 1 0 z 1
0 z 0 0 z

# switch test
0 z 0 0 z
1 z 0 1 1
0 z 0 0 z
1 z 0 1 1
*/
