// Digital circuit tristateout.dig as structural Verilog
module tristateout (
  input  out,
  input  en,
  output Y
);

  wire T1_d, T3_d, T5_s;

  PFET T1 (.G(en), .S(1'b1), .D(T1_d));
  NFET T2 (.G(en), .D(T1_d), .S(1'b0));
  PFET T3 (.G(T1_d), .S(1'b1), .D(T3_d));
  PFET T4 (.G(out), .S(T3_d), .D(Y));
  NFET T5 (.G(out), .D(Y), .S(T5_s));
  NFET T6 (.G(en), .D(T5_s), .S(1'b0));
endmodule

/* Test case:
out en Y
 0  1  1
 1  1  0
 0  0  z
 1  0  z
*/
