// Digital circuit count.dig as structural Verilog
module count (
  input  en,
  input  C,
  output [3:0] d,
  output ov
);

  wire add_1_c_o;
  wire [3:0] add_1_s, multiplexer_1_out;

  Add #(.Bits(4), .generic("this.Bits=int(args.bits);")) add_1 (
    .a(d), .b(4'b0001), .c_i(1'b0), .s(add_1_s), .c_o(add_1_c_o));
  Multiplexer #(.Bits(4), .generic("this.Bits=int(args.bits);")) multiplexer_1 (
    .sel(en), .in_0(d), .in_1(add_1_s), .out(multiplexer_1_out));
  D_FF #(.Bits(4), .generic("this.Bits=int(args.bits);")) d_ff_1 (.D(multiplexer_1_out), .C(C), .Q(d));  // open: nQ
  and and_1 (ov, add_1_c_o, en);
endmodule
