// Digital circuit main.dig as structural Verilog
module main (
  input  C,
  output [8:0] O
);

  wire count_1_p4, count_2_p4;

  // count #(.generic("bits:=2;")) count_1: pin names not known; wires that end beside it: 1'b1, C, O[1:0], count_1_p4
  // count #(.generic("bits:=3;")) count_2: pin names not known; wires that end beside it: count_1_p4, C, O[4:2], count_2_p4
  // count #(.generic("bits:=4;")) count_3: pin names not known; wires that end beside it: count_2_p4, C, O[8:5]

  // Notes on the sheet:
  //   C: Hz: 5
endmodule

/* Test case:
C O
loop(n,512)
C (n+1)
end loop
*/
