// Digital circuit mainNest.dig as structural Verilog
module mainNest (
  input  C,
  output [8:0] O
);

  wire nest_1_p4, nest_2_p4;

  // nest #(.generic("bits:=2;")) nest_1: pin names not known; wires that end beside it: 1'b1, C, O[1:0], nest_1_p4
  // nest #(.generic("bits:=3;")) nest_2: pin names not known; wires that end beside it: nest_1_p4, C, O[4:2], nest_2_p4
  nest #(.generic("bits:=4;")) nest_3 (.en(nest_2_p4), .C(C), .d(O[8:5]));  // open: ov

  // Notes on the sheet:
  //   C: Hz: 5
endmodule

/* Test case:
C O
loop(n,512)
C (n+1)
end loop
*/
