// Digital circuit memNode.dig as structural Verilog
module memNode (
  input  D_in,
  input  [1:0] A,
  input  C,
  input  str,
  output D_Out
);

  wire and_1_out, and_2_out, memleaf_1_d_out, memleaf_2_d_out;

  and and_1 (and_1_out, str, ~A[1]);  // And
  and and_2 (and_2_out, str, A[1]);
  memLeaf #(.generic("if (isPresent(args)) { export bits:=args.bits; export addr:=args.addr-1; if (args.addr>2) { setCircuit(\"memNode.dig\"); } } else { export bits:=int(1); }")) memleaf_1 (
    .D_in(D_in), .A(A[0]), .C(C), .str(and_1_out), .D_Out(memleaf_1_d_out));
  memLeaf #(.generic("if (isPresent(args)) { export bits:=args.bits; export addr:=args.addr-1; if (args.addr>2) { setCircuit(\"memNode.dig\"); } } else { export bits:=int(1); }")) memleaf_2 (
    .D_in(D_in), .A(A[0]), .C(C), .str(and_2_out), .D_Out(memleaf_2_d_out));
  Multiplexer #(.generic("if (isPresent(args)) { this.Bits=args.bits; }")) multiplexer_1 (
    .sel(A[1]), .in_0(memleaf_1_d_out), .in_1(memleaf_2_d_out), .out(D_Out));
endmodule
