// Digital circuit nest.dig as structural Verilog
module nest (
  input  en,
  input  C,
  output [3:0] d,
  output ov
);

  // count #(.generic("bits:=4; if (isPresent(args)) { bits=args.bits; }")) count_1: pin names not known; wires that end beside it: en, C, 1'b0, d, ov

  // Notes on the sheet:
  //   C: Hz: 5
endmodule
