// Digital circuit DiodeForeward.dig as structural Verilog
module DiodeForeward (
  input  A,
  output Y
);

  DiodeForward diodeforward_1 (.in(A), .out(Y));
  PullDown pulldown_1 (.out(Y));
endmodule

/* Test case:
A Y
1 1
0 0
Z 0
*/
