// Digital circuit const.dig as structural Verilog
module \const  (
  input  A,
  output Y_1,
  output Y_2
);

  // RelayDT relaydt_1: pin names not known; wires that end beside it: A, 1'b0, 1'b1, Y_2, Y_1
  PullDown pulldown_1 (.out(Y_2));
  PullDown pulldown_2 (.out(Y_1));

  // Notes on the sheet:
  //   see issue #255
endmodule

/* Test case:
A Y_1 Y_2
0  0   0
1  0   1
0  0   0
1  0   1
*/
