// Digital circuit inverter.dig as structural Verilog
module inverter (
  input  A,
  output Y
);

  // Relay #(.relayNormallyClosed("true")) relay_1: pin names not known; wires that end beside it: A, 1'b1, Y, Y
  // Relay relay_2: pin names not known; wires that end beside it: A, 1'b0
endmodule

/* Test case:
A Y
0 1
1 0
0 1
1 0
*/
