// Digital circuit relayFullAdder2.dig as structural Verilog
module relayFullAdder2 (
  input  [1:0] A,
  input  [1:0] B,
  input  C_in,
  output C_out,
  output [1:0] S
);

  wire relaydt_1_p4, relaydt_1_p5, relaydt_1_p6, relaydt_2_p3, relaydt_2_p4, relaydt_2_p5, relaydt_3_p3,
       relaydt_3_p5, relaydt_3_p11, relaydt_3_p12, relaydt_3_p16, relaydt_4_p2, relaydt_4_p4, relaydt_4_p10,
       relaydt_4_p15, relaydt_5_p3, relaydt_5_p4, relaydt_5_p5, relaydt_6_p3, relaydt_6_p4, relaydt_6_p5,
       relaydt_7_p2, relaydt_8_p2;

  // RelayDT #(.poles(2)) relaydt_1: pin names not known; wires that end beside it: 1'b1, 1'b1, A[1], relaydt_1_p4, relaydt_1_p5, relaydt_1_p6
  // RelayDT #(.poles(2)) relaydt_2: pin names not known; wires that end beside it: 1'b1, 1'b1, relaydt_2_p3, relaydt_2_p4, relaydt_2_p5
  // RelayDT #(.poles(2)) relaydt_3: pin names not known; wires that end beside it: A[0], 1'b0, relaydt_3_p3, relaydt_1_p5, relaydt_3_p5, relaydt_3_p3, relaydt_1_p4, relaydt_1_p6, relaydt_3_p5, B[0], relaydt_3_p11, relaydt_3_p12, 1'b0, relaydt_3_p11, 1'b0, relaydt_3_p16
  // RelayDT #(.poles(2)) relaydt_4: pin names not known; wires that end beside it: 1'b0, relaydt_4_p2, relaydt_2_p4, relaydt_4_p4, relaydt_4_p2, relaydt_2_p3, relaydt_2_p5, relaydt_4_p4, B[1], relaydt_4_p10, C_out, 1'b0, relaydt_4_p10, 1'b0, relaydt_4_p15
  // RelayDT #(.poles(2)) relaydt_5: pin names not known; wires that end beside it: 1'b1, 1'b1, relaydt_5_p3, relaydt_5_p4, relaydt_5_p5
  // RelayDT #(.poles(2)) relaydt_6: pin names not known; wires that end beside it: 1'b1, 1'b1, relaydt_6_p3, relaydt_6_p4, relaydt_6_p5
  // RelayDT #(.poles(2)) relaydt_7: pin names not known; wires that end beside it: relaydt_5_p4, relaydt_7_p2, relaydt_3_p16, relaydt_5_p3, relaydt_5_p5, relaydt_7_p2, C_in, S[0], relaydt_3_p12, 1'b0
  // RelayDT #(.poles(2)) relaydt_8: pin names not known; wires that end beside it: relaydt_6_p4, relaydt_8_p2, relaydt_4_p15, relaydt_6_p3, relaydt_6_p5, relaydt_8_p2, relaydt_3_p12, S[1], C_out, 1'b0
  PullDown #(.Bits(2)) pulldown_1 (.out(S));
  PullDown pulldown_2 (.out(C_out));
endmodule

/* Test case:
A B C_in S C_out
loop (C,2)
loop (A,4)
loop (B,4)
let s=A+B+C;
 (A) (B) (C) (s&3) (s>>2)
end loop
end loop
end loop
*/
