// Digital circuit selbsthaltung.dig as structural Verilog
module selbsthaltung (
  input  O,
  input  C,
  output Y,
  output Center
);

  // Relay #(.relayNormallyClosed("true")) relay_1: pin names not known; wires that end beside it: O, 1'b1, Center, Center
  // Relay relay_2: pin names not known; wires that end beside it: C, Y, Y
  // Relay relay_3: pin names not known; wires that end beside it: Center, Y
  PullDown pulldown_1 (.out(Y));
endmodule

/* Test case:
O C Y Center
0 0 0 1
0 1 1 1
0 0 1 1
1 0 0 z
1 1 0 0
0 1 1 1
*/
