// Digital circuit switch1.dig as structural Verilog
module switch1 (
  input  A,
  input  B,
  input  C,
  output Y
);

  wire relay_1_p3;

  // Relay relay_1: pin names not known; wires that end beside it: 1'b1, A, relay_1_p3
  // Relay relay_2: pin names not known; wires that end beside it: relay_1_p3, C, B, Y
  // Relay relay_3: pin names not known; wires that end beside it: relay_1_p3, Y
endmodule

/* Test case:
A B C Y
0 0 0 Z
0 0 1 Z
0 1 0 Z
0 1 1 Z
1 0 0 Z
1 0 1 1
1 1 0 1
1 1 1 1

# transitions
0 0 0 Z
0 0 1 Z
0 0 0 Z
0 1 0 Z
0 0 0 Z
0 1 1 Z
0 0 0 Z
1 0 0 Z
0 0 0 Z
1 0 1 1
0 0 0 Z
1 1 0 1
0 0 0 Z
1 1 1 1
0 0 0 Z
0 0 1 Z
0 1 0 Z
0 0 1 Z
0 1 1 Z
0 0 1 Z
1 0 0 Z
0 0 1 Z
1 0 1 1
0 0 1 Z
1 1 0 1
0 0 1 Z
1 1 1 1
0 0 1 Z
0 1 0 Z
0 1 1 Z
0 1 0 Z
1 0 0 Z
0 1 0 Z
1 0 1 1
0 1 0 Z
1 1 0 1
0 1 0 Z
1 1 1 1
0 1 0 Z
0 1 1 Z
1 0 0 Z
0 1 1 Z
1 0 1 1
0 1 1 Z
1 1 0 1
0 1 1 Z
1 1 1 1
0 1 1 Z
1 0 0 Z
1 0 1 1
1 0 0 Z
1 1 0 1
1 0 0 Z
1 1 1 1
1 0 0 Z
1 0 1 1
1 1 0 1
1 0 1 1
1 1 1 1
1 0 1 1
1 1 0 1
1 1 1 1
1 1 0 1
*/
