// Digital circuit switch_simple.dig as structural Verilog
module switch_simple (
  input  A,
  output Y1,
  output Y2,
  output Y3,
  output Y4,
  output Y5,
  output Y6,
  output Y7,
  output Y8
);

  // Relay relay_1: pin names not known; wires that end beside it: 1'b0, A, A, Y1
  // Relay relay_2: pin names not known; wires that end beside it: 1'b0, A, Y2
  // Relay relay_3: pin names not known; wires that end beside it: 1'b1, A, Y3
  // Relay relay_4: pin names not known; wires that end beside it: 1'b1, Y4
  // Relay relay_5: pin names not known; wires that end beside it: 1'b0, A, Y5
  // Relay relay_6: pin names not known; wires that end beside it: 1'b0, A, Y6
  // Relay relay_7: pin names not known; wires that end beside it: 1'b1, A, Y7
  // Relay relay_8: pin names not known; wires that end beside it: 1'b1, A, Y8
endmodule

/* Test case:
A Y1 Y2 Y3 Y4 Y5 Y6 Y7 Y8
0 z  z  z  z  z  z  z  z
1 0  0  1  1  0  0  1  1
0 z  z  z  z  z  z  z  z
1 0  0  1  1  0  0  1  1
*/
