// Digital circuit shift-inc.dig as structural Verilog
module shift_inc (
  input  [15:0] D_in,
  input  [3:0] sh,
  output [15:0] D
);

  wire shift_fixed_left_inc_1_p3;

  // shift_fixed_left_inc #(.generic("if (isPresent(args)) { export shift := 1<<(args.shiftBits-1); setCircuit(args.circuit); } else { // used if circuit is started as the main circuit export dataBits:=16; export shift:=8; }")) shift_fixed_left_inc_1: pin names not known; wires that end beside it: D_in, sh[3], shift_fixed_left_inc_1_p3
  // shift_inc #(.generic("if (isPresent(args)) { if (args.shiftBits=2) { export shift := 1; setCircuit(args.circuit); } else { export shiftBits := args.shiftBits-1; } } else { // used if circuit is started as the main circuit export dataBits:=16; export shiftBits:=3; export circuit:=\"shift-fixed-left-inc.dig\"; }")) shift_inc_1: pin names not known; wires that end beside it: shift_fixed_left_inc_1_p3, sh[2:0], D
endmodule
